// Logisim project computer.circ as structural Verilog
module NandFullAdder (
  input  A,
  input  B,
  input  Cin,
  output S,
  output Cout
);

  wire nand_1_out, nand_2_out, nand_3_out, nand_4_out, nand_5_out, nand_6_out, nand_7_out, nand_8_out,
       nand_9_out, nand_10_out, nand_11_out;

  nand nand_1 (nand_1_out, B, B);
  nand nand_2 (nand_2_out, A, A);
  nand nand_3 (nand_3_out, A, nand_1_out);
  nand nand_4 (nand_4_out, B, nand_2_out);
  nand nand_5 (nand_5_out, nand_3_out, nand_4_out);
  nand nand_6 (nand_6_out, Cin, Cin);
  nand nand_7 (nand_7_out, nand_5_out, nand_5_out);
  nand nand_8 (nand_8_out, nand_5_out, nand_6_out);
  nand nand_9 (nand_9_out, Cin, nand_7_out);
  nand nand_10 (nand_10_out, Cin, nand_5_out);
  nand nand_11 (nand_11_out, A, B);
  nand nand_12 (S, nand_8_out, nand_9_out);
  nand nand_13 (Cout, nand_10_out, nand_11_out);
endmodule

module NandFullAdder10 (
  input  [9:0] A,
  input  [9:0] B,
  output [9:0] S,
  output C
);

  wire nandfulladder_1_cout, nandfulladder_2_cout, nandfulladder_3_cout, nandfulladder_4_cout,
       nandfulladder_5_cout, nandfulladder_6_cout, nandfulladder_7_cout, nandfulladder_8_cout,
       nandfulladder_9_cout;

  NandFullAdder nandfulladder_1 (.A(A[0]), .B(B[0]), .Cin(1'b0), .S(S[0]), .Cout(nandfulladder_1_cout));
  NandFullAdder nandfulladder_2 (.A(A[1]), .B(B[1]), .Cin(nandfulladder_1_cout), .S(S[1]), .Cout(nandfulladder_2_cout));
  NandFullAdder nandfulladder_3 (.A(A[2]), .B(B[2]), .Cin(nandfulladder_2_cout), .S(S[2]), .Cout(nandfulladder_3_cout));
  NandFullAdder nandfulladder_4 (.A(A[3]), .B(B[3]), .Cin(nandfulladder_3_cout), .S(S[3]), .Cout(nandfulladder_4_cout));
  NandFullAdder nandfulladder_5 (.A(A[4]), .B(B[4]), .Cin(nandfulladder_4_cout), .S(S[4]), .Cout(nandfulladder_5_cout));
  NandFullAdder nandfulladder_6 (.A(A[5]), .B(B[5]), .Cin(nandfulladder_5_cout), .S(S[5]), .Cout(nandfulladder_6_cout));
  NandFullAdder nandfulladder_7 (.A(A[6]), .B(B[6]), .Cin(nandfulladder_6_cout), .S(S[6]), .Cout(nandfulladder_7_cout));
  NandFullAdder nandfulladder_8 (.A(A[7]), .B(B[7]), .Cin(nandfulladder_7_cout), .S(S[7]), .Cout(nandfulladder_8_cout));
  NandFullAdder nandfulladder_9 (.A(A[8]), .B(B[8]), .Cin(nandfulladder_8_cout), .S(S[8]), .Cout(nandfulladder_9_cout));
  NandFullAdder nandfulladder_10 (.A(A[9]), .B(B[9]), .Cin(nandfulladder_9_cout), .S(S[9]), .Cout(C));
endmodule

module NandALU (
  input  A1,
  input  A2,
  input  A3,
  input  A4,
  input  A5,
  input  A6,
  input  A7,
  input  A8,
  input  A9,
  input  A10,
  input  OC,
  input  ABN,
  input  AZ,
  input  AC,
  input  B1,
  input  B2,
  input  B3,
  input  B4,
  input  B5,
  input  B6,
  input  B7,
  input  B8,
  input  B9,
  input  B10,
  input  BZ,
  input  BC,
  output O1,
  output O2,
  output O3,
  output O4,
  output O5,
  output O6,
  output O7,
  output O8,
  output O9,
  output O10,
  output C
);

  wire nand_1_out, nand_2_out, nand_3_out, nand_4_out, nand_5_out, nand_6_out, nand_7_out, nand_8_out,
       nand_9_out, nand_10_out, nand_11_out, nand_12_out, nand_13_out, nand_14_out, nand_15_out, nand_16_out,
       nand_17_out, nand_18_out, nand_19_out, nand_20_out, nand_21_out, nand_22_out, nand_23_out,
       nand_24_out, nand_25_out, nand_26_out, nand_27_out, nand_28_out, nand_29_out, nand_30_out,
       nand_31_out, nand_32_out, nand_33_out, nand_34_out, nand_35_out, nand_36_out, nand_37_out,
       nand_38_out, nand_39_out, nand_40_out, nandfulladder10_1_p1, nandfulladder10_1_p2,
       nandfulladder10_1_p3, nandmux_1_o, nandmux_2_o, nandmux_3_o, nandmux_4_o, nandmux_5_o, nandmux_6_o,
       nandmux_7_o, nandmux_8_o, nandmux_9_o, nandmux_10_o, nandmux_11_o, nandmux_12_o, nandmux_13_o,
       nandmux_14_o, nandmux_15_o, nandmux_16_o, nandmux_17_o, nandmux_18_o, nandmux_19_o, nandmux_20_o,
       nandmux_21_o, nandmux_22_o, nandmux_23_o, nandmux_24_o, nandmux_25_o, nandmux_26_o, nandmux_27_o,
       nandmux_28_o, nandmux_29_o, nandmux_30_o, nandmux_31_o, nandmux_32_o, nandmux_33_o, nandmux_34_o,
       nandmux_35_o, nandmux_36_o, nandmux_37_o, nandmux_38_o, nandmux_39_o, nandmux_40_o, nandmux_41_o,
       nandmux_42_o, nandmux_43_o, nandmux_44_o, nandmux_45_o, nandmux_46_o, nandmux_47_o, nandmux_48_o,
       nandmux_49_o, nandmux_50_o, undriven, undriven_2, undriven_3, undriven_4, undriven_5, undriven_6,
       undriven_7;

  NandMUX nandmux_1 (.A(A1), .S(AZ), .B(1'b0), .O(nandmux_1_o));
  NandMUX nandmux_2 (.A(A2), .S(AZ), .B(1'b0), .O(nandmux_2_o));
  NandMUX nandmux_3 (.A(A3), .S(AZ), .B(1'b0), .O(nandmux_3_o));
  NandMUX nandmux_4 (.A(A4), .S(AZ), .B(1'b0), .O(nandmux_4_o));
  NandMUX nandmux_5 (.A(A5), .S(AZ), .B(1'b0), .O(nandmux_5_o));
  NandMUX nandmux_6 (.A(A6), .S(AZ), .B(1'b0), .O(nandmux_6_o));
  NandMUX nandmux_7 (.A(A7), .S(AZ), .B(1'b0), .O(nandmux_7_o));
  NandMUX nandmux_8 (.A(A8), .S(AZ), .B(1'b0), .O(nandmux_8_o));
  NandMUX nandmux_9 (.A(A9), .S(AZ), .B(1'b0), .O(nandmux_9_o));
  NandMUX nandmux_10 (.A(A10), .S(AZ), .B(1'b0), .O(nandmux_10_o));
  NandMUX nandmux_11 (.A(B1), .S(BZ), .B(1'b0), .O(nandmux_11_o));
  NandMUX nandmux_12 (.A(B2), .S(BZ), .B(1'b0), .O(nandmux_12_o));
  NandMUX nandmux_13 (.A(B3), .S(BZ), .B(1'b0), .O(nandmux_13_o));
  NandMUX nandmux_14 (.A(B4), .S(BZ), .B(1'b0), .O(nandmux_14_o));
  NandMUX nandmux_15 (.A(B5), .S(BZ), .B(1'b0), .O(nandmux_15_o));
  NandMUX nandmux_16 (.A(B6), .S(BZ), .B(1'b0), .O(nandmux_16_o));
  NandMUX nandmux_17 (.A(B7), .S(BZ), .B(1'b0), .O(nandmux_17_o));
  NandMUX nandmux_18 (.A(B8), .S(BZ), .B(1'b0), .O(nandmux_18_o));
  NandMUX nandmux_19 (.A(B9), .S(BZ), .B(1'b0), .O(nandmux_19_o));
  NandMUX nandmux_20 (.A(B10), .S(BZ), .B(1'b0), .O(nandmux_20_o));
  nand nand_1 (nand_1_out, nandmux_1_o, nandmux_1_o);
  nand nand_2 (nand_2_out, nandmux_2_o, nandmux_2_o);
  nand nand_3 (nand_3_out, nandmux_3_o, nandmux_3_o);
  nand nand_4 (nand_4_out, nandmux_4_o, nandmux_4_o);
  nand nand_5 (nand_5_out, nandmux_5_o, nandmux_5_o);
  nand nand_6 (nand_6_out, nandmux_6_o, nandmux_6_o);
  nand nand_7 (nand_7_out, nandmux_7_o, nandmux_7_o);
  nand nand_8 (nand_8_out, nandmux_8_o, nandmux_8_o);
  nand nand_9 (nand_9_out, nandmux_9_o, nandmux_9_o);
  nand nand_10 (nand_10_out, nandmux_10_o, nandmux_10_o);
  nand nand_11 (nand_11_out, nandmux_11_o, nandmux_11_o);
  nand nand_12 (nand_12_out, nandmux_12_o, nandmux_12_o);
  nand nand_13 (nand_13_out, nandmux_13_o, nandmux_13_o);
  nand nand_14 (nand_14_out, nandmux_14_o, nandmux_14_o);
  nand nand_15 (nand_15_out, nandmux_15_o, nandmux_15_o);
  nand nand_16 (nand_16_out, nandmux_16_o, nandmux_16_o);
  nand nand_17 (nand_17_out, nandmux_17_o, nandmux_17_o);
  nand nand_18 (nand_18_out, nandmux_18_o, nandmux_18_o);
  nand nand_19 (nand_19_out, nandmux_19_o, nandmux_19_o);
  nand nand_20 (nand_20_out, nandmux_20_o, nandmux_20_o);
  NandMUX nandmux_21 (.A(nandmux_1_o), .S(AC), .B(nand_1_out), .O(nandmux_21_o));
  NandMUX nandmux_22 (.A(nandmux_2_o), .S(AC), .B(nand_2_out), .O(nandmux_22_o));
  NandMUX nandmux_23 (.A(nandmux_3_o), .S(AC), .B(nand_3_out), .O(nandmux_23_o));
  NandMUX nandmux_24 (.A(nandmux_4_o), .S(AC), .B(nand_4_out), .O(nandmux_24_o));
  NandMUX nandmux_25 (.A(nandmux_5_o), .S(AC), .B(nand_5_out), .O(nandmux_25_o));
  NandMUX nandmux_26 (.A(nandmux_6_o), .S(AC), .B(nand_6_out), .O(nandmux_26_o));
  NandMUX nandmux_27 (.A(nandmux_7_o), .S(AC), .B(nand_7_out), .O(nandmux_27_o));
  NandMUX nandmux_28 (.A(nandmux_8_o), .S(AC), .B(nand_8_out), .O(nandmux_28_o));
  NandMUX nandmux_29 (.A(nandmux_9_o), .S(AC), .B(nand_9_out), .O(nandmux_29_o));
  NandMUX nandmux_30 (.A(nandmux_10_o), .S(AC), .B(nand_10_out), .O(nandmux_30_o));
  NandMUX nandmux_31 (.A(nandmux_11_o), .S(BC), .B(nand_11_out), .O(nandmux_31_o));
  NandMUX nandmux_32 (.A(nandmux_12_o), .S(BC), .B(nand_12_out), .O(nandmux_32_o));
  NandMUX nandmux_33 (.A(nandmux_13_o), .S(BC), .B(nand_13_out), .O(nandmux_33_o));
  NandMUX nandmux_34 (.A(nandmux_14_o), .S(BC), .B(nand_14_out), .O(nandmux_34_o));
  NandMUX nandmux_35 (.A(nandmux_15_o), .S(BC), .B(nand_15_out), .O(nandmux_35_o));
  NandMUX nandmux_36 (.A(nandmux_16_o), .S(BC), .B(nand_16_out), .O(nandmux_36_o));
  NandMUX nandmux_37 (.A(nandmux_17_o), .S(BC), .B(nand_17_out), .O(nandmux_37_o));
  NandMUX nandmux_38 (.A(nandmux_18_o), .S(BC), .B(nand_18_out), .O(nandmux_38_o));
  NandMUX nandmux_39 (.A(nandmux_19_o), .S(BC), .B(nand_19_out), .O(nandmux_39_o));
  NandMUX nandmux_40 (.A(nandmux_20_o), .S(BC), .B(nand_20_out), .O(nandmux_40_o));
  // NandFullAdder10 nandfulladder10_1: pin names not known; wires that end beside it: nandfulladder10_1_p1, nandfulladder10_1_p2, nandfulladder10_1_p3
  nand nand_21 (nand_21_out, nandfulladder10_1_p1, nandfulladder10_1_p1);
  nand nand_22 (nand_22_out, nandfulladder10_1_p2, nandfulladder10_1_p2);
  nand nand_23 (nand_23_out, nandfulladder10_1_p3, nandfulladder10_1_p3);
  nand nand_24 (nand_24_out, undriven, undriven);
  nand nand_25 (nand_25_out, undriven_2, undriven_2);
  nand nand_26 (nand_26_out, undriven_3, undriven_3);
  nand nand_27 (nand_27_out, undriven_4, undriven_4);
  nand nand_28 (nand_28_out, undriven_5, undriven_5);
  nand nand_29 (nand_29_out, undriven_6, undriven_6);
  nand nand_30 (nand_30_out, undriven_7, undriven_7);
  nand nand_31 (nand_31_out, nandmux_21_o, nandmux_31_o);
  nand nand_32 (nand_32_out, nandmux_22_o, nandmux_32_o);
  nand nand_33 (nand_33_out, nandmux_23_o, nandmux_33_o);
  nand nand_34 (nand_34_out, nandmux_24_o, nandmux_34_o);
  nand nand_35 (nand_35_out, nandmux_25_o, nandmux_35_o);
  nand nand_36 (nand_36_out, nandmux_26_o, nandmux_36_o);
  nand nand_37 (nand_37_out, nandmux_27_o, nandmux_37_o);
  nand nand_38 (nand_38_out, nandmux_28_o, nandmux_38_o);
  nand nand_39 (nand_39_out, nandmux_29_o, nandmux_39_o);
  nand nand_40 (nand_40_out, nandmux_30_o, nandmux_40_o);
  NandMUX nandmux_41 (.A(nandfulladder10_1_p1), .S(OC), .B(nand_21_out), .O(nandmux_41_o));
  NandMUX nandmux_42 (.A(nandfulladder10_1_p2), .S(OC), .B(nand_22_out), .O(nandmux_42_o));
  NandMUX nandmux_43 (.A(nandfulladder10_1_p3), .S(OC), .B(nand_23_out), .O(nandmux_43_o));
  NandMUX nandmux_44 (.A(undriven), .S(OC), .B(nand_24_out), .O(nandmux_44_o));
  NandMUX nandmux_45 (.A(undriven_2), .S(OC), .B(nand_25_out), .O(nandmux_45_o));
  NandMUX nandmux_46 (.A(undriven_3), .S(OC), .B(nand_26_out), .O(nandmux_46_o));
  NandMUX nandmux_47 (.A(undriven_4), .S(OC), .B(nand_27_out), .O(nandmux_47_o));
  NandMUX nandmux_48 (.A(undriven_5), .S(OC), .B(nand_28_out), .O(nandmux_48_o));
  NandMUX nandmux_49 (.A(undriven_6), .S(OC), .B(nand_29_out), .O(nandmux_49_o));
  NandMUX nandmux_50 (.A(undriven_7), .S(OC), .B(nand_30_out), .O(nandmux_50_o));
  NandMUX nandmux_51 (.A(nandmux_41_o), .S(ABN), .B(nand_31_out), .O(O1));
  NandMUX nandmux_52 (.A(nandmux_42_o), .S(ABN), .B(nand_32_out), .O(O2));
  NandMUX nandmux_53 (.A(nandmux_43_o), .S(ABN), .B(nand_33_out), .O(O3));
  NandMUX nandmux_54 (.A(nandmux_44_o), .S(ABN), .B(nand_34_out), .O(O4));
  NandMUX nandmux_55 (.A(nandmux_45_o), .S(ABN), .B(nand_35_out), .O(O5));
  NandMUX nandmux_56 (.A(nandmux_46_o), .S(ABN), .B(nand_36_out), .O(O6));
  NandMUX nandmux_57 (.A(nandmux_47_o), .S(ABN), .B(nand_37_out), .O(O7));
  NandMUX nandmux_58 (.A(nandmux_48_o), .S(ABN), .B(nand_38_out), .O(O8));
  NandMUX nandmux_59 (.A(nandmux_49_o), .S(ABN), .B(nand_39_out), .O(O9));
  NandMUX nandmux_60 (.A(nandmux_50_o), .S(ABN), .B(nand_40_out), .O(O10));
endmodule

module NandMUX (
  input  A,
  input  S,
  input  B,
  output O
);

  wire nand_1_out, nand_2_out, nand_3_out;

  nand nand_1 (nand_1_out, S, S);
  nand nand_2 (nand_2_out, A, nand_1_out);
  nand nand_3 (nand_3_out, S, B);
  nand nand_4 (O, nand_2_out, nand_3_out);
endmodule

module NandDFF (
  input  CLK,
  input  A,
  input  SB,
  output O,
  output OC
);

  wire nand_1_out, nand_2_out, nand_3_out;

  nand nand_1 (nand_1_out, A, A);
  nand nand_2 (nand_2_out, A, CLK);
  nand nand_3 (nand_3_out, CLK, nand_1_out);
  nand nand_4 (O, nand_2_out, SB, OC);
  nand nand_5 (OC, O, nand_3_out);
endmodule

module NandRegister10 (
  input  E,
  input  L,
  input  [9:0] I,
  input  SB,
  output [9:0] O
);

  wire nand_1_out, nand_2_out, nanddff_1_oc, nanddff_2_oc, nanddff_3_oc, nanddff_4_oc, nanddff_5_oc,
       nanddff_6_oc, nanddff_7_oc, nanddff_8_oc, nanddff_9_oc, nanddff_10_oc;

  nand nand_1 (nand_1_out, E, L);
  nand nand_2 (nand_2_out, nand_1_out, nand_1_out);
  NandDFF nanddff_1 (.CLK(nand_2_out), .A(I[0]), .SB(SB), .O(O[0]), .OC(nanddff_1_oc));
  // NoConnect on nanddff_1_oc
  NandDFF nanddff_2 (.CLK(nand_2_out), .A(I[1]), .SB(SB), .O(O[1]), .OC(nanddff_2_oc));
  // NoConnect on nanddff_2_oc
  NandDFF nanddff_3 (.CLK(nand_2_out), .A(I[2]), .SB(SB), .O(O[2]), .OC(nanddff_3_oc));
  // NoConnect on nanddff_3_oc
  NandDFF nanddff_4 (.CLK(nand_2_out), .A(I[3]), .SB(SB), .O(O[3]), .OC(nanddff_4_oc));
  // NoConnect on nanddff_4_oc
  NandDFF nanddff_5 (.CLK(nand_2_out), .A(I[4]), .SB(SB), .O(O[4]), .OC(nanddff_5_oc));
  // NoConnect on nanddff_5_oc
  NandDFF nanddff_6 (.CLK(nand_2_out), .A(I[5]), .SB(SB), .O(O[5]), .OC(nanddff_6_oc));
  // NoConnect on nanddff_6_oc
  NandDFF nanddff_7 (.CLK(nand_2_out), .A(I[6]), .SB(SB), .O(O[6]), .OC(nanddff_7_oc));
  // NoConnect on nanddff_7_oc
  NandDFF nanddff_8 (.CLK(nand_2_out), .A(I[7]), .SB(SB), .O(O[7]), .OC(nanddff_8_oc));
  // NoConnect on nanddff_8_oc
  NandDFF nanddff_9 (.CLK(nand_2_out), .A(I[8]), .SB(SB), .O(O[8]), .OC(nanddff_9_oc));
  // NoConnect on nanddff_9_oc
  NandDFF nanddff_10 (.CLK(nand_2_out), .A(I[9]), .SB(SB), .O(O[9]), .OC(nanddff_10_oc));
  // NoConnect on nanddff_10_oc
endmodule

module NandMUX10 (
  input  [9:0] A,
  input  [9:0] B,
  input  S,
  output [9:0] O
);

  NandMUX nandmux_1 (.A(A[0]), .S(S), .B(B[0]), .O(O[0]));
  NandMUX nandmux_2 (.A(A[1]), .S(S), .B(B[1]), .O(O[1]));
  NandMUX nandmux_3 (.A(A[2]), .S(S), .B(B[2]), .O(O[2]));
  NandMUX nandmux_4 (.A(A[3]), .S(S), .B(B[3]), .O(O[3]));
  NandMUX nandmux_5 (.A(A[4]), .S(S), .B(B[4]), .O(O[4]));
  NandMUX nandmux_6 (.A(A[5]), .S(S), .B(B[5]), .O(O[5]));
  NandMUX nandmux_7 (.A(A[6]), .S(S), .B(B[6]), .O(O[6]));
  NandMUX nandmux_8 (.A(A[7]), .S(S), .B(B[7]), .O(O[7]));
  NandMUX nandmux_9 (.A(A[8]), .S(S), .B(B[8]), .O(O[8]));
  NandMUX nandmux_10 (.A(A[9]), .S(S), .B(B[9]), .O(O[9]));
endmodule

module ControlledBuffer10 (
  input  [9:0] I,
  input  S,
  output [9:0] O
);

  assign O[0] = S ? I[0] : 1'bz;  // Controlled_Buffer controlled_buffer_1
  assign O[1] = S ? I[1] : 1'bz;  // Controlled_Buffer controlled_buffer_2
  assign O[2] = S ? I[2] : 1'bz;  // Controlled_Buffer controlled_buffer_3
  assign O[3] = S ? I[3] : 1'bz;  // Controlled_Buffer controlled_buffer_4
  assign O[4] = S ? I[4] : 1'bz;  // Controlled_Buffer controlled_buffer_5
  assign O[5] = S ? I[5] : 1'bz;  // Controlled_Buffer controlled_buffer_6
  assign O[6] = S ? I[6] : 1'bz;  // Controlled_Buffer controlled_buffer_7
  assign O[7] = S ? I[7] : 1'bz;  // Controlled_Buffer controlled_buffer_8
  assign O[8] = S ? I[8] : 1'bz;  // Controlled_Buffer controlled_buffer_9
  assign O[9] = S ? I[9] : 1'bz;  // Controlled_Buffer controlled_buffer_10
endmodule

module NandRegister8 (
  input  E,
  input  L,
  input  [7:0] I,
  input  SB,
  output [7:0] O
);

  wire nand_1_out, nand_2_out, nanddff_1_oc, nanddff_2_oc, nanddff_3_oc, nanddff_4_oc, nanddff_5_oc,
       nanddff_6_oc, nanddff_7_oc, nanddff_8_oc;

  nand nand_1 (nand_1_out, E, L);
  nand nand_2 (nand_2_out, nand_1_out, nand_1_out);
  NandDFF nanddff_1 (.CLK(nand_2_out), .A(I[0]), .SB(SB), .O(O[0]), .OC(nanddff_1_oc));
  // NoConnect on nanddff_1_oc
  NandDFF nanddff_2 (.CLK(nand_2_out), .A(I[1]), .SB(SB), .O(O[1]), .OC(nanddff_2_oc));
  // NoConnect on nanddff_2_oc
  NandDFF nanddff_3 (.CLK(nand_2_out), .A(I[2]), .SB(SB), .O(O[2]), .OC(nanddff_3_oc));
  // NoConnect on nanddff_3_oc
  NandDFF nanddff_4 (.CLK(nand_2_out), .A(I[3]), .SB(SB), .O(O[3]), .OC(nanddff_4_oc));
  // NoConnect on nanddff_4_oc
  NandDFF nanddff_5 (.CLK(nand_2_out), .A(I[4]), .SB(SB), .O(O[4]), .OC(nanddff_5_oc));
  // NoConnect on nanddff_5_oc
  NandDFF nanddff_6 (.CLK(nand_2_out), .A(I[5]), .SB(SB), .O(O[5]), .OC(nanddff_6_oc));
  // NoConnect on nanddff_6_oc
  NandDFF nanddff_7 (.CLK(nand_2_out), .A(I[6]), .SB(SB), .O(O[6]), .OC(nanddff_7_oc));
  // NoConnect on nanddff_7_oc
  NandDFF nanddff_8 (.CLK(nand_2_out), .A(I[7]), .SB(SB), .O(O[7]), .OC(nanddff_8_oc));
  // NoConnect on nanddff_8_oc
endmodule

module ControlledBuffer8 (
  input  [7:0] I,
  input  S,
  output [7:0] O
);

  assign O[0] = S ? I[0] : 1'bz;  // Controlled_Buffer controlled_buffer_1
  assign O[1] = S ? I[1] : 1'bz;  // Controlled_Buffer controlled_buffer_2
  assign O[2] = S ? I[2] : 1'bz;  // Controlled_Buffer controlled_buffer_3
  assign O[3] = S ? I[3] : 1'bz;  // Controlled_Buffer controlled_buffer_4
  assign O[4] = S ? I[4] : 1'bz;  // Controlled_Buffer controlled_buffer_5
  assign O[5] = S ? I[5] : 1'bz;  // Controlled_Buffer controlled_buffer_6
  assign O[6] = S ? I[6] : 1'bz;  // Controlled_Buffer controlled_buffer_7
  assign O[7] = S ? I[7] : 1'bz;  // Controlled_Buffer controlled_buffer_8
endmodule

module NandSyncCounter (
  input  [12:0] I,
  input  L,
  input  SB,
  input  E,
  output [12:0] O
);

  wire nand_1_out, nand_2_out, nand_3_out, nand_4_out, nand_5_out, nand_6_out, nand_7_out, nand_8_out,
       nand_9_out, nand_10_out, nand_11_out, nand_12_out, nand_13_out, nand_14_out, nand_15_out, nand_16_out,
       nand_17_out, nand_18_out, nand_19_out, nand_20_out, nand_21_out, nand_22_out, nand_23_out,
       nand_24_out, nand_25_out, nand_26_out, nand_27_out, nand_28_out, nand_29_out, nand_30_out,
       nand_31_out, nand_32_out, nand_33_out, nand_34_out, nand_35_out, nand_36_out, nandmsjkff2_1_oc,
       nandmux2_1_o1, nandmux2_1_o2, nandmux2_2_o1, nandmux2_2_o2, nandmux2_3_o1, nandmux2_3_o2,
       nandmux2_4_o1, nandmux2_4_o2, nandmux2_5_o1, nandmux2_5_o2, nandmux2_6_o1, nandmux2_6_o2,
       nandmux2_7_o1, nandmux2_7_o2, nandmux2_8_o1, nandmux2_8_o2, nandmux2_9_o1, nandmux2_9_o2,
       nandmux2_10_o1, nandmux2_10_o2, nandmux2_11_o1, nandmux2_11_o2, nandmux2_12_o1, nandmux2_12_o2,
       nandmux2_13_o1, nandmux2_13_o2;

  nand nand_1 (nand_1_out, I[0], I[0]);
  NandMUX2 nandmux2_1 (.B1(I[0]), .B2(nand_1_out), .S(L), .A1(1'b1), .A2(1'b1), .O1(nandmux2_1_o1), .O2(nandmux2_1_o2));
  NandMSJKFF2 nandmsjkff2_1 (.J(nandmux2_1_o1), .K(nandmux2_1_o2), .CLK(E), .SB(SB), .O(O[0]), .OC(nandmsjkff2_1_oc));
  nand nand_2 (nand_2_out, nandmsjkff2_1_oc, nandmsjkff2_1_oc);
  nand nand_3 (nand_3_out, I[1], I[1]);
  NandMUX2 nandmux2_2 (
    .B1(I[1]), .B2(nand_3_out), .S(L), .A1(nand_2_out), .A2(nand_2_out), .O1(nandmux2_2_o1),
    .O2(nandmux2_2_o2));
  NandMSJKFF2 nandmsjkff2_2 (.J(nandmux2_2_o1), .K(nandmux2_2_o2), .CLK(E), .SB(SB), .O(O[1]));  // open: OC
  nand nand_4 (nand_4_out, O[0], O[1]);
  nand nand_5 (nand_5_out, nand_4_out, nand_4_out);
  nand nand_6 (nand_6_out, I[2], I[2]);
  NandMUX2 nandmux2_3 (
    .B1(I[2]), .B2(nand_6_out), .S(L), .A1(nand_5_out), .A2(nand_5_out), .O1(nandmux2_3_o1),
    .O2(nandmux2_3_o2));
  NandMSJKFF2 nandmsjkff2_3 (.J(nandmux2_3_o1), .K(nandmux2_3_o2), .CLK(E), .SB(SB), .O(O[2]));  // open: OC
  nand nand_7 (nand_7_out, nand_5_out, O[2]);
  nand nand_8 (nand_8_out, nand_7_out, nand_7_out);
  nand nand_9 (nand_9_out, I[3], I[3]);
  NandMUX2 nandmux2_4 (
    .B1(I[3]), .B2(nand_9_out), .S(L), .A1(nand_8_out), .A2(nand_8_out), .O1(nandmux2_4_o1),
    .O2(nandmux2_4_o2));
  NandMSJKFF2 nandmsjkff2_4 (.J(nandmux2_4_o1), .K(nandmux2_4_o2), .CLK(E), .SB(SB), .O(O[3]));  // open: OC
  nand nand_10 (nand_10_out, nand_8_out, O[3]);
  nand nand_11 (nand_11_out, I[4], I[4]);
  nand nand_12 (nand_12_out, nand_10_out, nand_10_out);
  NandMUX2 nandmux2_5 (
    .B1(I[4]), .B2(nand_11_out), .S(L), .A1(nand_12_out), .A2(nand_12_out), .O1(nandmux2_5_o1),
    .O2(nandmux2_5_o2));
  NandMSJKFF2 nandmsjkff2_5 (.J(nandmux2_5_o1), .K(nandmux2_5_o2), .CLK(E), .SB(SB), .O(O[4]));  // open: OC
  nand nand_13 (nand_13_out, nand_12_out, O[4]);
  nand nand_14 (nand_14_out, nand_13_out, nand_13_out);
  nand nand_15 (nand_15_out, I[5], I[5]);
  NandMUX2 nandmux2_6 (
    .B1(I[5]), .B2(nand_15_out), .S(L), .A1(nand_14_out), .A2(nand_14_out), .O1(nandmux2_6_o1),
    .O2(nandmux2_6_o2));
  NandMSJKFF2 nandmsjkff2_6 (.J(nandmux2_6_o1), .K(nandmux2_6_o2), .CLK(E), .SB(SB), .O(O[5]));  // open: OC
  nand nand_16 (nand_16_out, nand_14_out, O[5]);
  nand nand_17 (nand_17_out, nand_16_out, nand_16_out);
  nand nand_18 (nand_18_out, I[6], I[6]);
  NandMUX2 nandmux2_7 (
    .B1(I[6]), .B2(nand_18_out), .S(L), .A1(nand_17_out), .A2(nand_17_out), .O1(nandmux2_7_o1),
    .O2(nandmux2_7_o2));
  NandMSJKFF2 nandmsjkff2_7 (.J(nandmux2_7_o1), .K(nandmux2_7_o2), .CLK(E), .SB(SB), .O(O[6]));  // open: OC
  nand nand_19 (nand_19_out, nand_17_out, O[6]);
  nand nand_20 (nand_20_out, nand_19_out, nand_19_out);
  nand nand_21 (nand_21_out, I[7], I[7]);
  NandMUX2 nandmux2_8 (
    .B1(I[7]), .B2(nand_21_out), .S(L), .A1(nand_20_out), .A2(nand_20_out), .O1(nandmux2_8_o1),
    .O2(nandmux2_8_o2));
  NandMSJKFF2 nandmsjkff2_8 (.J(nandmux2_8_o1), .K(nandmux2_8_o2), .CLK(E), .SB(SB), .O(O[7]));  // open: OC
  nand nand_22 (nand_22_out, nand_20_out, O[7]);
  nand nand_23 (nand_23_out, nand_22_out, nand_22_out);
  nand nand_24 (nand_24_out, I[8], I[8]);
  NandMUX2 nandmux2_9 (
    .B1(I[8]), .B2(nand_24_out), .S(L), .A1(nand_23_out), .A2(nand_23_out), .O1(nandmux2_9_o1),
    .O2(nandmux2_9_o2));
  NandMSJKFF2 nandmsjkff2_9 (.J(nandmux2_9_o1), .K(nandmux2_9_o2), .CLK(E), .SB(SB), .O(O[8]));  // open: OC
  nand nand_25 (nand_25_out, nand_23_out, O[8]);
  nand nand_26 (nand_26_out, nand_25_out, nand_25_out);
  nand nand_27 (nand_27_out, I[9], I[9]);
  NandMUX2 nandmux2_10 (
    .B1(I[9]), .B2(nand_27_out), .S(L), .A1(nand_26_out), .A2(nand_26_out), .O1(nandmux2_10_o1),
    .O2(nandmux2_10_o2));
  NandMSJKFF2 nandmsjkff2_10 (.J(nandmux2_10_o1), .K(nandmux2_10_o2), .CLK(E), .SB(SB), .O(O[9]));  // open: OC
  nand nand_28 (nand_28_out, nand_26_out, O[9]);
  nand nand_29 (nand_29_out, nand_28_out, nand_28_out);
  nand nand_30 (nand_30_out, I[10], I[10]);
  NandMUX2 nandmux2_11 (
    .B1(I[10]), .B2(nand_30_out), .S(L), .A1(nand_29_out), .A2(nand_29_out), .O1(nandmux2_11_o1),
    .O2(nandmux2_11_o2));
  NandMSJKFF2 nandmsjkff2_11 (.J(nandmux2_11_o1), .K(nandmux2_11_o2), .CLK(E), .SB(SB), .O(O[10]));  // open: OC
  nand nand_31 (nand_31_out, nand_29_out, O[10]);
  nand nand_32 (nand_32_out, nand_31_out, nand_31_out);
  nand nand_33 (nand_33_out, I[11], I[11]);
  NandMUX2 nandmux2_12 (
    .B1(I[11]), .B2(nand_33_out), .S(L), .A1(nand_32_out), .A2(nand_32_out), .O1(nandmux2_12_o1),
    .O2(nandmux2_12_o2));
  NandMSJKFF2 nandmsjkff2_12 (.J(nandmux2_12_o1), .K(nandmux2_12_o2), .CLK(E), .SB(SB), .O(O[11]));  // open: OC
  nand nand_34 (nand_34_out, nand_32_out, O[11]);
  nand nand_35 (nand_35_out, nand_34_out, nand_34_out);
  nand nand_36 (nand_36_out, I[12], I[12]);
  NandMUX2 nandmux2_13 (
    .B1(I[12]), .B2(nand_36_out), .S(L), .A1(nand_35_out), .A2(nand_35_out), .O1(nandmux2_13_o1),
    .O2(nandmux2_13_o2));
  NandMSJKFF2 nandmsjkff2_13 (.J(nandmux2_13_o1), .K(nandmux2_13_o2), .CLK(E), .SB(SB), .O(O[12]));  // open: OC
endmodule

module NandSRLatch (
  input  SC,
  input  SB,
  input  RC,
  output O,
  output OC
);

  nand nand_1 (O, SC, SB, OC);
  nand nand_2 (OC, O, RC);
endmodule

module NandSRFF (
  input  S,
  input  R,
  input  CLK,
  input  SB,
  output O,
  output OC
);

  wire nand_1_out, nand_2_out;

  nand nand_1 (nand_1_out, S, CLK);
  nand nand_2 (nand_2_out, CLK, R);
  NandSRLatch nandsrlatch_1 (.SB(SB), .SC(nand_1_out), .RC(nand_2_out), .O(O), .OC(OC));
endmodule

module NandMSJKFF2 (
  input  J,
  input  K,
  input  CLK,
  input  SB,
  output O,
  output OC
);

  wire nand_1_out, nand_2_out, nand_3_out, nand_4_out, nand_5_out, nandsrff_1_o, nandsrff_1_oc;

  nand nand_1 (nand_1_out, OC, J);
  nand nand_2 (nand_2_out, K, O);
  nand nand_3 (nand_3_out, nand_1_out, nand_1_out);
  nand nand_4 (nand_4_out, nand_2_out, nand_2_out);
  NandSRFF nandsrff_1 (.S(nand_3_out), .R(nand_4_out), .CLK(CLK), .SB(SB), .O(nandsrff_1_o), .OC(nandsrff_1_oc));
  nand nand_5 (nand_5_out, CLK, CLK);
  NandSRFF nandsrff_2 (.S(nandsrff_1_o), .R(nandsrff_1_oc), .CLK(nand_5_out), .SB(SB), .O(O), .OC(OC));
endmodule

module NandMUX2 (
  input  A1,
  input  B1,
  input  A2,
  input  B2,
  input  S,
  output O1,
  output O2
);

  NandMUX nandmux_1 (.A(A1), .S(S), .B(B1), .O(O1));
  NandMUX nandmux_2 (.A(A2), .S(S), .B(B2), .O(O2));
endmodule

module main_alt (
  input  in_1,
  input  in_2,
  input  in_3,
  input  in_4
);

  wire ALU_c, clock_1_out, flagsregister_1_p1, flagsregister_1_p2, flagsregister_1_p3, flagsregister_1_p4,
       flagsregister_1_p5, flagsregister_1_p6, flagsregister_1_p7, flagsregister_1_p8, flagsregister_1_p9,
       flagsregister_1_p10, flagsregister_1_p11, flagsregister_1_p12, flagsregister_1_p13,
       flagsregister_1_p14, flagsregister_1_p15, flagsregister_1_p16, flagsregister_1_p17,
       flagsregister_1_p18, nand_1_out, nandallbitsorcheck10_1_o, nandmux_1_o, undriven, undriven_2,
       undriven_3, undriven_4, undriven_5, undriven_6, undriven_7, undriven_8, undriven_9, undriven_10,
       undriven_11;
  wire [1:0] nanddemux8_1_b, UPPER_BITS_HOLDER_o;
  wire [7:0] nanddemux8_1_a, ram_1_data;
  wire [7:7] nanddemux8_1_b_2;
  wire [9:0] A_o, ALU_o, ALU_RESULT_o, B_o, C_o, controlledbuffer10_1_o, D_o, DATA_ADDRESS_TRANSLATOR_a,
       DATA_ADDRESS_TRANSLATOR_b;
  wire [12:0] ADDRESS_HOLDER_o, MAR_o, PC_o, PC_OUT_o;
  wire [14:13] MEMORY_MODE_FLAG_o;

  NandSyncCounter PC (.I(PC_OUT_o), .L(undriven_6), .O(PC_o));  // open: SB, E
  NandMSJKFF2 MEMORY_MODE_FLAG (.J(in_1), .K(in_2), .CLK(in_3), .SB(in_4), .O(MEMORY_MODE_FLAG_o[13]));  // open: OC
  ControlledBuffer13 PC_OUT (.I(PC_o), .S(undriven_11), .O(PC_OUT_o));
  nand nand_1 (nand_1_out, MEMORY_MODE_FLAG_o[13], MEMORY_MODE_FLAG_o[13]);
  NandRegisterHL13 ADDRESS_HOLDER (
    .LL_0_9(undriven_3), .LH_10_12(undriven_4), .I(PC_OUT_o), .O(ADDRESS_HOLDER_o));  // open: E, SB
  ControlledBuffer13 ADDRESS_HOLDER_OUT (.I(ADDRESS_HOLDER_o), .S(undriven_5), .O(PC_OUT_o));
  NandRegister13 MAR (.L(undriven_8), .I(PC_OUT_o), .SB(undriven_7), .O(MAR_o));  // open: E
  ControlledBuffer13 DATA_ADDRESS_LINK (
    .I({DATA_ADDRESS_TRANSLATOR_b[2:0], DATA_ADDRESS_TRANSLATOR_a}), .S(undriven_2), .O(PC_OUT_o));
  NandMUX nandmux_1 (.A(nand_1_out), .S(clock_1_out), .B(undriven_10), .O(nandmux_1_o));
  RAM #(.addrWidth(15), .databus("bidir"), .\type ("nonvolatile")) ram_1 (
    .addr({MEMORY_MODE_FLAG_o, MAR_o}), .we(undriven_9), .oe(1'b1), .data(ram_1_data));  // open: clk
  NandRegister2 UPPER_BITS_HOLDER (
    .L(MEMORY_MODE_FLAG_o[13]), .I(nanddemux8_1_b), .O(UPPER_BITS_HOLDER_o));  // open: E, SB
  Clock clock_1 (.out(clock_1_out));
  NandDEMUX10 DATA_ADDRESS_TRANSLATOR (
    .I(controlledbuffer10_1_o), .S(undriven), .A(DATA_ADDRESS_TRANSLATOR_a), .B(DATA_ADDRESS_TRANSLATOR_b));
  NandDEMUX8 nanddemux8_1 (
    .I(ram_1_data), .S(MEMORY_MODE_FLAG_o[13]), .A(nanddemux8_1_a),
    .B({{6{nanddemux8_1_b_2[7]}}, nanddemux8_1_b}));
  // FlagsRegister flagsregister_1: pin names not known; wires that end beside it: flagsregister_1_p1, flagsregister_1_p2, flagsregister_1_p3, flagsregister_1_p4, flagsregister_1_p5, flagsregister_1_p6, flagsregister_1_p7, flagsregister_1_p8, flagsregister_1_p9, flagsregister_1_p10, flagsregister_1_p11, flagsregister_1_p12, flagsregister_1_p13, flagsregister_1_p14, flagsregister_1_p15, flagsregister_1_p16, flagsregister_1_p17, flagsregister_1_p18
  ControlledBuffer10 controlledbuffer10_1 (
    .I({UPPER_BITS_HOLDER_o, nanddemux8_1_a}), .S(nandmux_1_o), .O(controlledbuffer10_1_o));
  ControlledBuffer10 CONTROL_LOGIC_OUT (.O(controlledbuffer10_1_o));  // open: I, S
  NandRegisterHL10 A (
    .I(controlledbuffer10_1_o), .LH(flagsregister_1_p7), .LL(flagsregister_1_p6), .O(A_o));  // open: E, SB
  NandRegisterHL10 B (
    .I(controlledbuffer10_1_o), .LH(flagsregister_1_p9), .LL(flagsregister_1_p8), .O(B_o));  // open: E, SB
  NandRegisterHL10 C (
    .I(controlledbuffer10_1_o), .LH(flagsregister_1_p11), .LL(flagsregister_1_p10), .O(C_o));  // open: E, SB
  NandRegisterHL10 D (
    .I(controlledbuffer10_1_o), .LH(flagsregister_1_p13), .LL(flagsregister_1_p12), .O(D_o));  // open: E, SB
  ControlledBuffer10 controlledbuffer10_2 (.I(A_o), .S(flagsregister_1_p4), .O(controlledbuffer10_1_o));
  ControlledBuffer10 controlledbuffer10_3 (.I(B_o), .S(flagsregister_1_p5), .O(controlledbuffer10_1_o));
  ControlledBuffer10 controlledbuffer10_4 (.I(C_o), .S(flagsregister_1_p15), .O(controlledbuffer10_1_o));
  ControlledBuffer10 controlledbuffer10_5 (.I(D_o), .S(flagsregister_1_p14), .O(controlledbuffer10_1_o));
  NandALU2 ALU (
    .AZ(controlledbuffer10_1_o[5]), .BZ(controlledbuffer10_1_o[7]), .AC(controlledbuffer10_1_o[6]),
    .BC(controlledbuffer10_1_o[8]), .N(flagsregister_1_p16), .OC(controlledbuffer10_1_o[9]), .A(A_o),
    .B(B_o), .O(ALU_o), .C(ALU_c));  // open: S
  NandRegister10 ALU_RESULT (.L(flagsregister_1_p18), .I(ALU_o), .O(ALU_RESULT_o));  // open: E, SB
  NandAllBitsORCheck10 nandallbitsorcheck10_1 (.I(ALU_o), .O(nandallbitsorcheck10_1_o));
  ControlledBuffer10 ALU_OUT (.I(ALU_RESULT_o), .S(flagsregister_1_p17), .O(controlledbuffer10_1_o));
  ALUResultFlagsRegister aluresultflagsregister_1 (
    .L(flagsregister_1_p18), .NZ(nandallbitsorcheck10_1_o), .C(ALU_c));  // open: E, SB, S, NZO, CO, SO
  // also tied to GND on the sheet: nanddemux8_1_b_2[7]

  // Notes on the sheet:
  //   ADDRESS BUS
  //   DATA BUS
endmodule

module NandALU2 (
  input  [9:0] A,
  input  [9:0] B,
  input  AZ,
  input  BZ,
  input  AC,
  input  BC,
  input  N,
  input  OC,
  output [9:0] O,
  output C,
  output S
);

  wire [8:0] nandfulladder10_1_s;
  wire [9:0] nand_1_out, nandinverter10_1_o, nandinverter10_2_o, nandinverter10_3_o, nandmux10_1_o,
       nandmux10_2_o, nandmux10_3_o, nandmux10_4_o, nandmux10_5_o;

  NandMUX10 nandmux10_1 (.S(AZ), .A(A), .B({10{1'b0}}), .O(nandmux10_1_o));
  NandMUX10 nandmux10_2 (.S(BZ), .A(B), .B({10{1'b0}}), .O(nandmux10_2_o));
  NandInverter10 nandinverter10_1 (.I(nandmux10_1_o), .O(nandinverter10_1_o));
  NandInverter10 nandinverter10_2 (.I(nandmux10_2_o), .O(nandinverter10_2_o));
  NandMUX10 nandmux10_3 (.S(AC), .A(nandmux10_1_o), .B(nandinverter10_1_o), .O(nandmux10_3_o));
  NandMUX10 nandmux10_4 (.S(BC), .A(nandmux10_2_o), .B(nandinverter10_2_o), .O(nandmux10_4_o));
  NandFullAdder10 nandfulladder10_1 (.B(nandmux10_4_o), .A(nandmux10_3_o), .C(C), .S({S, nandfulladder10_1_s}));
  nand nand_1 (nand_1_out[0], nandmux10_3_o[0], nandmux10_4_o[0]);
  nand nand_2 (nand_1_out[1], nandmux10_3_o[1], nandmux10_4_o[1]);
  nand nand_3 (nand_1_out[2], nandmux10_3_o[2], nandmux10_4_o[2]);
  nand nand_4 (nand_1_out[3], nandmux10_3_o[3], nandmux10_4_o[3]);
  nand nand_5 (nand_1_out[4], nandmux10_3_o[4], nandmux10_4_o[4]);
  nand nand_6 (nand_1_out[5], nandmux10_3_o[5], nandmux10_4_o[5]);
  nand nand_7 (nand_1_out[6], nandmux10_3_o[6], nandmux10_4_o[6]);
  nand nand_8 (nand_1_out[7], nandmux10_3_o[7], nandmux10_4_o[7]);
  nand nand_9 (nand_1_out[8], nandmux10_3_o[8], nandmux10_4_o[8]);
  nand nand_10 (nand_1_out[9], nandmux10_3_o[9], nandmux10_4_o[9]);
  NandMUX10 nandmux10_5 (.S(N), .A({S, nandfulladder10_1_s}), .B(nand_1_out), .O(nandmux10_5_o));
  NandInverter10 nandinverter10_3 (.I(nandmux10_5_o), .O(nandinverter10_3_o));
  NandMUX10 nandmux10_6 (.S(OC), .A(nandmux10_5_o), .B(nandinverter10_3_o), .O(O));
endmodule

module NandInverter10 (
  input  [9:0] I,
  output [9:0] O
);

  nand nand_1 (O[0], I[0], I[0]);
  nand nand_2 (O[1], I[1], I[1]);
  nand nand_3 (O[2], I[2], I[2]);
  nand nand_4 (O[3], I[3], I[3]);
  nand nand_5 (O[4], I[4], I[4]);
  nand nand_6 (O[5], I[5], I[5]);
  nand nand_7 (O[6], I[6], I[6]);
  nand nand_8 (O[7], I[7], I[7]);
  nand nand_9 (O[8], I[8], I[8]);
  nand nand_10 (O[9], I[9], I[9]);
endmodule

module NandMUX8 (
  input  [7:0] A,
  input  [7:0] B,
  input  S,
  output [7:0] O
);

  NandMUX nandmux_1 (.A(A[0]), .S(S), .B(B[0]), .O(O[0]));
  NandMUX nandmux_2 (.A(A[1]), .S(S), .B(B[1]), .O(O[1]));
  NandMUX nandmux_3 (.A(A[2]), .S(S), .B(B[2]), .O(O[2]));
  NandMUX nandmux_4 (.A(A[3]), .S(S), .B(B[3]), .O(O[3]));
  NandMUX nandmux_5 (.A(A[4]), .S(S), .B(B[4]), .O(O[4]));
  NandMUX nandmux_6 (.A(A[5]), .S(S), .B(B[5]), .O(O[5]));
  NandMUX nandmux_7 (.A(A[6]), .S(S), .B(B[6]), .O(O[6]));
  NandMUX nandmux_8 (.A(A[7]), .S(S), .B(B[7]), .O(O[7]));
endmodule

module NandDEMUX (
  input  I,
  input  S,
  output A,
  output B
);

  wire nand_1_out, nand_2_out, nand_3_out;

  nand nand_1 (nand_1_out, S, S);
  nand nand_2 (nand_2_out, I, nand_1_out);
  nand nand_3 (nand_3_out, I, S);
  nand nand_4 (A, nand_2_out, nand_2_out);
  nand nand_5 (B, nand_3_out, nand_3_out);
endmodule

module NandDEMUX8 (
  input  [7:0] I,
  input  S,
  output [7:0] A,
  output [7:0] B
);

  NandDEMUX nanddemux_1 (.I(I[0]), .S(S), .A(A[0]), .B(A[0]));
  NandDEMUX nanddemux_2 (.I(I[1]), .S(S), .A(B[1]), .B(A[1]));
  NandDEMUX nanddemux_3 (.I(I[2]), .S(S), .A(B[2]), .B(A[2]));
  NandDEMUX nanddemux_4 (.I(I[3]), .S(S), .A(B[3]), .B(A[3]));
  NandDEMUX nanddemux_5 (.I(I[4]), .S(S), .A(B[4]), .B(A[4]));
  NandDEMUX nanddemux_6 (.I(I[5]), .S(S), .A(B[5]), .B(A[5]));
  NandDEMUX nanddemux_7 (.I(I[6]), .S(S), .A(B[6]), .B(A[6]));
  NandDEMUX nanddemux_8 (.I(I[7]), .S(S), .A(B[7]), .B(A[7]));

  assign B[0] = A[0];
endmodule

module NandRegisterHL10 (
  input  E,
  input  LL,
  input  LH,
  input  [9:0] I,
  input  SB,
  output [9:0] O
);

  wire nand_1_out, nand_2_out, nand_3_out, nand_4_out, nanddff_1_oc, nanddff_2_oc, nanddff_3_oc,
       nanddff_4_oc, nanddff_5_oc, nanddff_6_oc, nanddff_7_oc, nanddff_8_oc, nanddff_9_oc, nanddff_10_oc;

  nand nand_1 (nand_1_out, LH, E);
  nand nand_2 (nand_2_out, nand_1_out, nand_1_out);
  nand nand_3 (nand_3_out, E, LL);
  nand nand_4 (nand_4_out, nand_3_out, nand_3_out);
  NandDFF nanddff_1 (.CLK(nand_4_out), .A(I[0]), .SB(SB), .O(O[0]), .OC(nanddff_1_oc));
  // NoConnect on nanddff_1_oc
  NandDFF nanddff_2 (.CLK(nand_4_out), .A(I[1]), .SB(SB), .O(O[1]), .OC(nanddff_2_oc));
  // NoConnect on nanddff_2_oc
  NandDFF nanddff_3 (.CLK(nand_4_out), .A(I[2]), .SB(SB), .O(O[2]), .OC(nanddff_3_oc));
  // NoConnect on nanddff_3_oc
  NandDFF nanddff_4 (.CLK(nand_4_out), .A(I[3]), .SB(SB), .O(O[3]), .OC(nanddff_4_oc));
  // NoConnect on nanddff_4_oc
  NandDFF nanddff_5 (.CLK(nand_4_out), .A(I[4]), .SB(SB), .O(O[4]), .OC(nanddff_5_oc));
  // NoConnect on nanddff_5_oc
  NandDFF nanddff_6 (.CLK(nand_2_out), .A(I[5]), .SB(SB), .O(O[5]), .OC(nanddff_6_oc));
  // NoConnect on nanddff_6_oc
  NandDFF nanddff_7 (.CLK(nand_2_out), .A(I[6]), .SB(SB), .O(O[6]), .OC(nanddff_7_oc));
  // NoConnect on nanddff_7_oc
  NandDFF nanddff_8 (.CLK(nand_2_out), .A(I[7]), .SB(SB), .O(O[7]), .OC(nanddff_8_oc));
  // NoConnect on nanddff_8_oc
  NandDFF nanddff_9 (.CLK(nand_2_out), .A(I[8]), .SB(SB), .O(O[8]), .OC(nanddff_9_oc));
  // NoConnect on nanddff_9_oc
  NandDFF nanddff_10 (.CLK(nand_2_out), .A(I[9]), .SB(SB), .O(O[9]), .OC(nanddff_10_oc));
  // NoConnect on nanddff_10_oc
endmodule

module NandAllBitsORCheck10 (
  input  [9:0] I,
  output O
);

  wire nand_1_out, nand_2_out, nand_3_out, nand_4_out, nand_5_out, nand_6_out, nand_7_out, nand_8_out,
       nand_9_out, nand_10_out, nand_11_out, nand_12_out, nand_13_out, nand_14_out, nand_15_out, nand_16_out,
       nand_17_out, nand_18_out, nand_19_out, nand_20_out, nand_21_out, nand_22_out, nand_23_out,
       nand_24_out, nand_25_out, nand_26_out;

  nand nand_1 (nand_1_out, I[0], I[0]);
  nand nand_2 (nand_2_out, I[1], I[1]);
  nand nand_3 (nand_3_out, nand_1_out, nand_2_out);
  nand nand_4 (nand_4_out, nand_3_out, nand_3_out);
  nand nand_5 (nand_5_out, I[2], I[2]);
  nand nand_6 (nand_6_out, nand_4_out, nand_5_out);
  nand nand_7 (nand_7_out, nand_6_out, nand_6_out);
  nand nand_8 (nand_8_out, I[3], I[3]);
  nand nand_9 (nand_9_out, nand_7_out, nand_8_out);
  nand nand_10 (nand_10_out, nand_9_out, nand_9_out);
  nand nand_11 (nand_11_out, I[4], I[4]);
  nand nand_12 (nand_12_out, nand_10_out, nand_11_out);
  nand nand_13 (nand_13_out, nand_12_out, nand_12_out);
  nand nand_14 (nand_14_out, I[5], I[5]);
  nand nand_15 (nand_15_out, nand_13_out, nand_14_out);
  nand nand_16 (nand_16_out, nand_15_out, nand_15_out);
  nand nand_17 (nand_17_out, I[6], I[6]);
  nand nand_18 (nand_18_out, nand_16_out, nand_17_out);
  nand nand_19 (nand_19_out, nand_18_out, nand_18_out);
  nand nand_20 (nand_20_out, I[7], I[7]);
  nand nand_21 (nand_21_out, nand_19_out, nand_20_out);
  nand nand_22 (nand_22_out, nand_21_out, nand_21_out);
  nand nand_23 (nand_23_out, I[8], I[8]);
  nand nand_24 (nand_24_out, nand_22_out, nand_23_out);
  nand nand_25 (nand_25_out, nand_24_out, nand_24_out);
  nand nand_26 (nand_26_out, I[9], I[9]);
  nand nand_27 (O, nand_25_out, nand_26_out);
endmodule

module ALUResultFlagsRegister (
  input  E,
  input  L,
  input  NZ,
  input  C,
  input  S,
  input  SB,
  output NZO,
  output CO,
  output SO
);

  wire nand_1_out, nand_2_out, nanddff_1_oc, nanddff_2_oc, nanddff_3_oc;
  wire [9:0] controlledbuffer10_1_o, nandregisterhl10_1_o, undriven;

  NandRegisterHL10 nandregisterhl10_1 (.I(undriven), .O(nandregisterhl10_1_o));  // open: LH, E, LL, SB
  nand nand_1 (nand_1_out, E, L);
  ControlledBuffer10 controlledbuffer10_1 (.I(nandregisterhl10_1_o), .O(controlledbuffer10_1_o));  // open: S
  nand nand_2 (nand_2_out, nand_1_out, nand_1_out);
  NandDFF nanddff_1 (.CLK(nand_2_out), .A(NZ), .SB(SB), .O(NZO), .OC(nanddff_1_oc));
  // NoConnect on nanddff_1_oc
  NandDFF nanddff_2 (.CLK(nand_2_out), .A(C), .SB(SB), .O(CO), .OC(nanddff_2_oc));
  // NoConnect on nanddff_2_oc
  NandDFF nanddff_3 (.CLK(nand_2_out), .A(S), .SB(SB), .O(SO), .OC(nanddff_3_oc));
  // NoConnect on nanddff_3_oc
endmodule

module FlagsRegister (
  input  E,
  input  L,
  input  SB,
  input  PC_LOAD,
  input  PC_OUT,
  input  MAR_LOAD,
  input  A_OUT,
  input  B_OUT,
  input  A_LOAD_LOW,
  input  A_LOAD_HIGH,
  input  B_LOAD_LOW,
  input  B_LOAD_HIGH,
  input  C_LOAD_LOW,
  input  C_LOAD_HIGH,
  input  D_LOAD_LOW,
  input  D_LOAD_HIGH,
  input  D_OUT,
  input  C_OUT,
  input  ALU_NAND,
  input  ALU_OUT,
  input  ALU_SAVE,
  output F_PC_LOAD,
  output F_PC_OUT,
  output F_MAR_LOAD,
  output F_A_OUT,
  output F_B_OUT,
  output F_A_LOAD_L,
  output F_A_LOAD_H,
  output F_B_LOAD_L,
  output F_B_LOAD_H,
  output F_C_LOAD_L,
  output F_C_LOAD_H,
  output F_D_LOAD_L,
  output F_D_LOAD_H,
  output F_D_OUT,
  output F_C_OUT,
  output F_ALU_NAND,
  output F_ALU_OUT,
  output F_ALU_SAVE
);

  wire nand_1_out, nand_2_out;

  nand nand_1 (nand_1_out, E, L);
  nand nand_2 (nand_2_out, nand_1_out, nand_1_out);
  NandDFF nanddff_1 (.CLK(nand_2_out), .A(PC_LOAD), .SB(SB), .O(F_PC_LOAD));  // open: OC
  NandDFF nanddff_2 (.CLK(nand_2_out), .A(PC_OUT), .O(F_PC_OUT));  // open: SB, OC
  NandDFF nanddff_3 (.CLK(nand_2_out), .A(MAR_LOAD), .O(F_MAR_LOAD));  // open: SB, OC
  NandDFF nanddff_4 (.CLK(nand_2_out), .A(A_OUT), .O(F_A_OUT));  // open: SB, OC
  NandDFF nanddff_5 (.CLK(nand_2_out), .A(B_OUT), .O(F_B_OUT));  // open: SB, OC
  NandDFF nanddff_6 (.CLK(nand_2_out), .A(A_LOAD_LOW), .O(F_A_LOAD_L));  // open: SB, OC
  NandDFF nanddff_7 (.CLK(nand_2_out), .A(A_LOAD_HIGH), .O(F_A_LOAD_H));  // open: SB, OC
  NandDFF nanddff_8 (.CLK(nand_2_out), .A(B_LOAD_LOW), .O(F_B_LOAD_L));  // open: SB, OC
  NandDFF nanddff_9 (.CLK(nand_2_out), .A(B_LOAD_HIGH), .O(F_B_LOAD_H));  // open: SB, OC
  NandDFF nanddff_10 (.CLK(nand_2_out), .A(C_LOAD_LOW), .O(F_C_LOAD_L));  // open: SB, OC
  NandDFF nanddff_11 (.CLK(nand_2_out), .A(C_LOAD_HIGH), .O(F_C_LOAD_H));  // open: SB, OC
  NandDFF nanddff_12 (.CLK(nand_2_out), .A(D_LOAD_LOW), .O(F_D_LOAD_L));  // open: SB, OC
  NandDFF nanddff_13 (.CLK(nand_2_out), .A(D_LOAD_HIGH), .SB(SB), .O(F_D_LOAD_H));  // open: OC
  NandDFF nanddff_14 (.CLK(nand_2_out), .A(D_OUT), .SB(SB), .O(F_D_OUT));  // open: OC
  NandDFF nanddff_15 (.CLK(nand_2_out), .A(C_OUT), .SB(SB), .O(F_C_OUT));  // open: OC
  NandDFF nanddff_16 (.CLK(nand_2_out), .A(ALU_NAND), .SB(SB), .O(F_ALU_NAND));  // open: OC
  NandDFF nanddff_17 (.CLK(nand_2_out), .A(ALU_OUT), .SB(SB), .O(F_ALU_OUT));  // open: OC
  NandDFF nanddff_18 (.CLK(nand_2_out), .A(ALU_SAVE), .SB(SB), .O(F_ALU_SAVE));  // open: OC
endmodule

module main_alt_backup (
  input  H
);

  wire ALU_c, flagsregister_1_f_a_load_h, flagsregister_1_f_a_load_l, flagsregister_1_f_a_out,
       flagsregister_1_f_alu_nand, flagsregister_1_f_alu_out, flagsregister_1_f_alu_save,
       flagsregister_1_f_b_load_h, flagsregister_1_f_b_load_l, flagsregister_1_f_b_out,
       flagsregister_1_f_c_load_h, flagsregister_1_f_c_load_l, flagsregister_1_f_c_out,
       flagsregister_1_f_d_load_h, flagsregister_1_f_d_load_l, flagsregister_1_f_d_out,
       flagsregister_1_f_mar_load, flagsregister_1_f_pc_out, nand_1_out, nandallbitsorcheck10_1_o, PC_p2;
  wire [7:0] nanddemux8_1_a, rom_1_data;
  wire [7:2] nanddemux8_1_b;
  wire [9:0] A_o, ALU_o, ALU_RESULT_o, B_o, C_o, D_o, nandregister8_1_o, PC_p1, PC_p3;
  wire [14:0] undriven;

  ROM #(.addrWidth(15)) rom_1 (.addr({undriven[14:11], H, undriven[9:0]}), .data(rom_1_data));
  NandRegister10 nandregister10_1 (.L(flagsregister_1_f_mar_load), .I(PC_p1), .O(undriven[9:0]));  // open: E, SB
  nand nand_1 (nand_1_out, H, H);
  NandDEMUX8 nanddemux8_1 (.I(rom_1_data), .S(H), .A(nanddemux8_1_a), .B({nanddemux8_1_b, nandregister8_1_o[9:8]}));
  RAM ram_1 ();  // open: addr, we, oe, clk, din, dout
  NandRegister8 nandregister8_1 (.L(nand_1_out), .I(nanddemux8_1_a), .O(nandregister8_1_o[7:0]));  // open: E, SB
  // NandSyncCounter PC: pin names not known; wires that end beside it: PC_p1, PC_p2, PC_p3
  ControlledBuffer10 controlledbuffer10_1 (.I(PC_p3), .S(flagsregister_1_f_pc_out), .O(PC_p1));
  ControlledBuffer10 controlledbuffer10_2 (.I(nandregister8_1_o), .O(PC_p1));  // open: S
  FlagsRegister flagsregister_1 (
    .F_B_LOAD_H(flagsregister_1_f_b_load_h), .F_C_LOAD_L(flagsregister_1_f_c_load_l),
    .F_C_LOAD_H(flagsregister_1_f_c_load_h), .F_D_LOAD_L(flagsregister_1_f_d_load_l),
    .F_D_LOAD_H(flagsregister_1_f_d_load_h), .F_D_OUT(flagsregister_1_f_d_out),
    .F_C_OUT(flagsregister_1_f_c_out), .F_ALU_NAND(flagsregister_1_f_alu_nand),
    .F_ALU_OUT(flagsregister_1_f_alu_out), .F_ALU_SAVE(flagsregister_1_f_alu_save), .F_PC_LOAD(PC_p2),
    .F_PC_OUT(flagsregister_1_f_pc_out), .F_MAR_LOAD(flagsregister_1_f_mar_load),
    .F_A_OUT(flagsregister_1_f_a_out), .F_B_OUT(flagsregister_1_f_b_out),
    .F_A_LOAD_L(flagsregister_1_f_a_load_l), .F_A_LOAD_H(flagsregister_1_f_a_load_h),
    .F_B_LOAD_L(flagsregister_1_f_b_load_l));  // open: SB, E, L, B_LOAD_HIGH, C_LOAD_LOW, C_LOAD_HIGH, D_LOAD_LOW, D_LOAD_HIGH, D_OUT, C_OUT, ALU_NAND, ALU_OUT, ALU_SAVE, PC_LOAD, PC_OUT, MAR_LOAD, A_OUT, B_OUT, A_LOAD_LOW, A_LOAD_HIGH, B_LOAD_LOW
  NandRegisterHL10 A (
    .I(PC_p1), .LH(flagsregister_1_f_a_load_h), .LL(flagsregister_1_f_a_load_l), .O(A_o));  // open: E, SB
  NandRegisterHL10 B (
    .I(PC_p1), .LH(flagsregister_1_f_b_load_h), .LL(flagsregister_1_f_b_load_l), .O(B_o));  // open: E, SB
  NandRegisterHL10 C (
    .I(PC_p1), .LH(flagsregister_1_f_c_load_h), .LL(flagsregister_1_f_c_load_l), .O(C_o));  // open: E, SB
  NandRegisterHL10 D (
    .I(PC_p1), .LH(flagsregister_1_f_d_load_h), .LL(flagsregister_1_f_d_load_l), .O(D_o));  // open: E, SB
  ControlledBuffer10 controlledbuffer10_3 (.I(A_o), .S(flagsregister_1_f_a_out), .O(PC_p1));
  ControlledBuffer10 controlledbuffer10_4 (.I(B_o), .S(flagsregister_1_f_b_out), .O(PC_p1));
  ControlledBuffer10 controlledbuffer10_5 (.I(C_o), .S(flagsregister_1_f_c_out), .O(PC_p1));
  ControlledBuffer10 controlledbuffer10_6 (.I(D_o), .S(flagsregister_1_f_d_out), .O(PC_p1));
  NandALU2 ALU (
    .AZ(PC_p1[5]), .BZ(PC_p1[7]), .AC(PC_p1[6]), .BC(PC_p1[8]), .N(flagsregister_1_f_alu_nand),
    .OC(PC_p1[9]), .A(A_o), .B(B_o), .O(ALU_o), .C(ALU_c));  // open: S
  NandRegister10 ALU_RESULT (.L(flagsregister_1_f_alu_save), .I(ALU_o), .O(ALU_RESULT_o));  // open: E, SB
  NandAllBitsORCheck10 nandallbitsorcheck10_1 (.I(ALU_o), .O(nandallbitsorcheck10_1_o));
  ControlledBuffer10 ALU_OUT (.I(ALU_RESULT_o), .S(flagsregister_1_f_alu_out), .O(PC_p1));
  ALUResultFlagsRegister aluresultflagsregister_1 (
    .L(flagsregister_1_f_alu_save), .NZ(nandallbitsorcheck10_1_o), .C(ALU_c));  // open: E, SB, S, NZO, CO, SO
endmodule

module ControlledBuffer13 (
  input  [12:0] I,
  input  S,
  output [12:0] O
);

  assign O[0] = S ? I[0] : 1'bz;  // Controlled_Buffer controlled_buffer_1
  assign O[1] = S ? I[1] : 1'bz;  // Controlled_Buffer controlled_buffer_2
  assign O[2] = S ? I[2] : 1'bz;  // Controlled_Buffer controlled_buffer_3
  assign O[3] = S ? I[3] : 1'bz;  // Controlled_Buffer controlled_buffer_4
  assign O[4] = S ? I[4] : 1'bz;  // Controlled_Buffer controlled_buffer_5
  assign O[5] = S ? I[5] : 1'bz;  // Controlled_Buffer controlled_buffer_6
  assign O[6] = S ? I[6] : 1'bz;  // Controlled_Buffer controlled_buffer_7
  assign O[7] = S ? I[7] : 1'bz;  // Controlled_Buffer controlled_buffer_8
  assign O[8] = S ? I[8] : 1'bz;  // Controlled_Buffer controlled_buffer_9
  assign O[9] = S ? I[9] : 1'bz;  // Controlled_Buffer controlled_buffer_10
  assign O[10] = S ? I[10] : 1'bz;  // Controlled_Buffer controlled_buffer_11
  assign O[11] = S ? I[11] : 1'bz;  // Controlled_Buffer controlled_buffer_12
  assign O[12] = S ? I[12] : 1'bz;  // Controlled_Buffer controlled_buffer_13
endmodule

module NandRegister13 (
  input  E,
  input  L,
  input  [12:0] I,
  input  SB,
  output [12:0] O
);

  wire nand_1_out, nand_2_out, nanddff_1_oc, nanddff_2_oc, nanddff_3_oc, nanddff_4_oc, nanddff_5_oc,
       nanddff_6_oc, nanddff_7_oc, nanddff_8_oc, nanddff_9_oc, nanddff_10_oc, nanddff_11_oc, nanddff_12_oc,
       nanddff_13_oc;

  nand nand_1 (nand_1_out, E, L);
  nand nand_2 (nand_2_out, nand_1_out, nand_1_out);
  NandDFF nanddff_1 (.CLK(nand_2_out), .A(I[0]), .SB(SB), .O(O[0]), .OC(nanddff_1_oc));
  // NoConnect on nanddff_1_oc
  NandDFF nanddff_2 (.CLK(nand_2_out), .A(I[1]), .SB(SB), .O(O[1]), .OC(nanddff_2_oc));
  // NoConnect on nanddff_2_oc
  NandDFF nanddff_3 (.CLK(nand_2_out), .A(I[2]), .SB(SB), .O(O[2]), .OC(nanddff_3_oc));
  // NoConnect on nanddff_3_oc
  NandDFF nanddff_4 (.CLK(nand_2_out), .A(I[3]), .SB(SB), .O(O[3]), .OC(nanddff_4_oc));
  // NoConnect on nanddff_4_oc
  NandDFF nanddff_5 (.CLK(nand_2_out), .A(I[4]), .SB(SB), .O(O[4]), .OC(nanddff_5_oc));
  // NoConnect on nanddff_5_oc
  NandDFF nanddff_6 (.CLK(nand_2_out), .A(I[5]), .SB(SB), .O(O[5]), .OC(nanddff_6_oc));
  // NoConnect on nanddff_6_oc
  NandDFF nanddff_7 (.CLK(nand_2_out), .A(I[6]), .SB(SB), .O(O[6]), .OC(nanddff_7_oc));
  // NoConnect on nanddff_7_oc
  NandDFF nanddff_8 (.CLK(nand_2_out), .A(I[7]), .SB(SB), .O(O[7]), .OC(nanddff_8_oc));
  // NoConnect on nanddff_8_oc
  NandDFF nanddff_9 (.CLK(nand_2_out), .A(I[8]), .SB(SB), .O(O[8]), .OC(nanddff_9_oc));
  // NoConnect on nanddff_9_oc
  NandDFF nanddff_10 (.CLK(nand_2_out), .A(I[9]), .SB(SB), .O(O[9]), .OC(nanddff_10_oc));
  // NoConnect on nanddff_10_oc
  NandDFF nanddff_11 (.CLK(nand_2_out), .A(I[10]), .SB(SB), .O(O[10]), .OC(nanddff_11_oc));
  // NoConnect on nanddff_11_oc
  NandDFF nanddff_12 (.CLK(nand_2_out), .A(I[11]), .SB(SB), .O(O[11]), .OC(nanddff_12_oc));
  // NoConnect on nanddff_12_oc
  NandDFF nanddff_13 (.CLK(nand_2_out), .A(I[12]), .SB(SB), .O(O[12]), .OC(nanddff_13_oc));
  // NoConnect on nanddff_13_oc
endmodule

module NandRegisterHL13 (
  input  E,
  input  LL_0_9,
  input  LH_10_12,
  input  [12:0] I,
  input  SB,
  output [12:0] O
);

  wire nand_1_out, nand_2_out, nand_3_out, nand_4_out, nanddff_1_oc, nanddff_2_oc, nanddff_3_oc,
       nanddff_4_oc, nanddff_5_oc, nanddff_6_oc, nanddff_7_oc, nanddff_8_oc, nanddff_9_oc, nanddff_10_oc,
       nanddff_11_oc, nanddff_12_oc, nanddff_13_oc;

  nand nand_1 (nand_1_out, E, LL_0_9);
  nand nand_2 (nand_2_out, E, LH_10_12);
  nand nand_3 (nand_3_out, nand_1_out, nand_1_out);
  nand nand_4 (nand_4_out, nand_2_out, nand_2_out);
  NandDFF nanddff_1 (.CLK(nand_3_out), .A(I[0]), .SB(SB), .O(O[0]), .OC(nanddff_1_oc));
  // NoConnect on nanddff_1_oc
  NandDFF nanddff_2 (.CLK(nand_3_out), .A(I[1]), .SB(SB), .O(O[1]), .OC(nanddff_2_oc));
  // NoConnect on nanddff_2_oc
  NandDFF nanddff_3 (.CLK(nand_3_out), .A(I[2]), .SB(SB), .O(O[2]), .OC(nanddff_3_oc));
  // NoConnect on nanddff_3_oc
  NandDFF nanddff_4 (.CLK(nand_3_out), .A(I[3]), .SB(SB), .O(O[3]), .OC(nanddff_4_oc));
  // NoConnect on nanddff_4_oc
  NandDFF nanddff_5 (.CLK(nand_3_out), .A(I[4]), .SB(SB), .O(O[4]), .OC(nanddff_5_oc));
  // NoConnect on nanddff_5_oc
  NandDFF nanddff_6 (.CLK(nand_3_out), .A(I[5]), .SB(SB), .O(O[5]), .OC(nanddff_6_oc));
  // NoConnect on nanddff_6_oc
  NandDFF nanddff_7 (.CLK(nand_3_out), .A(I[6]), .SB(SB), .O(O[6]), .OC(nanddff_7_oc));
  // NoConnect on nanddff_7_oc
  NandDFF nanddff_8 (.CLK(nand_3_out), .A(I[7]), .SB(SB), .O(O[7]), .OC(nanddff_8_oc));
  // NoConnect on nanddff_8_oc
  NandDFF nanddff_9 (.CLK(nand_3_out), .A(I[8]), .SB(SB), .O(O[8]), .OC(nanddff_9_oc));
  // NoConnect on nanddff_9_oc
  NandDFF nanddff_10 (.CLK(nand_3_out), .A(I[9]), .SB(SB), .O(O[9]), .OC(nanddff_10_oc));
  // NoConnect on nanddff_10_oc
  NandDFF nanddff_11 (.CLK(nand_4_out), .A(I[10]), .SB(SB), .O(O[10]), .OC(nanddff_11_oc));
  // NoConnect on nanddff_11_oc
  NandDFF nanddff_12 (.CLK(nand_4_out), .A(I[11]), .SB(SB), .O(O[11]), .OC(nanddff_12_oc));
  // NoConnect on nanddff_12_oc
  NandDFF nanddff_13 (.CLK(nand_4_out), .A(I[12]), .SB(SB), .O(O[12]), .OC(nanddff_13_oc));
  // NoConnect on nanddff_13_oc
endmodule

module NandDEMUX2Way (
  input  A,
  input  S1,
  input  S2,
  output O1,
  output O2,
  output O3,
  output O4
);

  wire nand_1_out, nand_2_out, nand_3_out, nand_4_out, nand_5_out, nand_6_out, nand_7_out, nand_8_out,
       nand_9_out, nand_10_out, nand_11_out, nand_12_out, nand_13_out, nand_15_out, nand_16_out, nand_17_out;

  nand nand_1 (nand_1_out, S1, S1);
  nand nand_2 (nand_2_out, S2, S2);
  nand nand_3 (nand_3_out, S1, S1);
  nand nand_4 (nand_4_out, S2, S2);
  nand nand_5 (nand_5_out, A, nand_1_out);
  nand nand_6 (nand_6_out, A, nand_3_out);
  nand nand_7 (nand_7_out, A, S1);
  nand nand_8 (nand_8_out, A, S1);
  nand nand_9 (nand_9_out, nand_5_out, nand_5_out);
  nand nand_10 (nand_10_out, nand_6_out, nand_6_out);
  nand nand_11 (nand_11_out, nand_7_out, nand_7_out);
  nand nand_12 (nand_12_out, nand_8_out, nand_8_out);
  nand nand_13 (nand_13_out, nand_9_out, nand_2_out);
  nand nand_14 (O1, nand_13_out, nand_13_out);
  nand nand_15 (nand_15_out, nand_10_out, S2);
  nand nand_16 (nand_16_out, nand_11_out, nand_4_out);
  nand nand_17 (nand_17_out, nand_12_out, S2);
  nand nand_18 (O2, nand_15_out, nand_15_out);
  nand nand_19 (O3, nand_16_out, nand_16_out);
  nand nand_20 (O4, nand_17_out, nand_17_out);
endmodule

module NandDEMUX2WaySpecial (
  input  A,
  input  S1,
  input  S2,
  output O1,
  output O2,
  output O3
);

  wire nand_1_out, nand_2_out, nand_3_out, nand_4_out, nand_5_out, nand_6_out, nand_7_out, nand_8_out,
       nand_9_out, nand_10_out, nand_11_out;

  nand nand_1 (nand_1_out, S2, S2);
  nand nand_2 (nand_2_out, S1, S1);
  nand nand_3 (nand_3_out, A, S1);
  nand nand_4 (nand_4_out, A, nand_2_out);
  nand nand_5 (nand_5_out, A, S1);
  nand nand_6 (nand_6_out, nand_3_out, nand_3_out);
  nand nand_7 (nand_7_out, nand_4_out, nand_4_out);
  nand nand_8 (nand_8_out, nand_5_out, nand_5_out);
  nand nand_9 (nand_9_out, nand_6_out, nand_1_out);
  nand nand_10 (nand_10_out, nand_7_out, S2);
  nand nand_11 (nand_11_out, nand_8_out, S2);
  nand nand_12 (O1, nand_9_out, nand_9_out);
  nand nand_13 (O2, nand_10_out, nand_10_out);
  nand nand_14 (O3, nand_11_out, nand_11_out);
endmodule

module NandDEMUX2WaySpecial5 (
  input  [4:0] I,
  input  S1,
  input  S2,
  output [4:0] O1,
  output [4:0] O2,
  output [4:0] O3
);

  NandDEMUX2WaySpecial nanddemux2wayspecial_1 (.A(I[0]), .S1(S1), .S2(S2), .O1(O1[0]), .O2(O2[0]), .O3(O3[0]));
  NandDEMUX2WaySpecial nanddemux2wayspecial_2 (.A(I[1]), .S1(S1), .S2(S2), .O1(O1[1]), .O2(O2[1]), .O3(O3[1]));
  NandDEMUX2WaySpecial nanddemux2wayspecial_3 (.A(I[2]), .S1(S1), .S2(S2), .O1(O1[2]), .O2(O2[2]), .O3(O3[2]));
  NandDEMUX2WaySpecial nanddemux2wayspecial_4 (.A(I[3]), .S1(S1), .S2(S2), .O1(O1[3]), .O2(O2[3]), .O3(O3[3]));
  NandDEMUX2WaySpecial nanddemux2wayspecial_5 (.A(I[4]), .S1(S1), .S2(S2), .O1(O1[4]), .O2(O2[4]), .O3(O3[4]));
endmodule

module NandDEMUX10 (
  input  [9:0] I,
  input  S,
  output [9:0] A,
  output [9:0] B
);

  NandDEMUX nanddemux_1 (.I(I[0]), .S(S), .A(A[0]), .B(B[0]));
  NandDEMUX nanddemux_2 (.I(I[1]), .S(S), .A(A[1]), .B(B[1]));
  NandDEMUX nanddemux_3 (.I(I[2]), .S(S), .A(A[2]), .B(B[2]));
  NandDEMUX nanddemux_4 (.I(I[3]), .S(S), .A(A[3]), .B(B[3]));
  NandDEMUX nanddemux_5 (.I(I[4]), .S(S), .A(A[4]), .B(B[4]));
  NandDEMUX nanddemux_6 (.I(I[5]), .S(S), .A(A[5]), .B(B[5]));
  NandDEMUX nanddemux_7 (.I(I[6]), .S(S), .A(A[6]), .B(B[6]));
  NandDEMUX nanddemux_8 (.I(I[7]), .S(S), .A(A[7]), .B(B[7]));
  NandDEMUX nanddemux_9 (.I(I[8]), .S(S), .A(A[8]), .B(B[8]));
  NandDEMUX nanddemux_10 (.I(I[9]), .S(S), .A(A[9]), .B(B[9]));
endmodule

module NandRegister2 (
  input  E,
  input  L,
  input  [1:0] I,
  input  SB,
  output [1:0] O
);

  wire nand_1_out, nand_2_out, nanddff_1_oc, nanddff_2_oc;

  nand nand_1 (nand_1_out, E, L);
  nand nand_2 (nand_2_out, nand_1_out, nand_1_out);
  NandDFF nanddff_1 (.CLK(nand_2_out), .A(I[0]), .SB(SB), .O(O[0]), .OC(nanddff_1_oc));
  // NoConnect on nanddff_1_oc
  NandDFF nanddff_2 (.CLK(nand_2_out), .A(I[1]), .SB(SB), .O(O[1]), .OC(nanddff_2_oc));
  // NoConnect on nanddff_2_oc
endmodule

module main_final (
);

  wire nand_1_out, nand_2_out, nand_3_out, nand_4_out, nand_5_out, nand_6_out, nand_7_out, nand_9_out,
       nand_10_out, nand_11_out, nand_12_out, nand_13_out, nand_14_out, nand_15_out, nand_16_out,
       nand_17_out, nand_18_out, nand_19_out, nand_20_out, nand_22_out, nand_23_out, nand_24_out,
       nand_25_out, nand_26_out, nand_27_out, nand_28_out, nand_29_out, nand_30_out, nand_31_out,
       nand_32_out, nand_33_out, nand_34_out, nand_35_out, nand_36_out, nand_37_out, nand_38_out,
       nand_39_out, nand_40_out, nand_41_out, nand_42_out, nand_43_out, nand_44_out, nand_45_out,
       nand_46_out, nand_47_out, nand_48_out, nand_49_out, nand_50_out, nand_51_out, nand_52_out,
       nand_53_out, nand_54_out, nand_55_out, nand_56_out, nand_57_out, nand_58_out, nand_59_out,
       nand_60_out, nand_61_out, nand_62_out, nand_63_out, nand_64_out, nand_65_out, nand_66_out,
       nand_67_out, nand_68_out, nand_69_out, nand_70_out, nand_71_out, nand_72_out, nand_73_out,
       nand_74_out, nand_75_out, nand_76_out, nand_77_out, nand_78_out, nand_79_out, nand_80_out,
       nand_81_out, nand_82_out, nand_84_out, nand_86_out, nand_87_out, nand_88_out, nand_89_out,
       nand_90_out, nand_93_out, nand_94_out, nand_95_out, nand_97_out, nand_98_out, nand_99_out,
       nand_100_out, nand_101_out, nand_104_out, nand_105_out, nand_106_out, nand_109_out, nand_110_out,
       nand_111_out, nand_112_out, nand_113_out, nand_116_out, nand_117_out, nand_118_out,
       nandallbitsorcheck5_1_o, nandallbitsorcheck10_1_o, nandalu3_1_c, nandalu3_1_s, nandandallbits5_1_o,
       nandmux_2_o, nandmux_3_o, nandmux_5_o, undriven;
  wire [1:0] machinecyclecounter_1_o;
  wire [2:0] aluresultflagsregister_1_nzo;
  wire [3:0] IR_o;
  wire [4:0] nanddemux5_1_a, nanddemux5_1_b, nanddemux5_2_a, nanddemux5_2_b, nanddemux5_3_a, nanddemux5_3_b;
  wire [4:3] nandmux_1_o;
  wire [9:0] A_o, ALU_RESULT_o, B_o, C_o, controlledbuffer10_1_o, D_o, MAR_o, nandalu3_1_o, PC_o, ram_1_data;
  wire [9:5] IR_o_2;
  wire [10:10] controlledbuffer24_1_o_2;
  wire [12:5] nand_102_out;
  wire [14:7] nand_114_out;
  wire [16:6] nanddemux2way_2_o1;
  wire [19:19] nand_96_out;
  wire [23:0] controlledbuffer24_1_o, controlledbuffer24_3_o;
  wire [23:3] nand_91_out;
  wire [23:19] nand_8_out;
  wire [23:22] IR_o_3;

  NandRegisterHL10 A (
    .I(controlledbuffer10_1_o), .LH(controlledbuffer24_1_o[6]), .LL(controlledbuffer24_1_o[5]),
    .SB(undriven), .O(A_o));  // open: E
  NandRegisterHL10 C (
    .I(controlledbuffer10_1_o), .LH(controlledbuffer24_1_o[8]), .LL(controlledbuffer24_1_o[7]),
    .SB(undriven), .O(C_o));  // open: E
  NandALU3 nandalu3_1 (
    .AZ(controlledbuffer10_1_o[5]), .BZ(controlledbuffer10_1_o[6]), .AC(controlledbuffer10_1_o[7]),
    .BC(controlledbuffer10_1_o[8]), .N(controlledbuffer24_1_o[3]), .X(controlledbuffer24_1_o[4]),
    .OC(controlledbuffer10_1_o[9]), .A(A_o), .B(B_o), .O(nandalu3_1_o), .C(nandalu3_1_c), .S(nandalu3_1_s));
  ControlledBuffer10 controlledbuffer10_1 (.I(A_o), .S(controlledbuffer24_1_o[9]), .O(controlledbuffer10_1_o));
  ControlledBuffer10 controlledbuffer10_2 (.I(C_o), .S(controlledbuffer24_1_o[10]), .O(controlledbuffer10_1_o));
  NandAllBitsORCheck10 nandallbitsorcheck10_1 (.I(nandalu3_1_o), .O(nandallbitsorcheck10_1_o));
  NandRegister10 ALU_RESULT (
    .L(controlledbuffer24_1_o[2]), .I(nandalu3_1_o), .SB(undriven), .O(ALU_RESULT_o));  // open: E
  NandRegisterHL10 B (
    .I(controlledbuffer10_1_o), .LH(controlledbuffer24_1_o[12]), .LL(controlledbuffer24_1_o[11]),
    .SB(undriven), .O(B_o));  // open: E
  NandRegisterHL10 D (
    .I(controlledbuffer10_1_o), .LH(controlledbuffer24_1_o[14]), .LL(controlledbuffer24_1_o[13]),
    .SB(undriven), .O(D_o));  // open: E
  MachineCycleCounter machinecyclecounter_1 (.O(machinecyclecounter_1_o));  // open: I, L, SB, E
  ALUResultFlagsRegister aluresultflagsregister_1 (
    .L(controlledbuffer24_1_o[2]), .SB(undriven), .NZ(nandallbitsorcheck10_1_o), .C(nandalu3_1_c),
    .S(nandalu3_1_s), .NZO(aluresultflagsregister_1_nzo[0]), .CO(aluresultflagsregister_1_nzo[1]),
    .SO(aluresultflagsregister_1_nzo[2]));  // open: E
  nand nand_1 (nand_1_out, machinecyclecounter_1_o[1], machinecyclecounter_1_o[1]);
  ControlledBuffer10 controlledbuffer10_3 (.I(ALU_RESULT_o), .S(controlledbuffer24_1_o[1]), .O(controlledbuffer10_1_o));
  ControlledBuffer10 controlledbuffer10_4 (.I(B_o), .S(controlledbuffer24_1_o[15]), .O(controlledbuffer10_1_o));
  ControlledBuffer10 controlledbuffer10_5 (.I(D_o), .S(controlledbuffer24_1_o[16]), .O(controlledbuffer10_1_o));
  nand nand_2 (nand_2_out, machinecyclecounter_1_o[0], machinecyclecounter_1_o[0]);
  ControlledBuffer10 ALU_FLAGS (
    .I({{7{1'b0}}, aluresultflagsregister_1_nzo}), .S(controlledbuffer24_1_o[0]), .O(controlledbuffer10_1_o));
  nand nand_3 (nand_3_out, nand_2_out, nand_1_out);
  nand nand_4 (nand_4_out, nand_2_out, machinecyclecounter_1_o[1]);
  nand nand_5 (nand_5_out, machinecyclecounter_1_o[0], nand_1_out);
  nand nand_6 (nand_6_out, machinecyclecounter_1_o[0], machinecyclecounter_1_o[1]);
  nand nand_7 (nand_7_out, nand_3_out, nand_3_out);
  nand nand_8 (nand_8_out[19], nand_4_out, nand_4_out);
  nand nand_9 (nand_9_out, nand_5_out, nand_5_out);
  nand nand_10 (nand_10_out, nand_6_out, nand_6_out);
  nand nand_11 (nand_11_out, nandandallbits5_1_o, nandandallbits5_1_o);
  nand nand_12 (nand_12_out, nand_95_out, nand_95_out);
  nand nand_13 (nand_13_out, nand_11_out, nand_12_out);
  nand nand_14 (nand_14_out, nand_13_out, nand_13_out);
  NandRegisterHL10 MAR (
    .I(controlledbuffer10_1_o), .LH(controlledbuffer24_1_o[23]), .LL(controlledbuffer24_1_o[22]),
    .SB(undriven), .O(MAR_o));  // open: E
  NandSyncCounter10 PC (
    .I(controlledbuffer10_1_o), .L(controlledbuffer24_1_o[17]), .SB(undriven), .E(nand_16_out), .O(PC_o));
  nand nand_15 (nand_15_out, nand_10_out, nand_14_out);
  nand nand_16 (nand_16_out, nand_15_out, nand_15_out);
  RAM #(.addrWidth(11), .dataWidth(10), .databus("bidir"), .\type ("nonvolatile")) ram_1 (
    .addr({controlledbuffer24_1_o_2[10], MAR_o}), .we(controlledbuffer24_1_o[21]), .oe(1'b1),
    .data(ram_1_data));  // open: clk
  ControlledBuffer10 controlledbuffer10_6 (.I(PC_o), .S(controlledbuffer24_1_o[18]), .O(controlledbuffer10_1_o));
  nand nand_17 (nand_17_out, nand_7_out, nand_7_out);
  nand nand_18 (nand_18_out, nand_8_out[19], nand_8_out[19]);
  nand nand_19 (nand_19_out, nand_7_out, nand_14_out);
  nand nand_20 (nand_20_out, nand_17_out, nand_18_out);
  nand nand_21 (nand_8_out[23], nand_19_out, nand_19_out);
  nand nand_22 (nand_22_out, nand_20_out, nand_20_out);
  nand nand_23 (nand_23_out, nand_10_out, nand_10_out);
  nand nand_24 (nand_24_out, nand_22_out, nand_23_out);
  ControlledBuffer10 controlledbuffer10_7 (.I(ram_1_data), .S(controlledbuffer24_1_o[19]), .O(controlledbuffer10_1_o));
  ControlledBuffer24 controlledbuffer24_1 (
    .I({{2{nand_8_out[23]}}, 2'b00, nand_8_out[19], nand_8_out[23], {18{1'b0}}}), .S(nand_24_out),
    .O({controlledbuffer24_1_o[23:21], controlledbuffer24_1_o_2[10], controlledbuffer24_1_o[19:0]}));
  NandRegister10 IR (.L(nand_8_out[19]), .I(controlledbuffer10_1_o), .O({IR_o_2, IR_o_3[22], IR_o}));  // open: E, SB
  ControlledBuffer24 controlledbuffer24_2 (
    .I(controlledbuffer24_3_o), .S(nand_9_out),
    .O({controlledbuffer24_1_o[23:21], controlledbuffer24_1_o_2[10], controlledbuffer24_1_o[19:0]}));
  nand nand_25 (nand_25_out, IR_o[1], IR_o[1]);
  nand nand_26 (nand_26_out, IR_o[2], IR_o[2]);
  nand nand_27 (nand_27_out, IR_o[0], IR_o[0]);
  nand nand_28 (nand_28_out, IR_o[1], IR_o[1]);
  NandAllBitsORCheck5 nandallbitsorcheck5_1 (.I({IR_o_3[22], IR_o}), .O(nandallbitsorcheck5_1_o));
  NandAndAllBits5 nandandallbits5_1 (.I({IR_o_3[22], IR_o}), .O(nandandallbits5_1_o));
  nand nand_29 (nand_29_out, IR_o[0], IR_o[1]);
  nand nand_30 (nand_30_out, IR_o[0], IR_o[2]);
  nand nand_31 (nand_31_out, IR_o[1], IR_o[1]);
  nand nand_32 (nand_32_out, IR_o[0], IR_o[1]);
  nand nand_33 (nand_33_out, IR_o[2], IR_o[2]);
  nand nand_34 (nand_34_out, nand_25_out, nand_26_out);
  nand nand_35 (nand_35_out, nand_27_out, nand_28_out);
  NandDEMUX2Way nanddemux2way_1 (
    .A(1'b1), .S1(IR_o_2[5]), .S2(IR_o_2[6]), .O1(nanddemux2way_2_o1[9]), .O2(nanddemux2way_2_o1[15]),
    .O3(nanddemux2way_2_o1[10]), .O4(nanddemux2way_2_o1[16]));
  NandDEMUX2Way nanddemux2way_2 (
    .A(1'b1), .S1(IR_o_2[8]), .S2(IR_o_2[9]), .O1(nanddemux2way_2_o1[6]), .O2(nanddemux2way_2_o1[12]),
    .O3(nanddemux2way_2_o1[8]), .O4(nanddemux2way_2_o1[14]));
  nand nand_36 (nand_36_out, IR_o[0], IR_o[0]);
  nand nand_37 (nand_37_out, IR_o[1], IR_o[1]);
  nand nand_38 (nand_38_out, nand_29_out, nand_29_out);
  nand nand_39 (nand_39_out, nand_30_out, nand_30_out);
  nand nand_40 (nand_40_out, nand_32_out, nand_32_out);
  nand nand_41 (nand_41_out, nand_34_out, nand_34_out);
  nand nand_42 (nand_42_out, nand_35_out, nand_35_out);
  nand nand_43 (nand_43_out, IR_o[2], IR_o[2]);
  nand nand_44 (nand_44_out, nandallbitsorcheck5_1_o, nandallbitsorcheck5_1_o);
  nand nand_45 (nand_45_out, nand_36_out, nand_37_out);
  nand nand_46 (nand_46_out, nand_38_out, IR_o[2]);
  nand nand_47 (nand_47_out, nand_39_out, nand_31_out);
  nand nand_48 (nand_48_out, nand_40_out, nand_33_out);
  nand nand_49 (nand_49_out, IR_o[0], nand_41_out);
  nand nand_50 (nand_50_out, nand_42_out, nand_43_out);
  nand nand_51 (nand_51_out, nand_45_out, nand_45_out);
  nand nand_52 (nand_52_out, nand_46_out, nand_46_out);
  nand nand_53 (nand_53_out, nand_47_out, nand_47_out);
  nand nand_54 (nand_54_out, nand_48_out, nand_48_out);
  nand nand_55 (nand_55_out, nand_49_out, nand_49_out);
  nand nand_56 (nand_56_out, nand_50_out, nand_50_out);
  nand nand_57 (nand_57_out, nand_51_out, IR_o[2]);
  nand nand_58 (nand_58_out, nand_57_out, nand_57_out);
  nand nand_59 (nand_59_out, IR_o[3], IR_o[3]);
  ControlledBuffer24 controlledbuffer24_3 (.I({24{1'b0}}), .S(nand_44_out), .O(controlledbuffer24_3_o));
  nand nand_60 (nand_60_out, nand_52_out, nand_59_out);
  nand nand_61 (nand_61_out, IR_o[3], IR_o[3]);
  nand nand_62 (nand_62_out, IR_o_3[22], IR_o_3[22]);
  nand nand_63 (nand_63_out, nand_60_out, nand_60_out);
  nand nand_64 (nand_64_out, nand_61_out, nand_62_out);
  nand nand_65 (nand_65_out, nandallbitsorcheck10_1_o, nandallbitsorcheck10_1_o);
  nand nand_66 (nand_66_out, nandalu3_1_c, nandalu3_1_c);
  nand nand_67 (nand_67_out, nand_56_out, nand_64_out);
  nand nand_68 (nand_68_out, IR_o[3], IR_o_3[22]);
  nand nand_69 (nand_69_out, nand_67_out, nand_67_out);
  nand nand_70 (nand_70_out, nand_68_out, nand_68_out);
  nand nand_71 (nand_71_out, IR_o[2], IR_o[2]);
  nand nand_72 (nand_72_out, IR_o[3], IR_o[3]);
  NandMUX nandmux_1 (.A(IR_o[3]), .S(nand_70_out), .B(1'b0), .O(nandmux_1_o[3]));
  nand nand_73 (nand_73_out, nand_71_out, nand_72_out);
  nand nand_74 (nand_74_out, nand_71_out, IR_o[3]);
  nand nand_75 (nand_75_out, IR_o[0], IR_o[0]);
  nand nand_76 (nand_76_out, nand_73_out, nand_73_out);
  nand nand_77 (nand_77_out, IR_o_3[22], IR_o_3[22]);
  nand nand_78 (nand_78_out, nand_74_out, nand_74_out);
  NandMUX nandmux_2 (.A(nand_65_out), .S(IR_o[3]), .B(nand_66_out), .O(nandmux_2_o));
  NandMUX nandmux_3 (.A(nandallbitsorcheck10_1_o), .S(IR_o[3]), .B(nandalu3_1_c), .O(nandmux_3_o));
  NandMUX nandmux_4 (.A(IR_o_3[22]), .S(nand_70_out), .B(1'b0), .O(nandmux_1_o[4]));
  nand nand_79 (nand_79_out, nand_75_out, IR_o[1]);
  nand nand_80 (nand_80_out, nand_79_out, nand_79_out);
  nand nand_81 (nand_81_out, nand_78_out, IR_o_3[22]);
  NandMUX nandmux_5 (.A(nandmux_2_o), .S(IR_o_3[22]), .B(nandmux_3_o), .O(nandmux_5_o));
  nand nand_82 (nand_82_out, nand_76_out, IR_o_3[22]);
  nand nand_83 (nand_91_out[21], nand_82_out, nand_82_out);
  nand nand_84 (nand_84_out, nand_76_out, nand_77_out);
  nand nand_85 (nand_91_out[23], nand_84_out, nand_84_out);
  nand nand_86 (nand_86_out, nand_81_out, nand_81_out);
  nand nand_87 (nand_87_out, IR_o[2], nand_72_out);
  nand nand_88 (nand_88_out, nand_86_out, nand_86_out);
  nand nand_89 (nand_89_out, nand_93_out, nand_93_out);
  nand nand_90 (nand_90_out, IR_o[2], nandmux_5_o);
  nand nand_91 (nand_91_out[3], nand_87_out, nand_87_out);
  nand nand_92 (nand_91_out[17], nand_88_out, nand_89_out);
  nand nand_93 (nand_93_out, nand_90_out, nand_90_out);
  ControlledBuffer24 controlledbuffer24_4 (
    .I({{19{1'b0}}, nandmux_1_o, 3'b100}), .S(nand_69_out), .O(controlledbuffer24_3_o));
  nand nand_94 (nand_94_out, nand_80_out, IR_o[2]);
  nand nand_95 (nand_95_out, nand_94_out, nand_94_out);
  nand nand_96 (nand_96_out[19], IR_o[3], IR_o_3[22]);
  ControlledBuffer24 controlledbuffer24_5 (
    .I({{2{nand_91_out[23]}}, {2{nand_91_out[21]}}, 2'b00, nand_91_out[17], nanddemux2way_2_o1[16:15], 4'b0000, nanddemux2way_2_o1[10:9], {5{1'b0}}, nand_91_out[3], 3'b000}),
    .S(nand_80_out), .O(controlledbuffer24_3_o));
  ControlledBuffer24 controlledbuffer24_6 (
    .I({4'b0000, nand_96_out[19], 4'b0000, {2{nanddemux2way_2_o1[14]}}, {2{nanddemux2way_2_o1[12]}}, 2'b00, {2{nanddemux2way_2_o1[8]}}, {2{nanddemux2way_2_o1[6]}}, 3'b000, IR_o_3[22], IR_o[3]}),
    .S(nand_55_out), .O(controlledbuffer24_3_o));
  nand nand_97 (nand_97_out, IR_o[3], IR_o[3]);
  nand nand_98 (nand_98_out, IR_o[3], IR_o[3]);
  nand nand_99 (nand_99_out, IR_o_3[22], IR_o_3[22]);
  nand nand_100 (nand_100_out, nand_97_out, IR_o_3[22]);
  nand nand_101 (nand_101_out, nand_98_out, nand_99_out);
  nand nand_102 (nand_102_out[5], nand_100_out, nand_100_out);
  nand nand_103 (nand_102_out[6], nand_101_out, nand_101_out);
  NandDEMUX5 nanddemux5_1 (.S(IR_o_3[22]), .I(IR_o_2), .A(nanddemux5_1_a), .B(nanddemux5_1_b));
  nand nand_104 (nand_104_out, IR_o_3[22], IR_o_3[22]);
  nand nand_105 (nand_105_out, IR_o[3], IR_o_3[22]);
  nand nand_106 (nand_106_out, IR_o[3], nand_104_out);
  nand nand_107 (nand_102_out[11], nand_105_out, nand_105_out);
  nand nand_108 (nand_102_out[12], nand_106_out, nand_106_out);
  ControlledBuffer10 controlledbuffer10_8 (
    .I({nanddemux5_1_b, nanddemux5_1_a}), .S(nand_54_out), .O(controlledbuffer10_1_o));
  ControlledBuffer24 controlledbuffer24_7 (
    .I({{11{1'b0}}, nand_102_out[12:11], 4'b0000, nand_102_out[6:5], {5{1'b0}}}), .S(nand_54_out),
    .O(controlledbuffer24_3_o));
  nand nand_109 (nand_109_out, IR_o[3], IR_o[3]);
  nand nand_110 (nand_110_out, IR_o[3], IR_o[3]);
  nand nand_111 (nand_111_out, IR_o_3[22], IR_o_3[22]);
  nand nand_112 (nand_112_out, nand_109_out, IR_o_3[22]);
  nand nand_113 (nand_113_out, nand_110_out, nand_111_out);
  nand nand_114 (nand_114_out[7], nand_112_out, nand_112_out);
  nand nand_115 (nand_114_out[8], nand_113_out, nand_113_out);
  NandDEMUX5 nanddemux5_2 (.S(IR_o_3[22]), .I(IR_o_2), .A(nanddemux5_2_a), .B(nanddemux5_2_b));
  nand nand_116 (nand_116_out, IR_o_3[22], IR_o_3[22]);
  nand nand_117 (nand_117_out, IR_o[3], IR_o_3[22]);
  nand nand_118 (nand_118_out, IR_o[3], nand_116_out);
  nand nand_119 (nand_114_out[13], nand_117_out, nand_117_out);
  nand nand_120 (nand_114_out[14], nand_118_out, nand_118_out);
  ControlledBuffer10 controlledbuffer10_9 (
    .I({nanddemux5_2_b, nanddemux5_2_a}), .S(nand_53_out), .O(controlledbuffer10_1_o));
  ControlledBuffer24 controlledbuffer24_8 (
    .I({{9{1'b0}}, nand_114_out[14:13], 4'b0000, nand_114_out[8:7], {7{1'b0}}}), .S(nand_53_out),
    .O(controlledbuffer24_3_o));
  NandDEMUX5 nanddemux5_3 (.S(IR_o_3[22]), .I(IR_o_2), .A(nanddemux5_3_a), .B(nanddemux5_3_b));
  nand nand_121 (IR_o_3[23], IR_o_3[22], IR_o_3[22]);
  ControlledBuffer10 controlledbuffer10_10 (
    .I({nanddemux5_3_b, nanddemux5_3_a}), .S(nand_63_out), .O(controlledbuffer10_1_o));
  ControlledBuffer24 controlledbuffer24_9 (.I({IR_o_3, {22{1'b0}}}), .S(nand_63_out), .O(controlledbuffer24_3_o));
  ControlledBuffer24 controlledbuffer24_10 (
    .I({{7{1'b0}}, nanddemux2way_2_o1[16:14], nanddemux2way_2_o1[14], {2{nanddemux2way_2_o1[12]}}, nanddemux2way_2_o1[10:8], nanddemux2way_2_o1[8], {2{nanddemux2way_2_o1[6]}}, {5{1'b0}}}),
    .S(nand_58_out), .O(controlledbuffer24_3_o));

  // Notes on the sheet:
  //   HALT
  //   NOOP
  //   STA/STAF/LOAD
  //   LAU/LAL/LBU/LBL
  //   LCU/LCL/LDU/LDL
  //   LMU/LML
  //   COPY
  //   ALU
  //   FROM
  //   TO
endmodule

module NandSyncCounter10 (
  input  [9:0] I,
  input  L,
  input  SB,
  input  E,
  output [9:0] O
);

  wire nand_1_out, nand_2_out, nand_3_out, nand_4_out, nand_5_out, nand_6_out, nand_7_out, nand_8_out,
       nand_9_out, nand_10_out, nand_11_out, nand_12_out, nand_13_out, nand_14_out, nand_15_out, nand_16_out,
       nand_17_out, nand_18_out, nand_19_out, nand_20_out, nand_21_out, nand_22_out, nand_23_out,
       nand_24_out, nand_25_out, nand_26_out, nand_27_out, nandmsjkff2_1_oc, nandmux2_1_o1, nandmux2_1_o2,
       nandmux2_2_o1, nandmux2_2_o2, nandmux2_3_o1, nandmux2_3_o2, nandmux2_4_o1, nandmux2_4_o2,
       nandmux2_5_o1, nandmux2_5_o2, nandmux2_6_o1, nandmux2_6_o2, nandmux2_7_o1, nandmux2_7_o2,
       nandmux2_8_o1, nandmux2_8_o2, nandmux2_9_o1, nandmux2_9_o2, nandmux2_10_o1, nandmux2_10_o2;

  nand nand_1 (nand_1_out, I[0], I[0]);
  NandMUX2 nandmux2_1 (.B1(I[0]), .B2(nand_1_out), .S(L), .A1(1'b1), .A2(1'b1), .O1(nandmux2_1_o1), .O2(nandmux2_1_o2));
  NandMSJKFF2 nandmsjkff2_1 (.J(nandmux2_1_o1), .K(nandmux2_1_o2), .CLK(E), .SB(SB), .O(O[0]), .OC(nandmsjkff2_1_oc));
  nand nand_2 (nand_2_out, nandmsjkff2_1_oc, nandmsjkff2_1_oc);
  nand nand_3 (nand_3_out, I[1], I[1]);
  NandMUX2 nandmux2_2 (
    .B1(I[1]), .B2(nand_3_out), .S(L), .A1(nand_2_out), .A2(nand_2_out), .O1(nandmux2_2_o1),
    .O2(nandmux2_2_o2));
  NandMSJKFF2 nandmsjkff2_2 (.J(nandmux2_2_o1), .K(nandmux2_2_o2), .CLK(E), .SB(SB), .O(O[1]));  // open: OC
  nand nand_4 (nand_4_out, O[0], O[1]);
  nand nand_5 (nand_5_out, nand_4_out, nand_4_out);
  nand nand_6 (nand_6_out, I[2], I[2]);
  NandMUX2 nandmux2_3 (
    .B1(I[2]), .B2(nand_6_out), .S(L), .A1(nand_5_out), .A2(nand_5_out), .O1(nandmux2_3_o1),
    .O2(nandmux2_3_o2));
  NandMSJKFF2 nandmsjkff2_3 (.J(nandmux2_3_o1), .K(nandmux2_3_o2), .CLK(E), .SB(SB), .O(O[2]));  // open: OC
  nand nand_7 (nand_7_out, nand_5_out, O[2]);
  nand nand_8 (nand_8_out, nand_7_out, nand_7_out);
  nand nand_9 (nand_9_out, I[3], I[3]);
  NandMUX2 nandmux2_4 (
    .B1(I[3]), .B2(nand_9_out), .S(L), .A1(nand_8_out), .A2(nand_8_out), .O1(nandmux2_4_o1),
    .O2(nandmux2_4_o2));
  NandMSJKFF2 nandmsjkff2_4 (.J(nandmux2_4_o1), .K(nandmux2_4_o2), .CLK(E), .SB(SB), .O(O[3]));  // open: OC
  nand nand_10 (nand_10_out, nand_8_out, O[3]);
  nand nand_11 (nand_11_out, I[4], I[4]);
  nand nand_12 (nand_12_out, nand_10_out, nand_10_out);
  NandMUX2 nandmux2_5 (
    .B1(I[4]), .B2(nand_11_out), .S(L), .A1(nand_12_out), .A2(nand_12_out), .O1(nandmux2_5_o1),
    .O2(nandmux2_5_o2));
  NandMSJKFF2 nandmsjkff2_5 (.J(nandmux2_5_o1), .K(nandmux2_5_o2), .CLK(E), .SB(SB), .O(O[4]));  // open: OC
  nand nand_13 (nand_13_out, nand_12_out, O[4]);
  nand nand_14 (nand_14_out, nand_13_out, nand_13_out);
  nand nand_15 (nand_15_out, I[5], I[5]);
  NandMUX2 nandmux2_6 (
    .B1(I[5]), .B2(nand_15_out), .S(L), .A1(nand_14_out), .A2(nand_14_out), .O1(nandmux2_6_o1),
    .O2(nandmux2_6_o2));
  NandMSJKFF2 nandmsjkff2_6 (.J(nandmux2_6_o1), .K(nandmux2_6_o2), .CLK(E), .SB(SB), .O(O[5]));  // open: OC
  nand nand_16 (nand_16_out, nand_14_out, O[5]);
  nand nand_17 (nand_17_out, nand_16_out, nand_16_out);
  nand nand_18 (nand_18_out, I[6], I[6]);
  NandMUX2 nandmux2_7 (
    .B1(I[6]), .B2(nand_18_out), .S(L), .A1(nand_17_out), .A2(nand_17_out), .O1(nandmux2_7_o1),
    .O2(nandmux2_7_o2));
  NandMSJKFF2 nandmsjkff2_7 (.J(nandmux2_7_o1), .K(nandmux2_7_o2), .CLK(E), .SB(SB), .O(O[6]));  // open: OC
  nand nand_19 (nand_19_out, nand_17_out, O[6]);
  nand nand_20 (nand_20_out, nand_19_out, nand_19_out);
  nand nand_21 (nand_21_out, I[7], I[7]);
  NandMUX2 nandmux2_8 (
    .B1(I[7]), .B2(nand_21_out), .S(L), .A1(nand_20_out), .A2(nand_20_out), .O1(nandmux2_8_o1),
    .O2(nandmux2_8_o2));
  NandMSJKFF2 nandmsjkff2_8 (.J(nandmux2_8_o1), .K(nandmux2_8_o2), .CLK(E), .SB(SB), .O(O[7]));  // open: OC
  nand nand_22 (nand_22_out, nand_20_out, O[7]);
  nand nand_23 (nand_23_out, nand_22_out, nand_22_out);
  nand nand_24 (nand_24_out, I[8], I[8]);
  NandMUX2 nandmux2_9 (
    .B1(I[8]), .B2(nand_24_out), .S(L), .A1(nand_23_out), .A2(nand_23_out), .O1(nandmux2_9_o1),
    .O2(nandmux2_9_o2));
  NandMSJKFF2 nandmsjkff2_9 (.J(nandmux2_9_o1), .K(nandmux2_9_o2), .CLK(E), .SB(SB), .O(O[8]));  // open: OC
  nand nand_25 (nand_25_out, nand_23_out, O[8]);
  nand nand_26 (nand_26_out, nand_25_out, nand_25_out);
  nand nand_27 (nand_27_out, I[9], I[9]);
  NandMUX2 nandmux2_10 (
    .B1(I[9]), .B2(nand_27_out), .S(L), .A1(nand_26_out), .A2(nand_26_out), .O1(nandmux2_10_o1),
    .O2(nandmux2_10_o2));
  NandMSJKFF2 nandmsjkff2_10 (.J(nandmux2_10_o1), .K(nandmux2_10_o2), .CLK(E), .SB(SB), .O(O[9]));  // open: OC
endmodule

module NandXOR (
  input  in_1,
  input  in_2,
  output out_3
);

  wire nand_1_out, nand_2_out, nand_3_out, nand_4_out;

  nand nand_1 (nand_1_out, in_2, in_2);
  nand nand_2 (nand_2_out, in_1, in_1);
  nand nand_3 (nand_3_out, in_1, nand_1_out);
  nand nand_4 (nand_4_out, in_2, nand_2_out);
  nand nand_5 (out_3, nand_3_out, nand_4_out);
endmodule

module NandALU3 (
  input  [9:0] A,
  input  [9:0] B,
  input  AZ,
  input  BZ,
  input  AC,
  input  BC,
  input  N,
  input  X,
  input  OC,
  output [9:0] O,
  output C,
  output S
);

  wire [8:0] nandfulladder10_1_s;
  wire [9:0] nand_1_out, nandinverter10_1_o, nandinverter10_2_o, nandinverter10_3_o, nandmux10_1_o,
       nandmux10_2_o, nandmux10_3_o, nandmux10_4_o, nandmux10_5_o, nandmux10_6_o, nandxor_1_out_3;

  NandMUX10 nandmux10_1 (.S(AZ), .A(A), .B({10{1'b0}}), .O(nandmux10_1_o));
  NandMUX10 nandmux10_2 (.S(BZ), .A(B), .B({10{1'b0}}), .O(nandmux10_2_o));
  NandInverter10 nandinverter10_1 (.I(nandmux10_1_o), .O(nandinverter10_1_o));
  NandInverter10 nandinverter10_2 (.I(nandmux10_2_o), .O(nandinverter10_2_o));
  NandMUX10 nandmux10_3 (.S(AC), .A(nandmux10_1_o), .B(nandinverter10_1_o), .O(nandmux10_3_o));
  NandMUX10 nandmux10_4 (.S(BC), .A(nandmux10_2_o), .B(nandinverter10_2_o), .O(nandmux10_4_o));
  NandFullAdder10 nandfulladder10_1 (.B(nandmux10_4_o), .A(nandmux10_3_o), .C(C), .S({S, nandfulladder10_1_s}));
  NandXOR nandxor_1 (.in_1(nandmux10_3_o[0]), .in_2(nandmux10_4_o[0]), .out_3(nandxor_1_out_3[0]));
  NandXOR nandxor_2 (.in_1(nandmux10_3_o[1]), .in_2(nandmux10_4_o[1]), .out_3(nandxor_1_out_3[1]));
  NandXOR nandxor_3 (.in_1(nandmux10_3_o[2]), .in_2(nandmux10_4_o[2]), .out_3(nandxor_1_out_3[2]));
  NandXOR nandxor_4 (.in_1(nandmux10_3_o[3]), .in_2(nandmux10_4_o[3]), .out_3(nandxor_1_out_3[3]));
  NandXOR nandxor_5 (.in_1(nandmux10_3_o[4]), .in_2(nandmux10_4_o[4]), .out_3(nandxor_1_out_3[4]));
  NandXOR nandxor_6 (.in_1(nandmux10_3_o[5]), .in_2(nandmux10_4_o[5]), .out_3(nandxor_1_out_3[5]));
  NandXOR nandxor_7 (.in_1(nandmux10_3_o[6]), .in_2(nandmux10_4_o[6]), .out_3(nandxor_1_out_3[6]));
  NandXOR nandxor_8 (.in_1(nandmux10_3_o[7]), .in_2(nandmux10_4_o[7]), .out_3(nandxor_1_out_3[7]));
  NandXOR nandxor_9 (.in_1(nandmux10_3_o[8]), .in_2(nandmux10_4_o[8]), .out_3(nandxor_1_out_3[8]));
  NandXOR nandxor_10 (.in_1(nandmux10_3_o[9]), .in_2(nandmux10_4_o[9]), .out_3(nandxor_1_out_3[9]));
  nand nand_1 (nand_1_out[0], nandmux10_3_o[0], nandmux10_4_o[0]);
  nand nand_2 (nand_1_out[1], nandmux10_3_o[1], nandmux10_4_o[1]);
  nand nand_3 (nand_1_out[2], nandmux10_3_o[2], nandmux10_4_o[2]);
  nand nand_4 (nand_1_out[3], nandmux10_3_o[3], nandmux10_4_o[3]);
  nand nand_5 (nand_1_out[4], nandmux10_3_o[4], nandmux10_4_o[4]);
  nand nand_6 (nand_1_out[5], nandmux10_3_o[5], nandmux10_4_o[5]);
  nand nand_7 (nand_1_out[6], nandmux10_3_o[6], nandmux10_4_o[6]);
  nand nand_8 (nand_1_out[7], nandmux10_3_o[7], nandmux10_4_o[7]);
  nand nand_9 (nand_1_out[8], nandmux10_3_o[8], nandmux10_4_o[8]);
  nand nand_10 (nand_1_out[9], nandmux10_3_o[9], nandmux10_4_o[9]);
  NandMUX10 nandmux10_5 (.S(N), .A({S, nandfulladder10_1_s}), .B(nand_1_out), .O(nandmux10_5_o));
  NandMUX10 nandmux10_6 (.S(X), .A(nandmux10_5_o), .B(nandxor_1_out_3), .O(nandmux10_6_o));
  NandInverter10 nandinverter10_3 (.I(nandmux10_6_o), .O(nandinverter10_3_o));
  NandMUX10 nandmux10_7 (.S(OC), .A(nandmux10_6_o), .B(nandinverter10_3_o), .O(O));
endmodule

module AndAndAllBits9 (
  input  [8:0] I,
  output O
);

  wire nand_1_out, nand_2_out, nand_3_out, nand_4_out, nand_5_out, nand_6_out, nand_7_out, nand_8_out,
       nand_9_out, nand_10_out, nand_11_out, nand_12_out, nand_13_out, nand_14_out, nand_15_out;

  nand nand_1 (nand_1_out, I[0], I[1]);
  nand nand_2 (nand_2_out, nand_1_out, nand_1_out);
  nand nand_3 (nand_3_out, nand_2_out, I[2]);
  nand nand_4 (nand_4_out, nand_3_out, nand_3_out);
  nand nand_5 (nand_5_out, nand_4_out, I[3]);
  nand nand_6 (nand_6_out, nand_5_out, nand_5_out);
  nand nand_7 (nand_7_out, nand_6_out, I[4]);
  nand nand_8 (nand_8_out, nand_7_out, nand_7_out);
  nand nand_9 (nand_9_out, nand_8_out, I[5]);
  nand nand_10 (nand_10_out, nand_9_out, nand_9_out);
  nand nand_11 (nand_11_out, nand_10_out, I[6]);
  nand nand_12 (nand_12_out, nand_11_out, nand_11_out);
  nand nand_13 (nand_13_out, nand_12_out, I[7]);
  nand nand_14 (nand_14_out, nand_13_out, nand_13_out);
  nand nand_15 (nand_15_out, nand_14_out, I[8]);
  nand nand_16 (O, nand_15_out, nand_15_out);
endmodule

module ControlledBuffer24 (
  input  [23:0] I,
  input  S,
  output [23:0] O
);

  assign O[0] = S ? I[0] : 1'bz;  // Controlled_Buffer controlled_buffer_1
  assign O[1] = S ? I[1] : 1'bz;  // Controlled_Buffer controlled_buffer_2
  assign O[2] = S ? I[2] : 1'bz;  // Controlled_Buffer controlled_buffer_3
  assign O[3] = S ? I[3] : 1'bz;  // Controlled_Buffer controlled_buffer_4
  assign O[4] = S ? I[4] : 1'bz;  // Controlled_Buffer controlled_buffer_5
  assign O[5] = S ? I[5] : 1'bz;  // Controlled_Buffer controlled_buffer_6
  assign O[6] = S ? I[6] : 1'bz;  // Controlled_Buffer controlled_buffer_7
  assign O[7] = S ? I[7] : 1'bz;  // Controlled_Buffer controlled_buffer_8
  assign O[8] = S ? I[8] : 1'bz;  // Controlled_Buffer controlled_buffer_9
  assign O[9] = S ? I[9] : 1'bz;  // Controlled_Buffer controlled_buffer_10
  assign O[10] = S ? I[10] : 1'bz;  // Controlled_Buffer controlled_buffer_11
  assign O[11] = S ? I[11] : 1'bz;  // Controlled_Buffer controlled_buffer_12
  assign O[12] = S ? I[12] : 1'bz;  // Controlled_Buffer controlled_buffer_13
  assign O[13] = S ? I[13] : 1'bz;  // Controlled_Buffer controlled_buffer_14
  assign O[14] = S ? I[14] : 1'bz;  // Controlled_Buffer controlled_buffer_15
  assign O[15] = S ? I[15] : 1'bz;  // Controlled_Buffer controlled_buffer_16
  assign O[16] = S ? I[16] : 1'bz;  // Controlled_Buffer controlled_buffer_17
  assign O[17] = S ? I[17] : 1'bz;  // Controlled_Buffer controlled_buffer_18
  assign O[18] = S ? I[18] : 1'bz;  // Controlled_Buffer controlled_buffer_19
  assign O[19] = S ? I[19] : 1'bz;  // Controlled_Buffer controlled_buffer_20
  assign O[20] = S ? I[20] : 1'bz;  // Controlled_Buffer controlled_buffer_21
  assign O[21] = S ? I[21] : 1'bz;  // Controlled_Buffer controlled_buffer_22
  assign O[22] = S ? I[22] : 1'bz;  // Controlled_Buffer controlled_buffer_23
  assign O[23] = S ? I[23] : 1'bz;  // Controlled_Buffer controlled_buffer_24
endmodule

module NandDEMUX5 (
  input  [4:0] I,
  input  S,
  output [4:0] A,
  output [4:0] B
);

  NandDEMUX nanddemux_1 (.I(I[0]), .S(S), .A(A[0]), .B(B[0]));
  NandDEMUX nanddemux_2 (.I(I[1]), .S(S), .A(B[1]), .B(A[1]));
  NandDEMUX nanddemux_3 (.I(I[2]), .S(S), .A(B[2]), .B(A[2]));
  NandDEMUX nanddemux_4 (.I(I[3]), .S(S), .A(B[3]), .B(A[3]));
  NandDEMUX nanddemux_5 (.I(I[4]), .S(S), .A(B[4]), .B(A[4]));
endmodule

module NandAllBitsORCheck5 (
  input  [4:0] I,
  output O
);

  wire nand_1_out, nand_2_out, nand_3_out, nand_4_out, nand_5_out, nand_6_out, nand_7_out, nand_8_out,
       nand_9_out, nand_10_out, nand_11_out;

  nand nand_1 (nand_1_out, I[0], I[0]);
  nand nand_2 (nand_2_out, I[1], I[1]);
  nand nand_3 (nand_3_out, nand_1_out, nand_2_out);
  nand nand_4 (nand_4_out, nand_3_out, nand_3_out);
  nand nand_5 (nand_5_out, I[2], I[2]);
  nand nand_6 (nand_6_out, nand_4_out, nand_5_out);
  nand nand_7 (nand_7_out, nand_6_out, nand_6_out);
  nand nand_8 (nand_8_out, I[3], I[3]);
  nand nand_9 (nand_9_out, nand_7_out, nand_8_out);
  nand nand_10 (nand_10_out, nand_9_out, nand_9_out);
  nand nand_11 (nand_11_out, I[4], I[4]);
  nand nand_12 (O, nand_10_out, nand_11_out);
endmodule

module NandAndAllBits5 (
  input  [4:0] I,
  output O
);

  wire nand_1_out, nand_2_out, nand_3_out, nand_4_out, nand_5_out, nand_6_out, nand_7_out;

  nand nand_1 (nand_1_out, I[0], I[1]);
  nand nand_2 (nand_2_out, nand_1_out, nand_1_out);
  nand nand_3 (nand_3_out, nand_2_out, I[2]);
  nand nand_4 (nand_4_out, nand_3_out, nand_3_out);
  nand nand_5 (nand_5_out, nand_4_out, I[3]);
  nand nand_6 (nand_6_out, nand_5_out, nand_5_out);
  nand nand_7 (nand_7_out, nand_6_out, I[4]);
  nand nand_8 (O, nand_7_out, nand_7_out);
endmodule

module MachineCycleCounter (
  input  [1:0] I,
  input  L,
  input  SB,
  input  E,
  output [1:0] O
);

  wire nand_1_out, nand_2_out, nand_3_out, nandmsjkff2_1_oc, nandmux2_1_o1, nandmux2_1_o2, nandmux2_2_o1,
       nandmux2_2_o2;

  nand nand_1 (nand_1_out, I[0], I[0]);
  NandMUX2 nandmux2_1 (.B1(I[0]), .B2(nand_1_out), .S(L), .A1(1'b1), .A2(1'b1), .O1(nandmux2_1_o1), .O2(nandmux2_1_o2));
  NandMSJKFF2 nandmsjkff2_1 (.J(nandmux2_1_o1), .K(nandmux2_1_o2), .CLK(E), .SB(SB), .O(O[0]), .OC(nandmsjkff2_1_oc));
  nand nand_2 (nand_2_out, nandmsjkff2_1_oc, nandmsjkff2_1_oc);
  nand nand_3 (nand_3_out, I[1], I[1]);
  NandMUX2 nandmux2_2 (
    .B1(I[1]), .B2(nand_3_out), .S(L), .A1(nand_2_out), .A2(nand_2_out), .O1(nandmux2_2_o1),
    .O2(nandmux2_2_o2));
  NandMSJKFF2 nandmsjkff2_2 (.J(nandmux2_2_o1), .K(nandmux2_2_o2), .CLK(E), .SB(SB), .O(O[1]));  // open: OC
endmodule
