// Logisim project sutra_1.circ as structural Verilog
module main (
  input  in_1,
  input  in_2,
  output [9:0] IR_CONTENTS,
  output [37:0] FLAGS_CONTENT
);

  wire ACCU_out, ALUFSET_out, bcd_to_7_segment_decoder_8_p1, CARRY_out, clock_1_out, controlled_buffer_1_out,
       controlled_buffer_3_out, COPY_out, HALT_o, ILOCK_oc, ILOCKSET_out, JUMP_out, LOADIL_out, LOADISR_out,
       LOADIU_out, MACHINE_CYCLE_o, MACHINE_CYCLE_oc, nand_1_out, nand_2_out, nand_3_out, nand_4_out,
       nand_5_out, nand_6_out, nand_7_out, nand_8_out, nand_9_out, nand_10_out, nand_11_out, nand_12_out,
       nand_13_out, nand_15_out, nand_16_out, nand_17_out, nand_18_out, nand_19_out, nand_20_out,
       nand_21_out, nand_22_out, nand_23_out, nand_24_out, nand_25_out, nand_26_out, nand_27_out,
       nand_28_out, nand_29_out, nand_30_out, nand_31_out, nand_32_out, nand_33_out, nand_34_out,
       nand_35_out, nand_36_out, nand_38_out, nand_39_out, nand_40_out, nand_41_out, nand_42_out,
       nand_43_out, nand_44_out, nand_45_out, nand_46_out, nand_47_out, nand_48_out, nand_49_out,
       nand_50_out, nand_51_out, nand_52_out, nand_53_out, nand_54_out, nand_56_out, nand_57_out,
       nand_58_out, nand_59_out, nand_60_out, nand_61_out, nand_62_out, nand_63_out, nand_64_out,
       nand_65_out, nand_66_out, nand_67_out, nand_68_out, nand_69_out, nand_70_out, nand_71_out,
       nand_72_out, nand_73_out, nand_74_out, nand_75_out, nand_76_out, nand_77_out, nand_78_out,
       nand_79_out, nand_80_out, nand_81_out, nand_82_out, nand_83_out, nand_84_out, nand_85_out,
       nand_86_out, nand_87_out, nand_88_out, nand_89_out, nand_90_out, nand_92_out, nand_93_out,
       nand_96_out, nand_97_out, nand_98_out, nand_99_out, nand_100_out, nand_101_out, nand_102_out,
       nand_103_out, nand_104_out, nand_105_out, NEGATIVE_out, NOOP_out, or3_1_o, or4_1_o, or4_2_o, or4_3_o,
       or5_1_o, or5_2_o, or10_1_o, or10_2_o, undriven, undriven_2, ZERO_out;
  wire [1:1] nand_14_out;
  wire [2:0] ALU_RESULT_FLAGS_o, button_3_out, INSTRUCTION_DATA_OUT_o_2, nand_55_out;
  wire [3:0] and2_4_1_o, buffer4_1_o, IMR_o, ISR_o, LOAD_out, mux2to1_4_1_o, nand_95_out, not4_1_o,
       or2_4_1_o, RIGHT_out;
  wire [4:1] ALUEVAL_out;
  wire [6:0] aluflagsregister_1_o, INSTRUCTION_DATA_OUT_o;
  wire [9:0] alu_1_o, ALU_RESULT_o, ALUFSET_FLAGS_o, B_o, binary_to_bcd_converter_1_p1, buffer10_4_o,
       buffer10_10_o, C_o, COPY_RS_o, D_o, LOADIL_U_R_o, SP_o;
  wire [9:2] buffer10_1_o, COPY_R_OR_ALUSTOREF_R_OR_ALUSTORER_R_OR_LOAD_o;
  wire [9:3] ALUEVAL_RS_OR_STORE_OUT_ALUFSET_REGISTER_o, undriven_10;
  wire [19:0] buffer20_1_o, MAR_o, synccounternew_1_o;
  wire [26:6] undriven_5, undriven_8, undriven_11;
  wire [31:0] screencontroller_1_c, screencontroller_1_c_1, screencontroller_1_c_2, screencontroller_1_c_3,
       screencontroller_1_c_4, screencontroller_1_c_5, screencontroller_1_c_6, screencontroller_1_c_7,
       screencontroller_1_c_8, screencontroller_1_c_9, screencontroller_1_c_10, screencontroller_1_c_11,
       screencontroller_1_c_12, screencontroller_1_c_13, screencontroller_1_c_14, screencontroller_1_c_15,
       screencontroller_1_c_16, screencontroller_1_c_17, screencontroller_1_c_18, screencontroller_1_c_19,
       screencontroller_1_c_20, screencontroller_1_c_21, screencontroller_1_c_22, screencontroller_1_c_23,
       screencontroller_1_c_24, screencontroller_1_c_25, screencontroller_1_c_26, screencontroller_1_c_27,
       screencontroller_1_c_28, screencontroller_1_c_29, screencontroller_1_c_30, screencontroller_1_c_31,
       screencontroller_1_c_32, screencontroller_1_c_33, screencontroller_1_c_34, screencontroller_1_c_35,
       screencontroller_1_c_36, screencontroller_1_c_37, screencontroller_1_c_38, screencontroller_1_c_39,
       screencontroller_1_c_40, screencontroller_1_c_41, screencontroller_1_c_42, screencontroller_1_c_43,
       screencontroller_1_c_44, screencontroller_1_c_45, screencontroller_1_c_46, screencontroller_1_c_47,
       screencontroller_1_c_48, screencontroller_1_c_49, screencontroller_1_c_50, screencontroller_1_c_51,
       screencontroller_1_c_52, screencontroller_1_c_53, screencontroller_1_c_54, screencontroller_1_c_55,
       screencontroller_1_c_56, screencontroller_1_c_57, screencontroller_1_c_58, screencontroller_1_c_59,
       screencontroller_1_c_60, screencontroller_1_c_61, screencontroller_1_c_62, screencontroller_1_c_63;
  wire [34:6] undriven_4;
  wire [34:7] undriven_3, undriven_6, undriven_7, undriven_9;
  wire [37:0] buffer38_1_o, controldestination_1_o;

  Or4 or4_1 (.I(LOAD_out), .O(or4_1_o));
  Buffer10 LOADIL_U_R (.I(IR_CONTENTS), .E(nand_14_out[1]), .O(LOADIL_U_R_o));
  Buffer10 COPY_R_OR_ALUSTOREF_R_OR_ALUSTORER_R_OR_LOAD (
    .I(IR_CONTENTS), .E(or4_1_o), .O({COPY_R_OR_ALUSTOREF_R_OR_ALUSTORER_R_OR_LOAD_o, LOADIL_U_R_o[6:5]}));
  Or5 or5_1 (.I({LOAD_out[3:1], nand_14_out[1], LOAD_out[0]}), .O(or5_1_o));
  assign controlled_buffer_1_out = nand_14_out[1] ? LOADIL_U_R_o[7] : 1'bz;  // Controlled_Buffer controlled_buffer_1
  assign COPY_R_OR_ALUSTOREF_R_OR_ALUSTORER_R_OR_LOAD_o[2] = nand_14_out[1] ? 1'b0 : 1'bz;  // Controlled_Buffer controlled_buffer_2
  assign controlled_buffer_3_out = nand_14_out[1] ? LOADIL_U_R_o[8] : 1'bz;  // Controlled_Buffer controlled_buffer_3
  assign controlled_buffer_1_out = LOAD_out[1] ? 1'b1 : 1'bz;  // Controlled_Buffer controlled_buffer_4
  assign controlled_buffer_3_out = LOAD_out[1] ? 1'b1 : 1'bz;  // Controlled_Buffer controlled_buffer_5
  assign controlled_buffer_1_out = LOAD_out[2] ? 1'b1 : 1'bz;  // Controlled_Buffer controlled_buffer_6
  assign controlled_buffer_3_out = LOAD_out[2] ? 1'b1 : 1'bz;  // Controlled_Buffer controlled_buffer_7
  assign controlled_buffer_1_out = LOAD_out[3] ? 1'b1 : 1'bz;  // Controlled_Buffer controlled_buffer_8
  assign controlled_buffer_3_out = LOAD_out[3] ? 1'b1 : 1'bz;  // Controlled_Buffer controlled_buffer_9
  assign controlled_buffer_1_out = LOAD_out[0] ? 1'b1 : 1'bz;  // Controlled_Buffer controlled_buffer_10
  assign controlled_buffer_3_out = LOAD_out[0] ? 1'b1 : 1'bz;  // Controlled_Buffer controlled_buffer_11
  Clock clock_1 (.out(clock_1_out));
  Or3 or3_1 (.I(ALUEVAL_out[3:1]), .O(or3_1_o));
  ControlDestination controldestination_1 (
    .OUTPUT_ENABLE(or5_1_o), .UPPER(controlled_buffer_1_out), .LOWER(controlled_buffer_3_out),
    .S({COPY_R_OR_ALUSTOREF_R_OR_ALUSTORER_R_OR_LOAD_o[2], LOADIL_U_R_o[6:5]}), .O(controldestination_1_o));
  nand nand_1 (nand_1_out, undriven, undriven);
  nand nand_2 (nand_2_out, nand_1_out, undriven_2);
  nand nand_3 (nand_3_out, clock_1_out, clock_1_out);
  nand nand_4 (nand_4_out, nand_2_out, nand_2_out);
  nand nand_5 (nand_5_out, nand_19_out, nand_3_out);
  nand nand_6 (nand_6_out, nand_19_out, clock_1_out);
  Buffer10 COPY_RS (.I(IR_CONTENTS), .E(LOAD_out[1]), .O(COPY_RS_o));
  Buffer10 ALUEVAL_RS_OR_STORE_OUT_ALUFSET_REGISTER (
    .I(IR_CONTENTS), .E(or3_1_o), .O({ALUEVAL_RS_OR_STORE_OUT_ALUFSET_REGISTER_o, COPY_RS_o[5:3]}));
  nand nand_7 (nand_7_out, nand_5_out, nand_5_out);
  nand nand_8 (nand_8_out, nand_6_out, nand_6_out);
  Or5 or5_2 (.I({ALUEVAL_out, LOAD_out[1]}), .O(or5_2_o));
  Buffer10 buffer10_1 (.I(IR_CONTENTS), .E(ALUEVAL_out[3]), .O({buffer10_1_o, COPY_RS_o[4:3]}));
  Buffer38 buffer38_1 (.I({38{1'b0}}), .E(nand_4_out), .O(buffer38_1_o));
  assign COPY_RS_o[5] = ALUEVAL_out[3] ? 1'b0 : 1'bz;  // Controlled_Buffer controlled_buffer_12
  Buffer10 INSTRUCTION_DATA_OUT (
    .I(ALUFSET_FLAGS_o), .E(MACHINE_CYCLE_o), .O({INSTRUCTION_DATA_OUT_o_2, INSTRUCTION_DATA_OUT_o}));
  ControlSource controlsource_1 (.OUTPUT_ENABLE(or5_2_o), .S(COPY_RS_o[5:3]), .O(controldestination_1_o));
  Buffer10 ALUFSET_FLAGS (.I({3'b000, IR_CONTENTS[6:0]}), .E(ALUFSET_out), .O(ALUFSET_FLAGS_o));
  JKFlipFlop MACHINE_CYCLE (
    .SB(in_2), .J(1'b1), .CLK(nand_7_out), .K(1'b1), .O(MACHINE_CYCLE_o), .OC(MACHINE_CYCLE_oc));
  NormalRegister IR (
    .CLK(nand_8_out), .LL(nand_36_out), .LH(nand_36_out), .SB(in_2),
    .I({INSTRUCTION_DATA_OUT_o_2, INSTRUCTION_DATA_OUT_o}), .O(IR_CONTENTS));
  Buffer38 FETCH (.I(38'h50000000), .E(nand_36_out), .O(FLAGS_CONTENT));
  nand nand_9 (nand_9_out, IR_CONTENTS[9], IR_CONTENTS[9]);
  nand nand_10 (nand_10_out, IR_CONTENTS[8], IR_CONTENTS[8]);
  nand nand_11 (nand_11_out, IR_CONTENTS[7], IR_CONTENTS[7]);
  Buffer10 IR_OUT (.I(IR_CONTENTS), .E(FLAGS_CONTENT[36]), .O({INSTRUCTION_DATA_OUT_o_2, INSTRUCTION_DATA_OUT_o}));
  nand nand_12 (nand_12_out, nand_9_out, IR_CONTENTS[8]);
  Clock clock_2 ();  // open: out
  NormalRegister B (
    .CLK(nand_8_out), .LL(FLAGS_CONTENT[11]), .LH(FLAGS_CONTENT[12]), .SB(in_2),
    .I({INSTRUCTION_DATA_OUT_o_2, INSTRUCTION_DATA_OUT_o}), .O(B_o));
  nand nand_13 (nand_13_out, nand_12_out, nand_12_out);
  nand nand_14 (nand_14_out[1], nand_15_out, nand_27_out);
  _7_Segment_Display u_7_segment_display_1 ();  // open: g, f, a, b, e, d, c, dp
  // BCD_to_7_Segment_decoder bcd_to_7_segment_decoder_1: pin names not known
  // Binary_to_BCD_converter #(.binvalue(10)) binary_to_bcd_converter_1: pin names not known; wires that end beside it: binary_to_bcd_converter_1_p1
  _7_Segment_Display u_7_segment_display_2 ();  // open: g, f, a, b, e, d, c, dp
  // BCD_to_7_Segment_decoder bcd_to_7_segment_decoder_2: pin names not known
  // Binary_to_BCD_converter #(.binvalue(10)) binary_to_bcd_converter_2: pin names not known; wires that end beside it: B_o
  nand nand_15 (nand_15_out, nand_11_out, nand_13_out);
  nand LOADIL (LOADIL_out, nand_15_out, nand_15_out);
  _7_Segment_Display u_7_segment_display_3 ();  // open: g, f, a, b, e, d, c, dp
  // BCD_to_7_Segment_decoder bcd_to_7_segment_decoder_3: pin names not known
  _7_Segment_Display u_7_segment_display_4 ();  // open: g, f, a, b, e, d, c, dp
  _7_Segment_Display u_7_segment_display_5 ();  // open: g, f, a, b, e, d, c, dp
  // BCD_to_7_Segment_decoder bcd_to_7_segment_decoder_4: pin names not known
  // BCD_to_7_Segment_decoder bcd_to_7_segment_decoder_5: pin names not known
  _7_Segment_Display u_7_segment_display_6 ();  // open: g, f, a, b, e, d, c, dp
  // BCD_to_7_Segment_decoder bcd_to_7_segment_decoder_6: pin names not known
  Buffer10 buffer10_2 (.I(B_o), .E(FLAGS_CONTENT[13]), .O({INSTRUCTION_DATA_OUT_o_2, INSTRUCTION_DATA_OUT_o}));
  _7_Segment_Display u_7_segment_display_7 ();  // open: g, f, a, b, e, d, c, dp
  // BCD_to_7_Segment_decoder bcd_to_7_segment_decoder_7: pin names not known
  Buffer38 INSTRUCTION_FLAGS_OUT (.I(controldestination_1_o), .E(MACHINE_CYCLE_o), .O(FLAGS_CONTENT));
  Buffer38 ALUFSET_O (.I(38'h20), .E(ALUFSET_out), .O(controldestination_1_o));
  _7_Segment_Display u_7_segment_display_8 ();  // open: g, f, a, b, e, d, c, dp
  // BCD_to_7_Segment_decoder bcd_to_7_segment_decoder_8: pin names not known; wires that end beside it: bcd_to_7_segment_decoder_8_p1
  UniversalShiftRegister A (
    .CLK(nand_8_out), .LL(FLAGS_CONTENT[7]), .LH(FLAGS_CONTENT[8]), .SB(in_2), .S1(FLAGS_CONTENT[9]),
    .S2(FLAGS_CONTENT[10]), .I({INSTRUCTION_DATA_OUT_o_2, INSTRUCTION_DATA_OUT_o}),
    .O(binary_to_bcd_converter_1_p1));
  Buffer38 buffer38_2 (
    .I({3'b000, undriven_3[34:31], {5{1'b0}}, undriven_3[25:24], 2'b00, undriven_3[21], 2'b00, undriven_3[18:17], 1'b0, undriven_3[15:14], 1'b0, undriven_3[12:7], {7{1'b0}}}),
    .E(nand_14_out[1]), .O(controldestination_1_o));
  Buffer38 buffer38_3 (
    .I({3'b000, undriven_4[34:31], 4'b0000, undriven_4[26:21], 1'b0, undriven_4[19:6], {6{1'b0}}}),
    .E(LOAD_out[1]), .O(controldestination_1_o));
  Buffer10 LOADIL_DATA (.I({{5{1'b0}}, IR_CONTENTS[4:0]}), .E(LOADIL_out), .O(ALUFSET_FLAGS_o));
  Buffer10 LOADIU_DATA (.I({IR_CONTENTS[4:0], {5{1'b0}}}), .E(LOADIU_out), .O(ALUFSET_FLAGS_o));
  Clock clock_3 (.out(bcd_to_7_segment_decoder_8_p1));
  And10 HALT (.I(IR_CONTENTS), .O(HALT_o));
  nand nand_16 (nand_16_out, nand_89_out, nand_89_out);
  nand nand_17 (nand_17_out, MACHINE_CYCLE_oc, MACHINE_CYCLE_oc);
  nand nand_18 (nand_18_out, IR_CONTENTS[7], nand_13_out);
  Buffer10 buffer10_3 (
    .I(binary_to_bcd_converter_1_p1), .E(FLAGS_CONTENT[6]),
    .O({INSTRUCTION_DATA_OUT_o_2, INSTRUCTION_DATA_OUT_o}));
  NormalRegister C (
    .CLK(nand_8_out), .LL(FLAGS_CONTENT[14]), .LH(FLAGS_CONTENT[15]), .SB(in_2),
    .I({INSTRUCTION_DATA_OUT_o_2, INSTRUCTION_DATA_OUT_o}), .O(C_o));
  nand nand_19 (nand_19_out, HALT_o, HALT_o);
  nand ALUFSET (ALUFSET_out, nand_18_out, nand_18_out);
  nand nand_20 (nand_20_out, IR_CONTENTS[8], IR_CONTENTS[8]);
  nand nand_21 (nand_21_out, nand_16_out, nand_17_out);
  Clock clock_4 ();  // open: out
  nand nand_22 (nand_22_out, nand_9_out, nand_10_out);
  nand nand_23 (nand_23_out, nand_26_out, nand_11_out);
  nand nand_24 (nand_24_out, nand_20_out, IR_CONTENTS[9]);
  _7_Segment_Display u_7_segment_display_9 ();  // open: g, f, a, b, e, d, c, dp
  // BCD_to_7_Segment_decoder bcd_to_7_segment_decoder_9: pin names not known
  // Binary_to_BCD_converter #(.binvalue(10)) binary_to_bcd_converter_3: pin names not known; wires that end beside it: C_o
  nand nand_25 (nand_25_out, nand_21_out, nand_21_out);
  nand nand_26 (nand_26_out, nand_22_out, nand_22_out);
  nand COPY (COPY_out, nand_23_out, nand_23_out);
  nand nand_27 (nand_27_out, nand_26_out, IR_CONTENTS[7]);
  nand LOADIU (LOADIU_out, nand_27_out, nand_27_out);
  nand nand_28 (nand_28_out, IR_CONTENTS[7], IR_CONTENTS[7]);
  nand nand_29 (nand_29_out, nand_24_out, nand_24_out);
  Buffer10 buffer10_4 (.I({INSTRUCTION_DATA_OUT_o_2, INSTRUCTION_DATA_OUT_o}), .E(FLAGS_CONTENT[4]), .O(buffer10_4_o));
  _7_Segment_Display u_7_segment_display_10 ();  // open: g, f, a, b, e, d, c, dp
  _7_Segment_Display u_7_segment_display_11 ();  // open: g, f, a, b, e, d, c, dp
  // BCD_to_7_Segment_decoder bcd_to_7_segment_decoder_10: pin names not known
  // BCD_to_7_Segment_decoder bcd_to_7_segment_decoder_11: pin names not known
  nand nand_30 (nand_30_out, nand_105_out, nand_105_out);
  nand nand_31 (nand_31_out, nand_19_out, MACHINE_CYCLE_oc);
  Buffer38 buffer38_4 (.I({38{1'b0}}), .E(HALT_o), .O(FLAGS_CONTENT));
  nand nand_32 (nand_32_out, COPY_out, IR_CONTENTS[6]);
  nand nand_33 (nand_33_out, nand_28_out, nand_29_out);
  nand nand_34 (nand_34_out, nand_29_out, IR_CONTENTS[7]);
  ALUFlagsRegister aluflagsregister_1 (
    .CLK(nand_8_out), .LL(FLAGS_CONTENT[5]), .LH(FLAGS_CONTENT[5]), .SB(in_2), .I(INSTRUCTION_DATA_OUT_o),
    .O(aluflagsregister_1_o));
  Buffer10 buffer10_5 (.I(C_o), .E(FLAGS_CONTENT[16]), .O({INSTRUCTION_DATA_OUT_o_2, INSTRUCTION_DATA_OUT_o}));
  _7_Segment_Display u_7_segment_display_12 ();  // open: g, f, a, b, e, d, c, dp
  // BCD_to_7_Segment_decoder bcd_to_7_segment_decoder_12: pin names not known
  nand nand_35 (nand_35_out, nand_25_out, nand_30_out);
  nand nand_36 (nand_36_out, nand_31_out, nand_31_out);
  nand nand_37 (LOAD_out[1], nand_32_out, nand_32_out);
  nand nand_38 (nand_38_out, IR_CONTENTS[6], IR_CONTENTS[6]);
  nand nand_39 (nand_39_out, nand_33_out, nand_33_out);
  nand nand_40 (nand_40_out, nand_34_out, nand_34_out);
  nand nand_41 (nand_41_out, nand_38_out, nand_39_out);
  nand nand_42 (nand_42_out, nand_39_out, IR_CONTENTS[6]);
  nand nand_43 (nand_43_out, nand_38_out, nand_40_out);
  nand nand_44 (nand_44_out, IR_CONTENTS[5], IR_CONTENTS[5]);
  nand nand_45 (nand_45_out, nand_41_out, nand_41_out);
  nand nand_46 (nand_46_out, nand_42_out, nand_42_out);
  nand nand_47 (nand_47_out, nand_43_out, nand_43_out);
  ALU alu_1 (
    .A(binary_to_bcd_converter_1_p1), .B(buffer10_4_o), .AZ(aluflagsregister_1_o[0]),
    .AC(aluflagsregister_1_o[1]), .BZ(aluflagsregister_1_o[2]), .BC(aluflagsregister_1_o[3]),
    .Cin(aluflagsregister_1_o[4]), .N(aluflagsregister_1_o[5]), .OC(aluflagsregister_1_o[6]),
    .Cout(nand_55_out[2]), .O(alu_1_o));
  nand nand_48 (nand_48_out, nand_44_out, nand_45_out);
  nand nand_49 (nand_49_out, nand_48_out, nand_48_out);
  nand nand_50 (nand_50_out, nand_45_out, IR_CONTENTS[5]);
  nand nand_51 (nand_51_out, nand_44_out, nand_46_out);
  nand nand_52 (nand_52_out, nand_46_out, IR_CONTENTS[5]);
  nand nand_53 (nand_53_out, nand_44_out, nand_47_out);
  nand nand_54 (nand_54_out, nand_47_out, IR_CONTENTS[5]);
  nand nand_55 (nand_55_out[0], or10_2_o, or10_2_o);
  NormalRegister D (
    .CLK(nand_8_out), .LL(FLAGS_CONTENT[17]), .LH(FLAGS_CONTENT[18]), .SB(in_2),
    .I({INSTRUCTION_DATA_OUT_o_2, INSTRUCTION_DATA_OUT_o}), .O(D_o));
  nand nand_56 (nand_56_out, FLAGS_CONTENT[27], FLAGS_CONTENT[27]);
  nand nand_57 (nand_57_out, IR_CONTENTS[4], IR_CONTENTS[4]);
  nand nand_58 (nand_58_out, nand_50_out, nand_50_out);
  nand nand_59 (nand_59_out, nand_51_out, nand_51_out);
  nand nand_60 (nand_60_out, nand_52_out, nand_52_out);
  nand nand_61 (nand_61_out, nand_53_out, nand_53_out);
  nand ILOCKSET (ILOCKSET_out, nand_54_out, nand_54_out);
  nand nand_62 (nand_62_out, nand_56_out, nand_73_out);
  SyncCounterNew synccounternew_1 (
    .SB(in_2), .CLK(nand_8_out), .ENABLE(nand_21_out), .L(nand_62_out), .I(buffer20_1_o),
    .O(synccounternew_1_o));
  NormalRegister20 MAR (
    .CLK(nand_8_out), .LLL(FLAGS_CONTENT[31]), .LLH(FLAGS_CONTENT[32]), .LHL(FLAGS_CONTENT[33]),
    .LHH(FLAGS_CONTENT[34]), .SB(in_2), .IL({INSTRUCTION_DATA_OUT_o_2, INSTRUCTION_DATA_OUT_o}),
    .IH({INSTRUCTION_DATA_OUT_o_2, INSTRUCTION_DATA_OUT_o}), .O(MAR_o));
  Or10 or10_1 (.I(IR_CONTENTS), .O(or10_1_o));
  nand nand_63 (nand_63_out, nand_57_out, nand_49_out);
  nand ALUEVAL (ALUEVAL_out[1], nand_63_out, nand_63_out);
  nand nand_64 (nand_64_out, nand_49_out, IR_CONTENTS[4]);
  nand ALUSTOREF (LOAD_out[2], nand_64_out, nand_64_out);
  nand nand_65 (nand_65_out, nand_57_out, nand_58_out);
  nand ALUTSTORER (LOAD_out[3], nand_65_out, nand_65_out);
  nand nand_66 (nand_66_out, nand_58_out, IR_CONTENTS[4]);
  nand nand_67 (nand_67_out, nand_57_out, nand_59_out);
  nand nand_68 (nand_68_out, nand_59_out, IR_CONTENTS[4]);
  nand nand_69 (nand_69_out, nand_60_out, nand_57_out);
  nand nand_70 (nand_70_out, IR_CONTENTS[4], nand_60_out);
  nand nand_71 (nand_71_out, nand_57_out, nand_61_out);
  nand nand_72 (nand_72_out, nand_61_out, IR_CONTENTS[4]);
  nand nand_73 (nand_73_out, nand_105_out, nand_105_out);
  nand nand_74 (nand_74_out, nand_105_out, nand_105_out);
  nand NOOP (NOOP_out, or10_1_o, or10_1_o);
  nand STORE (ALUEVAL_out[2], nand_66_out, nand_66_out);
  nand LOAD (LOAD_out[0], nand_67_out, nand_67_out);
  nand ACCU (ACCU_out, nand_68_out, nand_68_out);
  nand JUMP (JUMP_out, nand_69_out, nand_69_out);
  nand OUTT (ALUEVAL_out[3], nand_70_out, nand_70_out);
  nand LOADISR (LOADISR_out, nand_71_out, nand_71_out);
  nand ALUFSET_REGISTER (ALUEVAL_out[4], nand_72_out, nand_72_out);
  Or10 or10_2 (.I(alu_1_o), .O(or10_2_o));
  nand nand_75 (nand_75_out, FLAGS_CONTENT[28], nand_73_out);
  nand nand_76 (nand_76_out, nand_74_out, FLAGS_CONTENT[35]);
  NormalRegister ALU_RESULT (
    .CLK(nand_8_out), .LL(FLAGS_CONTENT[2]), .LH(FLAGS_CONTENT[2]), .SB(in_2), .I(alu_1_o), .O(ALU_RESULT_o));
  NormalRegister3 ALU_RESULT_FLAGS (
    .CLK(nand_8_out), .LOAD(FLAGS_CONTENT[3]), .SB(in_2), .I({nand_55_out[2], alu_1_o[9], nand_55_out[0]}),
    .O(ALU_RESULT_FLAGS_o));
  Buffer10 buffer10_6 (.I(D_o), .E(FLAGS_CONTENT[19]), .O({INSTRUCTION_DATA_OUT_o_2, INSTRUCTION_DATA_OUT_o}));
  _7_Segment_Display u_7_segment_display_13 ();  // open: g, f, a, b, e, d, c, dp
  // BCD_to_7_Segment_decoder bcd_to_7_segment_decoder_13: pin names not known
  Buffer20 buffer20_1 (.I(synccounternew_1_o), .E(nand_77_out), .O(buffer20_1_o));
  nand nand_77 (nand_77_out, nand_75_out, nand_75_out);
  Buffer20 buffer20_2 (.I(20'hff800), .E(nand_105_out), .O(buffer20_1_o));
  Buffer20 buffer20_3 (.I(MAR_o), .E(nand_78_out), .O(buffer20_1_o));
  nand nand_78 (nand_78_out, nand_76_out, nand_76_out);
  _7_Segment_Display u_7_segment_display_14 ();  // open: g, f, a, b, e, d, c, dp
  // BCD_to_7_Segment_decoder bcd_to_7_segment_decoder_14: pin names not known
  // Binary_to_BCD_converter #(.binvalue(10)) binary_to_bcd_converter_4: pin names not known; wires that end beside it: D_o
  RAM #(.addrWidth(20), .dataWidth(10), .databus("bidir"), .enables("line"), .trigger("high"), .\type ("nonvolatile")) ram_1 (
    .addr(buffer20_1_o), .we(FLAGS_CONTENT[29]), .oe(FLAGS_CONTENT[30]), .clk(nand_8_out),
    .data({INSTRUCTION_DATA_OUT_o_2, INSTRUCTION_DATA_OUT_o}));
  _7_Segment_Display u_7_segment_display_15 ();  // open: g, f, a, b, e, d, c, dp
  // BCD_to_7_Segment_decoder bcd_to_7_segment_decoder_15: pin names not known
  NormalRegister SP (
    .CLK(nand_8_out), .LL(FLAGS_CONTENT[24]), .LH(FLAGS_CONTENT[25]), .SB(in_2),
    .I({INSTRUCTION_DATA_OUT_o_2, INSTRUCTION_DATA_OUT_o}), .O(SP_o));
  Buffer38 buffer38_5 (.I({38{1'b0}}), .E(NOOP_out), .O(controldestination_1_o));
  Buffer38 buffer38_6 (
    .I({{11{1'b0}}, undriven_5[26], 2'b00, undriven_5[23:22], 2'b00, undriven_5[19], 2'b00, undriven_5[16], 2'b00, undriven_5[13], {6{1'b0}}, undriven_5[6], 6'b011100}),
    .E(ALUEVAL_out[1]), .O(controldestination_1_o));
  Buffer38 buffer38_7 (
    .I({3'b000, undriven_6[34:31], {5{1'b0}}, undriven_6[25:24], 2'b00, undriven_6[21], 2'b00, undriven_6[18:17], 1'b0, undriven_6[15:14], 1'b0, undriven_6[12:7], 7'b0000010}),
    .E(LOAD_out[2]), .O(controldestination_1_o));
  Buffer38 buffer38_8 (
    .I({3'b000, undriven_7[34:31], {5{1'b0}}, undriven_7[25:24], 2'b00, undriven_7[21], 2'b00, undriven_7[18:17], 1'b0, undriven_7[15:14], 1'b0, undriven_7[12:7], 7'b0000001}),
    .E(LOAD_out[3]), .O(controldestination_1_o));
  Buffer38 buffer38_9 (
    .I({11'h104, undriven_8[26], 2'b00, undriven_8[23:22], 2'b00, undriven_8[19], 2'b00, undriven_8[16], 2'b00, undriven_8[13], {6{1'b0}}, undriven_8[6], {6{1'b0}}}),
    .E(ALUEVAL_out[2]), .O(controldestination_1_o));
  Buffer38 buffer38_10 (
    .I({3'b001, undriven_9[34:31], 5'b10000, undriven_9[25:24], 2'b00, undriven_9[21], 2'b00, undriven_9[18:17], 1'b0, undriven_9[15:14], 1'b0, undriven_9[12:7], {7{1'b0}}}),
    .E(LOAD_out[0]), .O(controldestination_1_o));
  Buffer38 buffer38_11 (
    .I({{27{1'b0}}, IR_CONTENTS[0], IR_CONTENTS[1], {9{1'b0}}}), .E(ACCU_out), .O(controldestination_1_o));
  Buffer38 buffer38_12 (.I(38'h808000000), .E(nand_89_out), .O(controldestination_1_o));
  nand nand_79 (nand_79_out, IR_CONTENTS[0], IR_CONTENTS[0]);
  nand nand_80 (nand_80_out, IR_CONTENTS[1], IR_CONTENTS[1]);
  Buffer38 buffer38_13 (.I(38'h3000000000), .E(ILOCKSET_out), .O(controldestination_1_o));
  Buffer38 buffer38_14 (.I(38'h1000100000), .E(LOADISR_out), .O(controldestination_1_o));
  Buffer38 buffer38_15 (.I(38'h20), .E(ALUEVAL_out[4]), .O(controldestination_1_o));
  _7_Segment_Display u_7_segment_display_16 ();  // open: g, f, a, b, e, d, c, dp
  // BCD_to_7_Segment_decoder bcd_to_7_segment_decoder_16: pin names not known
  Buffer10 buffer10_7 (.I(ALU_RESULT_o), .E(FLAGS_CONTENT[0]), .O({INSTRUCTION_DATA_OUT_o_2, INSTRUCTION_DATA_OUT_o}));
  Buffer10 buffer10_8 (
    .I({undriven_10, ALU_RESULT_FLAGS_o}), .E(FLAGS_CONTENT[1]),
    .O({INSTRUCTION_DATA_OUT_o_2, INSTRUCTION_DATA_OUT_o}));
  nand nand_81 (nand_81_out, JUMP_out, nand_82_out);
  nand nand_82 (nand_82_out, or4_2_o, or4_2_o);
  nand nand_83 (nand_83_out, JUMP_out, or4_2_o);
  nand nand_84 (nand_84_out, nand_79_out, nand_80_out);
  nand UNCONDITIONAL (nand_95_out[3], nand_84_out, nand_84_out);
  nand nand_85 (nand_85_out, IR_CONTENTS[0], nand_80_out);
  nand nand_86 (nand_86_out, nand_79_out, IR_CONTENTS[1]);
  nand nand_87 (nand_87_out, IR_CONTENTS[0], IR_CONTENTS[1]);
  Buffer10 buffer10_9 (.I(SP_o), .E(FLAGS_CONTENT[26]), .O({INSTRUCTION_DATA_OUT_o_2, INSTRUCTION_DATA_OUT_o}));
  Buffer38 buffer38_16 (.I({38{1'b0}}), .E(nand_88_out), .O(controldestination_1_o));
  nand nand_88 (nand_88_out, nand_81_out, nand_81_out);
  nand nand_89 (nand_89_out, nand_83_out, nand_83_out);
  nand ZERO (ZERO_out, nand_85_out, nand_85_out);
  nand NEGATIVE (NEGATIVE_out, nand_86_out, nand_86_out);
  nand CARRY (CARRY_out, nand_87_out, nand_87_out);
  Buffer38 buffer38_17 (
    .I({{11{1'b0}}, undriven_11[26], 2'b00, undriven_11[23:22], 2'b00, undriven_11[19], 2'b00, undriven_11[16], 2'b00, undriven_11[13], {6{1'b0}}, undriven_11[6], {6{1'b0}}}),
    .E(ALUEVAL_out[3]), .O(controldestination_1_o));
  nand nand_90 (nand_90_out, ALU_RESULT_FLAGS_o[0], ZERO_out);
  nand nand_91 (nand_95_out[2], nand_90_out, nand_90_out);
  nand nand_92 (nand_92_out, ALU_RESULT_FLAGS_o[1], NEGATIVE_out);
  nand nand_93 (nand_93_out, ALU_RESULT_FLAGS_o[2], CARRY_out);
  nand nand_94 (nand_95_out[1], nand_92_out, nand_92_out);
  nand nand_95 (nand_95_out[0], nand_93_out, nand_93_out);
  Or4 or4_2 (.I(nand_95_out), .O(or4_2_o));
  nand nand_96 (nand_96_out, ALUEVAL_out[3], MACHINE_CYCLE_o);
  nand nand_97 (nand_97_out, nand_96_out, nand_96_out);
  Button button_1 (.out(button_3_out[2]));
  Button button_2 (.out(button_3_out[1]));
  Button button_3 (.out(button_3_out[0]));
  nand nand_98 (nand_98_out, FLAGS_CONTENT[20], FLAGS_CONTENT[20]);
  nand nand_99 (nand_99_out, MACHINE_CYCLE_oc, MACHINE_CYCLE_oc);
  Buffer10 buffer10_10 (.I({INSTRUCTION_DATA_OUT_o_2, INSTRUCTION_DATA_OUT_o}), .E(nand_97_out), .O(buffer10_10_o));
  nand nand_100 (nand_100_out, nand_98_out, nand_99_out);
  Mux2To1_4 mux2to1_4_1 (.A(or2_4_1_o), .B(INSTRUCTION_DATA_OUT_o[3:0]), .S(FLAGS_CONTENT[20]), .O(mux2to1_4_1_o));
  Or2_4 or2_4_1 (.A(RIGHT_out), .B(ISR_o), .O(or2_4_1_o));
  NormalRegister1 ILOCK (
    .CLK(nand_8_out), .LOAD(FLAGS_CONTENT[37]), .D(INSTRUCTION_DATA_OUT_o[0]), .SB(in_2), .OC(ILOCK_oc));  // open: O
  DotMatrix #(.matrixcols(64), .matrixrows(32)) dotmatrix_1 (
    .col0(screencontroller_1_c), .col1(screencontroller_1_c_1), .col2(screencontroller_1_c_2),
    .col3(screencontroller_1_c_3), .col4(screencontroller_1_c_4), .col5(screencontroller_1_c_5),
    .col6(screencontroller_1_c_6), .col7(screencontroller_1_c_7), .col8(screencontroller_1_c_8),
    .col9(screencontroller_1_c_9), .col10(screencontroller_1_c_10), .col11(screencontroller_1_c_11),
    .col12(screencontroller_1_c_12), .col13(screencontroller_1_c_13), .col14(screencontroller_1_c_14),
    .col15(screencontroller_1_c_15), .col16(screencontroller_1_c_16), .col17(screencontroller_1_c_17),
    .col18(screencontroller_1_c_18), .col19(screencontroller_1_c_19), .col20(screencontroller_1_c_20),
    .col21(screencontroller_1_c_21), .col22(screencontroller_1_c_22), .col23(screencontroller_1_c_23),
    .col24(screencontroller_1_c_24), .col25(screencontroller_1_c_25), .col26(screencontroller_1_c_26),
    .col27(screencontroller_1_c_27), .col28(screencontroller_1_c_28), .col29(screencontroller_1_c_29),
    .col30(screencontroller_1_c_30), .col31(screencontroller_1_c_31), .col32(screencontroller_1_c_32),
    .col33(screencontroller_1_c_33), .col34(screencontroller_1_c_34), .col35(screencontroller_1_c_35),
    .col36(screencontroller_1_c_36), .col37(screencontroller_1_c_37), .col38(screencontroller_1_c_38),
    .col39(screencontroller_1_c_39), .col40(screencontroller_1_c_40), .col41(screencontroller_1_c_41),
    .col42(screencontroller_1_c_42), .col43(screencontroller_1_c_43), .col44(screencontroller_1_c_44),
    .col45(screencontroller_1_c_45), .col46(screencontroller_1_c_46), .col47(screencontroller_1_c_47),
    .col48(screencontroller_1_c_48), .col49(screencontroller_1_c_49), .col50(screencontroller_1_c_50),
    .col51(screencontroller_1_c_51), .col52(screencontroller_1_c_52), .col53(screencontroller_1_c_53),
    .col54(screencontroller_1_c_54), .col55(screencontroller_1_c_55), .col56(screencontroller_1_c_56),
    .col57(screencontroller_1_c_57), .col58(screencontroller_1_c_58), .col59(screencontroller_1_c_59),
    .col60(screencontroller_1_c_60), .col61(screencontroller_1_c_61), .col62(screencontroller_1_c_62),
    .col63(screencontroller_1_c_63));
  ScreenController screencontroller_1 (
    .DATA(buffer10_10_o), .CLK(nand_8_out), .C(screencontroller_1_c), .C_1(screencontroller_1_c_1),
    .C_2(screencontroller_1_c_2), .C_3(screencontroller_1_c_3), .C_4(screencontroller_1_c_4),
    .C_5(screencontroller_1_c_5), .C_6(screencontroller_1_c_6), .C_7(screencontroller_1_c_7),
    .C_8(screencontroller_1_c_8), .C_9(screencontroller_1_c_9), .C_10(screencontroller_1_c_10),
    .C_11(screencontroller_1_c_11), .C_12(screencontroller_1_c_12), .C_13(screencontroller_1_c_13),
    .C_14(screencontroller_1_c_14), .C_15(screencontroller_1_c_15), .C_16(screencontroller_1_c_16),
    .C_17(screencontroller_1_c_17), .C_18(screencontroller_1_c_18), .C_19(screencontroller_1_c_19),
    .C_20(screencontroller_1_c_20), .C_21(screencontroller_1_c_21), .C_22(screencontroller_1_c_22),
    .C_23(screencontroller_1_c_23), .C_24(screencontroller_1_c_24), .C_25(screencontroller_1_c_25),
    .C_26(screencontroller_1_c_26), .C_27(screencontroller_1_c_27), .C_28(screencontroller_1_c_28),
    .C_29(screencontroller_1_c_29), .C_30(screencontroller_1_c_30), .C_31(screencontroller_1_c_31),
    .C_32(screencontroller_1_c_32), .C_33(screencontroller_1_c_33), .C_34(screencontroller_1_c_34),
    .C_35(screencontroller_1_c_35), .C_36(screencontroller_1_c_36), .C_37(screencontroller_1_c_37),
    .C_38(screencontroller_1_c_38), .C_39(screencontroller_1_c_39), .C_40(screencontroller_1_c_40),
    .C_41(screencontroller_1_c_41), .C_42(screencontroller_1_c_42), .C_43(screencontroller_1_c_43),
    .C_44(screencontroller_1_c_44), .C_45(screencontroller_1_c_45), .C_46(screencontroller_1_c_46),
    .C_47(screencontroller_1_c_47), .C_48(screencontroller_1_c_48), .C_49(screencontroller_1_c_49),
    .C_50(screencontroller_1_c_50), .C_51(screencontroller_1_c_51), .C_52(screencontroller_1_c_52),
    .C_53(screencontroller_1_c_53), .C_54(screencontroller_1_c_54), .C_55(screencontroller_1_c_55),
    .C_56(screencontroller_1_c_56), .C_57(screencontroller_1_c_57), .C_58(screencontroller_1_c_58),
    .C_59(screencontroller_1_c_59), .C_60(screencontroller_1_c_60), .C_61(screencontroller_1_c_61),
    .C_62(screencontroller_1_c_62), .C_63(screencontroller_1_c_63));
  NormalRegister4 ISR (.CLK(nand_8_out), .LOAD(nand_100_out), .SB(in_2), .I(mux2to1_4_1_o), .O(ISR_o));
  NormalRegister4 IMR (
    .CLK(nand_8_out), .LOAD(FLAGS_CONTENT[21]), .SB(in_2), .I(INSTRUCTION_DATA_OUT_o[3:0]), .O(IMR_o));
  Button UP (.out(RIGHT_out[3]));
  Button DOWN (.out(RIGHT_out[2]));
  Button LEFT (.out(RIGHT_out[1]));
  nand nand_101 (nand_101_out, FLAGS_CONTENT[23], FLAGS_CONTENT[23]);
  nand nand_102 (nand_102_out, FLAGS_CONTENT[22], FLAGS_CONTENT[22]);
  Button RIGHT (.out(RIGHT_out[0]));
  nand nand_103 (nand_103_out, nand_101_out, nand_102_out);
  Buffer4 buffer4_1 (.I(ISR_o), .E(FLAGS_CONTENT[22]), .O(buffer4_1_o));
  Not4 not4_1 (.I(IMR_o), .O(not4_1_o));
  Buffer4 buffer4_2 (.I(IMR_o), .E(FLAGS_CONTENT[23]), .O(buffer4_1_o));
  And2_4 and2_4_1 (.A(ISR_o), .B(not4_1_o), .O(and2_4_1_o));
  Buffer10 buffer10_11 (
    .I({{6{1'b0}}, buffer4_1_o}), .E(nand_103_out), .O({INSTRUCTION_DATA_OUT_o_2, INSTRUCTION_DATA_OUT_o}));
  Or4 or4_3 (.I(and2_4_1_o), .O(or4_3_o));
  nand nand_104 (nand_104_out, or4_3_o, ILOCK_oc);
  nand nand_105 (nand_105_out, nand_104_out, nand_104_out);

  // Notes on the sheet:
  //   A
  //   B
  //   C
  //   ISR ADDRESS
  //   D
  //   MEMORY
endmodule

module SRLatch (
  input  S,
  input  E,
  input  SB,
  input  R,
  output O,
  output OC
);

  wire nand_1_out, nand_2_out;

  nand nand_1 (nand_1_out, S, E);
  nand nand_2 (nand_2_out, E, R);
  nand nand_3 (O, nand_1_out, OC);
  nand nand_4 (OC, O, SB, nand_2_out);
endmodule

module DLatch (
  input  E,
  input  D,
  input  SB,
  output O,
  output OC
);

  wire nand_1_out, nand_2_out;

  nand nand_1 (nand_1_out, E, D);
  nand nand_2 (nand_2_out, nand_1_out, E);
  nand nand_3 (O, nand_1_out, OC);
  nand nand_4 (OC, O, SB, nand_2_out);
endmodule

module UniversalShiftRegister (
  input  CLK,
  input  LL,
  input  LH,
  input  SB,
  input  S1,
  input  S2,
  input  [9:0] I,
  output [9:0] O
);

  wire mux4to1_1_o, mux4to1_2_o, mux4to1_3_o, mux4to1_4_o, mux4to1_5_o, mux4to1_6_o, mux4to1_7_o,
       mux4to1_8_o, mux4to1_9_o, mux4to1_10_o, nand_1_out, nand_2_out, nand_3_out, nand_4_out, nand_5_out,
       nand_6_out, nand_7_out, nand_8_out, nand_10_out, nand_11_out, nand_12_out, nand_13_out, nand_14_out,
       nand_15_out;

  nand nand_1 (nand_1_out, S1, S1);
  nand nand_2 (nand_2_out, S2, S2);
  nand nand_3 (nand_3_out, S1, S2);
  nand nand_4 (nand_4_out, nand_1_out, nand_2_out);
  nand nand_5 (nand_5_out, LL, LL);
  nand nand_6 (nand_6_out, nand_3_out, nand_3_out);
  nand nand_7 (nand_7_out, nand_4_out, CLK);
  nand nand_8 (nand_8_out, nand_5_out, nand_6_out);
  // NAND_Gate nand_9 has open pins: in0=nand_7_out, in1=nand_7_out, out=open
  nand nand_10 (nand_10_out, CLK, nand_8_out);
  nand nand_11 (nand_11_out, nand_10_out, nand_10_out);
  nand nand_12 (nand_12_out, LH, LH);
  nand nand_13 (nand_13_out, nand_12_out, nand_6_out);
  nand nand_14 (nand_14_out, CLK, nand_13_out);
  Mux4To1 mux4to1_1 (.A(O[0]), .B(O[1]), .C(1'b0), .D(I[0]), .S1(S1), .S2(S2), .O(mux4to1_1_o));
  nand nand_15 (nand_15_out, nand_14_out, nand_14_out);
  DFlipFlop dflipflop_1 (.CLK(nand_11_out), .D(mux4to1_1_o), .SB(SB), .O(O[0]));  // open: OC
  Mux4To1 mux4to1_2 (.A(O[1]), .B(O[2]), .C(O[0]), .D(I[1]), .S1(S1), .S2(S2), .O(mux4to1_2_o));
  DFlipFlop dflipflop_2 (.CLK(nand_11_out), .D(mux4to1_2_o), .SB(SB), .O(O[1]));  // open: OC
  Mux4To1 mux4to1_3 (.A(O[2]), .B(O[3]), .C(O[1]), .D(I[2]), .S1(S1), .S2(S2), .O(mux4to1_3_o));
  DFlipFlop dflipflop_3 (.CLK(nand_11_out), .D(mux4to1_3_o), .SB(SB), .O(O[2]));  // open: OC
  Mux4To1 mux4to1_4 (.A(O[3]), .B(O[4]), .C(O[2]), .D(I[3]), .S1(S1), .S2(S2), .O(mux4to1_4_o));
  DFlipFlop dflipflop_4 (.CLK(nand_11_out), .D(mux4to1_4_o), .SB(SB), .O(O[3]));  // open: OC
  Mux4To1 mux4to1_5 (.A(O[4]), .B(O[5]), .C(O[3]), .D(I[4]), .S1(S1), .S2(S2), .O(mux4to1_5_o));
  DFlipFlop dflipflop_5 (.CLK(nand_11_out), .D(mux4to1_5_o), .SB(SB), .O(O[4]));  // open: OC
  Mux4To1 mux4to1_6 (.A(O[5]), .B(O[6]), .C(O[4]), .D(I[5]), .S1(S1), .S2(S2), .O(mux4to1_6_o));
  DFlipFlop dflipflop_6 (.CLK(nand_15_out), .D(mux4to1_6_o), .SB(SB), .O(O[5]));  // open: OC
  Mux4To1 mux4to1_7 (.A(O[6]), .B(O[7]), .C(O[5]), .D(I[6]), .S1(S1), .S2(S2), .O(mux4to1_7_o));
  DFlipFlop dflipflop_7 (.CLK(nand_15_out), .D(mux4to1_7_o), .SB(SB), .O(O[6]));  // open: OC
  Mux4To1 mux4to1_8 (.A(O[7]), .B(O[8]), .C(O[6]), .D(I[7]), .S1(S1), .S2(S2), .O(mux4to1_8_o));
  DFlipFlop dflipflop_8 (.CLK(nand_15_out), .D(mux4to1_8_o), .SB(SB), .O(O[7]));  // open: OC
  Mux4To1 mux4to1_9 (.A(O[8]), .B(O[9]), .C(O[7]), .D(I[8]), .S1(S1), .S2(S2), .O(mux4to1_9_o));
  DFlipFlop dflipflop_9 (.CLK(nand_15_out), .D(mux4to1_9_o), .SB(SB), .O(O[8]));  // open: OC
  Mux4To1 mux4to1_10 (.A(O[9]), .B(1'b0), .C(O[8]), .D(I[9]), .S1(S1), .S2(S2), .O(mux4to1_10_o));
  DFlipFlop dflipflop_10 (.CLK(nand_15_out), .D(mux4to1_10_o), .SB(SB), .O(O[9]));  // open: OC
endmodule

module Mux2To1 (
  input  A,
  input  B,
  input  S,
  output O
);

  wire nand_1_out, nand_2_out, nand_3_out;

  nand nand_1 (nand_1_out, S, S);
  nand nand_2 (nand_2_out, A, nand_1_out);
  nand nand_3 (nand_3_out, B, S);
  nand nand_4 (O, nand_2_out, nand_3_out);
endmodule

module Mux4To1 (
  input  A,
  input  B,
  input  C,
  input  D,
  input  S1,
  input  S2,
  output O
);

  wire mux2to1_1_o, mux2to1_2_o;

  Mux2To1 mux2to1_1 (.A(A), .B(C), .S(S1), .O(mux2to1_1_o));
  Mux2To1 mux2to1_2 (.A(B), .B(D), .S(S1), .O(mux2to1_2_o));
  Mux2To1 mux2to1_3 (.A(mux2to1_1_o), .B(mux2to1_2_o), .S(S2), .O(O));
endmodule

module DFlipFlop (
  input  CLK,
  input  D,
  input  SB,
  output O,
  output OC
);

  wire dlatch_1_o, nand_1_out;

  nand nand_1 (nand_1_out, CLK, CLK);
  DLatch dlatch_1 (.E(nand_1_out), .D(D), .SB(SB), .O(dlatch_1_o));  // open: OC
  DLatch dlatch_2 (.E(CLK), .D(dlatch_1_o), .SB(SB), .O(O), .OC(OC));
endmodule

module NormalRegister (
  input  CLK,
  input  LL,
  input  LH,
  input  SB,
  input  [9:0] I,
  output [9:0] O
);

  wire nand_1_out, nand_2_out, nand_3_out, nand_4_out;

  nand nand_1 (nand_1_out, CLK, LL);
  nand nand_2 (nand_2_out, nand_1_out, nand_1_out);
  nand nand_3 (nand_3_out, CLK, LH);
  nand nand_4 (nand_4_out, nand_3_out, nand_3_out);
  DFlipFlop dflipflop_1 (.CLK(nand_2_out), .D(I[0]), .SB(SB), .O(O[0]));  // open: OC
  DFlipFlop dflipflop_2 (.CLK(nand_2_out), .D(I[1]), .SB(SB), .O(O[1]));  // open: OC
  DFlipFlop dflipflop_3 (.CLK(nand_2_out), .D(I[2]), .SB(SB), .O(O[2]));  // open: OC
  DFlipFlop dflipflop_4 (.CLK(nand_2_out), .D(I[3]), .SB(SB), .O(O[3]));  // open: OC
  DFlipFlop dflipflop_5 (.CLK(nand_2_out), .D(I[4]), .SB(SB), .O(O[4]));  // open: OC
  DFlipFlop dflipflop_6 (.CLK(nand_4_out), .D(I[5]), .SB(SB), .O(O[5]));  // open: OC
  DFlipFlop dflipflop_7 (.CLK(nand_4_out), .D(I[6]), .SB(SB), .O(O[6]));  // open: OC
  DFlipFlop dflipflop_8 (.CLK(nand_4_out), .D(I[7]), .SB(SB), .O(O[7]));  // open: OC
  DFlipFlop dflipflop_9 (.CLK(nand_4_out), .D(I[8]), .SB(SB), .O(O[8]));  // open: OC
  DFlipFlop dflipflop_10 (.CLK(nand_4_out), .D(I[9]), .SB(SB), .O(O[9]));  // open: OC
endmodule

module SyncCounter (
  input  SB,
  input  CLK,
  input  ENABLE,
  input  L,
  input  [19:0] I,
  output [19:0] O
);

  wire jkflipflop_12_o, mux2to1_1_o, mux2to1_2_o, mux2to1_3_o, mux2to1_4_o, mux2to1_5_o, mux2to1_6_o,
       mux2to1_7_o, mux2to1_8_o, mux2to1_9_o, mux2to1_10_o, mux2to1_11_o, mux2to1_12_o, mux2to1_13_o,
       mux2to1_14_o, mux2to1_15_o, mux2to1_16_o, mux2to1_17_o, mux2to1_18_o, mux2to1_19_o, mux2to1_20_o,
       mux2to1_21_o, mux2to1_22_o, mux2to1_23_o, mux2to1_24_o, mux2to1_25_o, mux2to1_26_o, mux2to1_27_o,
       mux2to1_28_o, mux2to1_29_o, mux2to1_30_o, mux2to1_31_o, mux2to1_32_o, mux2to1_33_o, mux2to1_34_o,
       mux2to1_35_o, mux2to1_36_o, mux2to1_37_o, mux2to1_38_o, mux2to1_39_o, mux2to1_40_o, nand_1_out,
       nand_2_out, nand_3_out, nand_4_out, nand_5_out, nand_6_out, nand_7_out, nand_8_out, nand_9_out,
       nand_10_out, nand_11_out, nand_12_out, nand_13_out, nand_14_out, nand_15_out, nand_16_out,
       nand_17_out, nand_18_out, nand_19_out, nand_20_out, nand_21_out, nand_22_out, nand_23_out,
       nand_24_out, nand_25_out, nand_26_out, nand_27_out, nand_28_out, nand_29_out, nand_30_out,
       nand_31_out, nand_32_out, nand_33_out, nand_34_out, nand_35_out, nand_36_out, nand_37_out,
       nand_38_out, nand_39_out, nand_40_out, nand_41_out, nand_42_out, nand_43_out, nand_44_out,
       nand_45_out, nand_46_out, nand_47_out, nand_48_out, nand_49_out, nand_50_out, nand_51_out,
       nand_52_out, nand_53_out, nand_54_out, nand_55_out, nand_56_out, nand_57_out, nand_58_out,
       nand_59_out, nand_60_out;

  nand nand_1 (nand_1_out, CLK, ENABLE);
  nand nand_2 (nand_2_out, nand_1_out, nand_1_out);
  JKFlipFlop jkflipflop_1 (.SB(SB), .J(1'b1), .CLK(nand_2_out), .K(1'b1), .O(O[0]));  // open: OC
  Mux2To1 mux2to1_1 (.A(O[0]), .B(I[0]), .S(L), .O(mux2to1_1_o));
  nand nand_3 (nand_3_out, mux2to1_1_o, mux2to1_1_o);
  Mux2To1 mux2to1_2 (.A(mux2to1_1_o), .B(nand_3_out), .S(L), .O(mux2to1_2_o));
  JKFlipFlop jkflipflop_2 (.SB(SB), .J(mux2to1_1_o), .CLK(nand_2_out), .K(mux2to1_2_o), .O(O[1]));  // open: OC
  nand nand_4 (nand_4_out, O[0], O[1]);
  nand nand_5 (nand_5_out, nand_4_out, nand_4_out);
  Mux2To1 mux2to1_3 (.A(nand_5_out), .B(I[1]), .S(L), .O(mux2to1_3_o));
  nand nand_6 (nand_6_out, mux2to1_3_o, mux2to1_3_o);
  Mux2To1 mux2to1_4 (.A(mux2to1_3_o), .B(nand_6_out), .S(L), .O(mux2to1_4_o));
  JKFlipFlop jkflipflop_3 (.SB(SB), .J(mux2to1_3_o), .CLK(nand_2_out), .K(mux2to1_4_o), .O(O[2]));  // open: OC
  nand nand_7 (nand_7_out, nand_5_out, O[2]);
  nand nand_8 (nand_8_out, nand_7_out, nand_7_out);
  Mux2To1 mux2to1_5 (.A(nand_8_out), .B(I[2]), .S(L), .O(mux2to1_5_o));
  nand nand_9 (nand_9_out, mux2to1_5_o, mux2to1_5_o);
  Mux2To1 mux2to1_6 (.A(mux2to1_5_o), .B(nand_9_out), .S(L), .O(mux2to1_6_o));
  JKFlipFlop jkflipflop_4 (.SB(SB), .J(mux2to1_5_o), .CLK(nand_2_out), .K(mux2to1_6_o), .O(O[3]));  // open: OC
  nand nand_10 (nand_10_out, nand_8_out, O[3]);
  nand nand_11 (nand_11_out, nand_10_out, nand_10_out);
  Mux2To1 mux2to1_7 (.A(nand_11_out), .B(I[3]), .S(L), .O(mux2to1_7_o));
  nand nand_12 (nand_12_out, mux2to1_7_o, mux2to1_7_o);
  Mux2To1 mux2to1_8 (.A(mux2to1_7_o), .B(nand_12_out), .S(L), .O(mux2to1_8_o));
  JKFlipFlop jkflipflop_5 (.SB(SB), .J(mux2to1_7_o), .CLK(nand_2_out), .K(mux2to1_8_o), .O(O[4]));  // open: OC
  nand nand_13 (nand_13_out, nand_11_out, O[4]);
  nand nand_14 (nand_14_out, nand_13_out, nand_13_out);
  Mux2To1 mux2to1_9 (.A(nand_14_out), .B(I[4]), .S(L), .O(mux2to1_9_o));
  nand nand_15 (nand_15_out, mux2to1_9_o, mux2to1_9_o);
  Mux2To1 mux2to1_10 (.A(mux2to1_9_o), .B(nand_15_out), .S(L), .O(mux2to1_10_o));
  JKFlipFlop jkflipflop_6 (.SB(SB), .J(mux2to1_9_o), .CLK(nand_2_out), .K(mux2to1_10_o), .O(O[5]));  // open: OC
  nand nand_16 (nand_16_out, nand_14_out, O[5]);
  nand nand_17 (nand_17_out, nand_16_out, nand_16_out);
  Mux2To1 mux2to1_11 (.A(nand_17_out), .B(I[5]), .S(L), .O(mux2to1_11_o));
  nand nand_18 (nand_18_out, mux2to1_11_o, mux2to1_11_o);
  Mux2To1 mux2to1_12 (.A(mux2to1_11_o), .B(nand_18_out), .S(L), .O(mux2to1_12_o));
  JKFlipFlop jkflipflop_7 (.SB(SB), .J(mux2to1_11_o), .CLK(nand_2_out), .K(mux2to1_12_o), .O(O[6]));  // open: OC
  nand nand_19 (nand_19_out, nand_17_out, O[6]);
  nand nand_20 (nand_20_out, nand_19_out, nand_19_out);
  Mux2To1 mux2to1_13 (.A(nand_20_out), .B(I[6]), .S(L), .O(mux2to1_13_o));
  nand nand_21 (nand_21_out, mux2to1_13_o, mux2to1_13_o);
  Mux2To1 mux2to1_14 (.A(mux2to1_13_o), .B(nand_21_out), .S(L), .O(mux2to1_14_o));
  JKFlipFlop jkflipflop_8 (.SB(SB), .J(mux2to1_13_o), .CLK(nand_2_out), .K(mux2to1_14_o), .O(O[7]));  // open: OC
  nand nand_22 (nand_22_out, nand_20_out, O[7]);
  nand nand_23 (nand_23_out, nand_22_out, nand_22_out);
  Mux2To1 mux2to1_15 (.A(nand_23_out), .B(I[7]), .S(L), .O(mux2to1_15_o));
  nand nand_24 (nand_24_out, mux2to1_15_o, mux2to1_15_o);
  Mux2To1 mux2to1_16 (.A(mux2to1_15_o), .B(nand_24_out), .S(L), .O(mux2to1_16_o));
  JKFlipFlop jkflipflop_9 (.SB(SB), .J(mux2to1_15_o), .CLK(nand_2_out), .K(mux2to1_16_o), .O(O[8]));  // open: OC
  nand nand_25 (nand_25_out, nand_23_out, O[8]);
  nand nand_26 (nand_26_out, nand_25_out, nand_25_out);
  Mux2To1 mux2to1_17 (.A(nand_26_out), .B(I[8]), .S(L), .O(mux2to1_17_o));
  nand nand_27 (nand_27_out, mux2to1_17_o, mux2to1_17_o);
  Mux2To1 mux2to1_18 (.A(mux2to1_17_o), .B(nand_27_out), .S(L), .O(mux2to1_18_o));
  JKFlipFlop jkflipflop_10 (.SB(SB), .J(mux2to1_17_o), .CLK(nand_2_out), .K(mux2to1_18_o), .O(O[9]));  // open: OC
  nand nand_28 (nand_28_out, nand_26_out, O[9]);
  nand nand_29 (nand_29_out, nand_28_out, nand_28_out);
  Mux2To1 mux2to1_19 (.A(nand_29_out), .B(I[9]), .S(L), .O(mux2to1_19_o));
  nand nand_30 (nand_30_out, mux2to1_19_o, mux2to1_19_o);
  Mux2To1 mux2to1_20 (.A(mux2to1_19_o), .B(nand_30_out), .S(L), .O(mux2to1_20_o));
  JKFlipFlop jkflipflop_11 (.SB(SB), .J(mux2to1_19_o), .CLK(nand_2_out), .K(mux2to1_20_o), .O(O[10]));  // open: OC
  nand nand_31 (nand_31_out, nand_29_out, O[10]);
  nand nand_32 (nand_32_out, nand_31_out, nand_31_out);
  Mux2To1 mux2to1_21 (.A(nand_32_out), .B(I[10]), .S(L), .O(mux2to1_21_o));
  nand nand_33 (nand_33_out, mux2to1_21_o, mux2to1_21_o);
  Mux2To1 mux2to1_22 (.A(mux2to1_21_o), .B(nand_33_out), .S(L), .O(mux2to1_22_o));
  JKFlipFlop jkflipflop_12 (
    .SB(SB), .J(mux2to1_21_o), .CLK(nand_2_out), .K(mux2to1_22_o), .O(jkflipflop_12_o));  // open: OC
  nand nand_34 (nand_34_out, nand_32_out, jkflipflop_12_o);
  nand nand_35 (nand_35_out, nand_34_out, nand_34_out);
  Mux2To1 mux2to1_23 (.A(nand_35_out), .B(I[11]), .S(L), .O(mux2to1_23_o));
  nand nand_36 (nand_36_out, mux2to1_23_o, mux2to1_23_o);
  Mux2To1 mux2to1_24 (.A(mux2to1_23_o), .B(nand_36_out), .S(L), .O(mux2to1_24_o));
  JKFlipFlop jkflipflop_13 (.SB(SB), .J(mux2to1_23_o), .CLK(nand_2_out), .K(mux2to1_24_o), .O(O[11]));  // open: OC
  nand nand_37 (nand_37_out, nand_35_out, O[11]);
  nand nand_38 (nand_38_out, nand_37_out, nand_37_out);
  Mux2To1 mux2to1_25 (.A(nand_38_out), .B(I[12]), .S(L), .O(mux2to1_25_o));
  nand nand_39 (nand_39_out, mux2to1_25_o, mux2to1_25_o);
  Mux2To1 mux2to1_26 (.A(mux2to1_25_o), .B(nand_39_out), .S(L), .O(mux2to1_26_o));
  JKFlipFlop jkflipflop_14 (.SB(SB), .J(mux2to1_25_o), .CLK(nand_2_out), .K(mux2to1_26_o), .O(O[12]));  // open: OC
  nand nand_40 (nand_40_out, nand_38_out, O[12]);
  nand nand_41 (nand_41_out, nand_40_out, nand_40_out);
  Mux2To1 mux2to1_27 (.A(nand_41_out), .B(I[13]), .S(L), .O(mux2to1_27_o));
  nand nand_42 (nand_42_out, mux2to1_27_o, mux2to1_27_o);
  Mux2To1 mux2to1_28 (.A(mux2to1_27_o), .B(nand_42_out), .S(L), .O(mux2to1_28_o));
  JKFlipFlop jkflipflop_15 (.SB(SB), .J(mux2to1_27_o), .CLK(nand_2_out), .K(mux2to1_28_o), .O(O[13]));  // open: OC
  nand nand_43 (nand_43_out, nand_41_out, O[13]);
  nand nand_44 (nand_44_out, nand_43_out, nand_43_out);
  Mux2To1 mux2to1_29 (.A(nand_44_out), .B(I[14]), .S(L), .O(mux2to1_29_o));
  nand nand_45 (nand_45_out, mux2to1_29_o, mux2to1_29_o);
  Mux2To1 mux2to1_30 (.A(mux2to1_29_o), .B(nand_45_out), .S(L), .O(mux2to1_30_o));
  JKFlipFlop jkflipflop_16 (.SB(SB), .J(mux2to1_29_o), .CLK(nand_2_out), .K(mux2to1_30_o), .O(O[14]));  // open: OC
  nand nand_46 (nand_46_out, nand_44_out, O[14]);
  nand nand_47 (nand_47_out, nand_46_out, nand_46_out);
  Mux2To1 mux2to1_31 (.A(nand_47_out), .B(I[15]), .S(L), .O(mux2to1_31_o));
  nand nand_48 (nand_48_out, mux2to1_31_o, mux2to1_31_o);
  Mux2To1 mux2to1_32 (.A(mux2to1_31_o), .B(nand_48_out), .S(L), .O(mux2to1_32_o));
  JKFlipFlop jkflipflop_17 (.SB(SB), .J(mux2to1_31_o), .CLK(nand_2_out), .K(mux2to1_32_o), .O(O[15]));  // open: OC
  nand nand_49 (nand_49_out, nand_47_out, O[15]);
  nand nand_50 (nand_50_out, nand_49_out, nand_49_out);
  Mux2To1 mux2to1_33 (.A(nand_50_out), .B(I[16]), .S(L), .O(mux2to1_33_o));
  nand nand_51 (nand_51_out, mux2to1_33_o, mux2to1_33_o);
  Mux2To1 mux2to1_34 (.A(mux2to1_33_o), .B(nand_51_out), .S(L), .O(mux2to1_34_o));
  JKFlipFlop jkflipflop_18 (.SB(SB), .J(mux2to1_33_o), .CLK(nand_2_out), .K(mux2to1_34_o), .O(O[16]));  // open: OC
  nand nand_52 (nand_52_out, nand_50_out, O[16]);
  nand nand_53 (nand_53_out, nand_52_out, nand_52_out);
  Mux2To1 mux2to1_35 (.A(nand_53_out), .B(I[17]), .S(L), .O(mux2to1_35_o));
  nand nand_54 (nand_54_out, mux2to1_35_o, mux2to1_35_o);
  Mux2To1 mux2to1_36 (.A(mux2to1_35_o), .B(nand_54_out), .S(L), .O(mux2to1_36_o));
  JKFlipFlop jkflipflop_19 (.SB(SB), .J(mux2to1_35_o), .CLK(nand_2_out), .K(mux2to1_36_o), .O(O[17]));  // open: OC
  nand nand_55 (nand_55_out, nand_53_out, O[17]);
  nand nand_56 (nand_56_out, nand_55_out, nand_55_out);
  Mux2To1 mux2to1_37 (.A(nand_56_out), .B(I[18]), .S(L), .O(mux2to1_37_o));
  nand nand_57 (nand_57_out, mux2to1_37_o, mux2to1_37_o);
  Mux2To1 mux2to1_38 (.A(mux2to1_37_o), .B(nand_57_out), .S(L), .O(mux2to1_38_o));
  JKFlipFlop jkflipflop_20 (.SB(SB), .J(mux2to1_37_o), .CLK(nand_2_out), .K(mux2to1_38_o), .O(O[18]));  // open: OC
  nand nand_58 (nand_58_out, nand_56_out, O[18]);
  nand nand_59 (nand_59_out, nand_58_out, nand_58_out);
  Mux2To1 mux2to1_39 (.A(nand_59_out), .B(I[19]), .S(L), .O(mux2to1_39_o));
  nand nand_60 (nand_60_out, mux2to1_39_o, mux2to1_39_o);
  Mux2To1 mux2to1_40 (.A(mux2to1_39_o), .B(nand_60_out), .S(L), .O(mux2to1_40_o));
  JKFlipFlop jkflipflop_21 (.SB(SB), .J(mux2to1_39_o), .CLK(nand_2_out), .K(mux2to1_40_o), .O(O[19]));  // open: OC
endmodule

module JKFlipFlop (
  input  SB,
  input  J,
  input  CLK,
  input  K,
  output O,
  output OC
);

  wire dlatch_1_o, nand_1_out, nand_2_out, nand_3_out, nand_4_out, nand_5_out, nand_6_out, nand_7_out,
       nand_8_out, nand_9_out;

  nand nand_1 (nand_1_out, J, J);
  nand nand_2 (nand_2_out, K, K);
  nand nand_3 (nand_3_out, nand_1_out, nand_2_out);
  nand nand_4 (nand_4_out, nand_3_out, nand_3_out);
  nand nand_5 (nand_5_out, K, O);
  nand nand_6 (nand_6_out, nand_4_out, O);
  nand nand_7 (nand_7_out, nand_5_out, J);
  nand nand_8 (nand_8_out, CLK, CLK);
  nand nand_9 (nand_9_out, nand_6_out, nand_7_out);
  DLatch dlatch_1 (.E(nand_8_out), .D(nand_9_out), .SB(SB), .O(dlatch_1_o));  // open: OC
  DLatch dlatch_2 (.E(CLK), .D(dlatch_1_o), .SB(SB), .O(O), .OC(OC));
endmodule

module ALU (
  input  [9:0] A,
  input  [9:0] B,
  input  AZ,
  input  AC,
  input  BZ,
  input  BC,
  input  Cin,
  input  N,
  input  OC,
  output Cout,
  output [9:0] O
);

  wire [9:0] fulladder10_1_o, inverter10_1_o, inverter10_2_o, inverter10_3_o, mux2to1_10_1_o, mux2to1_10_2_o,
       mux2to1_10_3_o, mux2to1_10_4_o, mux2to1_10_5_o, nand10_1_o;

  Mux2To1_10 mux2to1_10_1 (.A(A), .B({10{1'b0}}), .S(AZ), .O(mux2to1_10_1_o));
  Mux2To1_10 mux2to1_10_2 (.A(B), .B({10{1'b0}}), .S(BZ), .O(mux2to1_10_2_o));
  Inverter10 inverter10_1 (.I(mux2to1_10_1_o), .O(inverter10_1_o));
  Inverter10 inverter10_2 (.I(mux2to1_10_2_o), .O(inverter10_2_o));
  Mux2To1_10 mux2to1_10_3 (.A(mux2to1_10_1_o), .B(inverter10_1_o), .S(AC), .O(mux2to1_10_3_o));
  Mux2To1_10 mux2to1_10_4 (.A(mux2to1_10_2_o), .B(inverter10_2_o), .S(BC), .O(mux2to1_10_4_o));
  FullAdder10 fulladder10_1 (.Cin(Cin), .A(mux2to1_10_3_o), .B(mux2to1_10_4_o), .O(fulladder10_1_o), .Cout(Cout));
  Nand10 nand10_1 (.A(mux2to1_10_3_o), .B(mux2to1_10_4_o), .O(nand10_1_o));
  Mux2To1_10 mux2to1_10_5 (.A(fulladder10_1_o), .B(nand10_1_o), .S(N), .O(mux2to1_10_5_o));
  Inverter10 inverter10_3 (.I(mux2to1_10_5_o), .O(inverter10_3_o));
  Mux2To1_10 mux2to1_10_6 (.A(mux2to1_10_5_o), .B(inverter10_3_o), .S(OC), .O(O));
endmodule

module Mux2To1_10 (
  input  [9:0] A,
  input  [9:0] B,
  input  S,
  output [9:0] O
);

  Mux2To1 mux2to1_1 (.A(A[0]), .B(B[0]), .S(S), .O(O[0]));
  Mux2To1 mux2to1_2 (.A(A[1]), .B(B[1]), .S(S), .O(O[1]));
  Mux2To1 mux2to1_3 (.A(A[2]), .B(B[2]), .S(S), .O(O[2]));
  Mux2To1 mux2to1_4 (.A(A[3]), .B(B[3]), .S(S), .O(O[3]));
  Mux2To1 mux2to1_5 (.A(A[4]), .B(B[4]), .S(S), .O(O[4]));
  Mux2To1 mux2to1_6 (.A(A[5]), .B(B[5]), .S(S), .O(O[5]));
  Mux2To1 mux2to1_7 (.A(A[6]), .B(B[6]), .S(S), .O(O[6]));
  Mux2To1 mux2to1_8 (.A(A[7]), .B(B[7]), .S(S), .O(O[7]));
  Mux2To1 mux2to1_9 (.A(A[8]), .B(B[8]), .S(S), .O(O[8]));
  Mux2To1 mux2to1_10 (.A(A[9]), .B(B[9]), .S(S), .O(O[9]));
endmodule

module Inverter10 (
  input  [9:0] I,
  output [9:0] O
);

  Nand10 nand10_1 (.A(I), .B(I), .O(O));
endmodule

module FullAdder (
  input  A,
  input  B,
  input  Cin,
  output O,
  output Cout
);

  wire nand_1_out, nand_2_out, nand_3_out, nand_4_out, nand_5_out, nand_6_out, nand_7_out, nand_8_out,
       nand_9_out, nand_10_out, nand_11_out;

  nand nand_1 (nand_1_out, A, A);
  nand nand_2 (nand_2_out, B, B);
  nand nand_3 (nand_3_out, B, A);
  nand nand_4 (nand_4_out, A, nand_2_out);
  nand nand_5 (nand_5_out, nand_1_out, B);
  nand nand_6 (nand_6_out, nand_4_out, nand_5_out);
  nand nand_7 (nand_7_out, nand_6_out, nand_6_out);
  nand nand_8 (nand_8_out, Cin, Cin);
  nand nand_9 (nand_9_out, Cin, nand_6_out);
  nand nand_10 (nand_10_out, nand_6_out, nand_8_out);
  nand nand_11 (nand_11_out, nand_7_out, Cin);
  nand nand_12 (O, nand_10_out, nand_11_out);
  nand nand_13 (Cout, nand_9_out, nand_3_out);
endmodule

module HalfAdder (
  input  A,
  input  B,
  output S,
  output C
);

  wire nand_1_out, nand_2_out, nand_3_out, nand_5_out, nand_6_out;

  nand nand_1 (nand_1_out, A, A);
  nand nand_2 (nand_2_out, B, B);
  nand nand_3 (nand_3_out, B, A);
  nand nand_4 (C, nand_3_out, nand_3_out);
  nand nand_5 (nand_5_out, A, nand_2_out);
  nand nand_6 (nand_6_out, nand_1_out, B);
  nand nand_7 (S, nand_5_out, nand_6_out);
endmodule

module FullAdder10 (
  input  Cin,
  input  [9:0] A,
  input  [9:0] B,
  output [9:0] O,
  output Cout
);

  wire fulladder_1_cout, fulladder_2_cout, fulladder_3_cout, fulladder_4_cout, fulladder_5_cout,
       fulladder_6_cout, fulladder_7_cout, fulladder_8_cout, fulladder_9_cout;

  FullAdder fulladder_1 (.A(A[0]), .B(B[0]), .Cin(Cin), .O(O[0]), .Cout(fulladder_1_cout));
  FullAdder fulladder_2 (.A(A[1]), .B(B[1]), .Cin(fulladder_1_cout), .O(O[1]), .Cout(fulladder_2_cout));
  FullAdder fulladder_3 (.A(A[2]), .B(B[2]), .Cin(fulladder_2_cout), .O(O[2]), .Cout(fulladder_3_cout));
  FullAdder fulladder_4 (.A(A[3]), .B(B[3]), .Cin(fulladder_3_cout), .O(O[3]), .Cout(fulladder_4_cout));
  FullAdder fulladder_5 (.A(A[4]), .B(B[4]), .Cin(fulladder_4_cout), .O(O[4]), .Cout(fulladder_5_cout));
  FullAdder fulladder_6 (.A(A[5]), .B(B[5]), .Cin(fulladder_5_cout), .O(O[5]), .Cout(fulladder_6_cout));
  FullAdder fulladder_7 (.A(A[6]), .B(B[6]), .Cin(fulladder_6_cout), .O(O[6]), .Cout(fulladder_7_cout));
  FullAdder fulladder_8 (.A(A[7]), .B(B[7]), .Cin(fulladder_7_cout), .O(O[7]), .Cout(fulladder_8_cout));
  FullAdder fulladder_9 (.A(A[8]), .B(B[8]), .Cin(fulladder_8_cout), .O(O[8]), .Cout(fulladder_9_cout));
  FullAdder fulladder_10 (.A(A[9]), .B(B[9]), .Cin(fulladder_9_cout), .O(O[9]), .Cout(Cout));
endmodule

module Nand10 (
  input  [9:0] A,
  input  [9:0] B,
  output [9:0] O
);

  nand nand_1 (O[0], A[0], B[0]);
  nand nand_2 (O[1], A[1], B[1]);
  nand nand_3 (O[2], A[2], B[2]);
  nand nand_4 (O[3], A[3], B[3]);
  nand nand_5 (O[4], A[4], B[4]);
  nand nand_6 (O[5], A[5], B[5]);
  nand nand_7 (O[6], A[6], B[6]);
  nand nand_8 (O[7], A[7], B[7]);
  nand nand_9 (O[8], A[8], B[8]);
  nand nand_10 (O[9], A[9], B[9]);
endmodule

module Buffer10 (
  input  [9:0] I,
  input  E,
  output [9:0] O
);

  assign O[0] = E ? I[0] : 1'bz;  // Controlled_Buffer controlled_buffer_1
  assign O[1] = E ? I[1] : 1'bz;  // Controlled_Buffer controlled_buffer_2
  assign O[2] = E ? I[2] : 1'bz;  // Controlled_Buffer controlled_buffer_3
  assign O[3] = E ? I[3] : 1'bz;  // Controlled_Buffer controlled_buffer_4
  assign O[4] = E ? I[4] : 1'bz;  // Controlled_Buffer controlled_buffer_5
  assign O[5] = E ? I[5] : 1'bz;  // Controlled_Buffer controlled_buffer_6
  assign O[6] = E ? I[6] : 1'bz;  // Controlled_Buffer controlled_buffer_7
  assign O[7] = E ? I[7] : 1'bz;  // Controlled_Buffer controlled_buffer_8
  assign O[8] = E ? I[8] : 1'bz;  // Controlled_Buffer controlled_buffer_9
  assign O[9] = E ? I[9] : 1'bz;  // Controlled_Buffer controlled_buffer_10
endmodule

module ALUFlagsRegister (
  input  CLK,
  input  LL,
  input  LH,
  input  SB,
  input  [6:0] I,
  output [6:0] O
);

  wire nand_1_out, nand_2_out, nand_3_out, nand_4_out;

  nand nand_1 (nand_1_out, CLK, LL);
  nand nand_2 (nand_2_out, nand_1_out, nand_1_out);
  nand nand_3 (nand_3_out, CLK, LH);
  nand nand_4 (nand_4_out, nand_3_out, nand_3_out);
  DLatch dlatch_1 (.E(nand_2_out), .D(I[0]), .SB(SB), .O(O[0]));  // open: OC
  DLatch dlatch_2 (.E(nand_2_out), .D(I[1]), .SB(SB), .O(O[1]));  // open: OC
  DLatch dlatch_3 (.E(nand_2_out), .D(I[2]), .SB(SB), .O(O[2]));  // open: OC
  DLatch dlatch_4 (.E(nand_2_out), .D(I[3]), .SB(SB), .O(O[3]));  // open: OC
  DLatch dlatch_5 (.E(nand_2_out), .D(I[4]), .SB(SB), .O(O[4]));  // open: OC
  DLatch dlatch_6 (.E(nand_4_out), .D(I[5]), .SB(SB), .O(O[5]));  // open: OC
  DLatch dlatch_7 (.E(nand_4_out), .D(I[6]), .SB(SB), .O(O[6]));  // open: OC
endmodule

module Mux2To1_20 (
  input  [19:0] A,
  input  [19:0] B,
  input  S,
  output [19:0] O
);

  Mux2To1_10 mux2to1_10_1 (.A(A[9:0]), .B(B[9:0]), .S(S), .O(O[9:0]));
  Mux2To1_10 mux2to1_10_2 (.A(A[19:10]), .B(B[19:10]), .S(S), .O(O[19:10]));
endmodule

module Buffer20 (
  input  [19:0] I,
  input  E,
  output [19:0] O
);

  Buffer10 buffer10_1 (.I(I[9:0]), .E(E), .O(O[9:0]));
  Buffer10 buffer10_2 (.I(I[19:10]), .E(E), .O(O[19:10]));
endmodule

module NormalRegister20 (
  input  CLK,
  input  LLL,
  input  LLH,
  input  LHL,
  input  LHH,
  input  SB,
  input  [9:0] IL,
  input  [9:0] IH,
  output [19:0] O
);

  NormalRegister normalregister_1 (.CLK(CLK), .LL(LLL), .LH(LLH), .SB(SB), .I(IL), .O(O[9:0]));
  NormalRegister normalregister_2 (.CLK(CLK), .LL(LHL), .LH(LHH), .SB(SB), .I(IH), .O(O[19:10]));
endmodule

module NormalRegister4 (
  input  CLK,
  input  LOAD,
  input  SB,
  input  [3:0] I,
  output [3:0] O
);

  wire nand_1_out, nand_2_out;

  nand nand_1 (nand_1_out, CLK, LOAD);
  nand nand_2 (nand_2_out, nand_1_out, nand_1_out);
  DFlipFlop dflipflop_1 (.CLK(nand_2_out), .D(I[0]), .SB(SB), .O(O[0]));  // open: OC
  DFlipFlop dflipflop_2 (.CLK(nand_2_out), .D(I[1]), .SB(SB), .O(O[1]));  // open: OC
  DFlipFlop dflipflop_3 (.CLK(nand_2_out), .D(I[2]), .SB(SB), .O(O[2]));  // open: OC
  DFlipFlop dflipflop_4 (.CLK(nand_2_out), .D(I[3]), .SB(SB), .O(O[3]));  // open: OC
endmodule

module Buffer4 (
  input  [3:0] I,
  input  E,
  output [3:0] O
);

  assign O[0] = E ? I[0] : 1'bz;  // Controlled_Buffer controlled_buffer_1
  assign O[1] = E ? I[1] : 1'bz;  // Controlled_Buffer controlled_buffer_2
  assign O[2] = E ? I[2] : 1'bz;  // Controlled_Buffer controlled_buffer_3
  assign O[3] = E ? I[3] : 1'bz;  // Controlled_Buffer controlled_buffer_4
endmodule

module NormalRegister3 (
  input  CLK,
  input  LOAD,
  input  SB,
  input  [2:0] I,
  output [2:0] O
);

  wire nand_1_out, nand_2_out;

  nand nand_1 (nand_1_out, CLK, LOAD);
  nand nand_2 (nand_2_out, nand_1_out, nand_1_out);
  DFlipFlop dflipflop_1 (.CLK(nand_2_out), .D(I[0]), .SB(SB), .O(O[0]));  // open: OC
  DFlipFlop dflipflop_2 (.CLK(nand_2_out), .D(I[1]), .SB(SB), .O(O[1]));  // open: OC
  DFlipFlop dflipflop_3 (.CLK(nand_2_out), .D(I[2]), .SB(SB), .O(O[2]));  // open: OC
endmodule

module Or10 (
  input  [9:0] I,
  output O
);

  wire nand_1_out, nand_2_out, nand_3_out, nand_4_out, nand_5_out, nand_6_out, nand_7_out, nand_8_out,
       nand_9_out, nand_10_out, nand_11_out, nand_12_out, nand_13_out, nand_14_out, nand_15_out, nand_16_out,
       nand_17_out, nand_18_out, nand_19_out, nand_20_out, nand_21_out, nand_22_out, nand_23_out,
       nand_24_out, nand_25_out, nand_26_out;

  nand nand_1 (nand_1_out, I[0], I[0]);
  nand nand_2 (nand_2_out, I[1], I[1]);
  nand nand_3 (nand_3_out, nand_1_out, nand_2_out);
  nand nand_4 (nand_4_out, nand_3_out, nand_3_out);
  nand nand_5 (nand_5_out, I[2], I[2]);
  nand nand_6 (nand_6_out, nand_4_out, nand_5_out);
  nand nand_7 (nand_7_out, nand_6_out, nand_6_out);
  nand nand_8 (nand_8_out, I[3], I[3]);
  nand nand_9 (nand_9_out, nand_7_out, nand_8_out);
  nand nand_10 (nand_10_out, nand_9_out, nand_9_out);
  nand nand_11 (nand_11_out, I[4], I[4]);
  nand nand_12 (nand_12_out, nand_10_out, nand_11_out);
  nand nand_13 (nand_13_out, nand_12_out, nand_12_out);
  nand nand_14 (nand_14_out, I[5], I[5]);
  nand nand_15 (nand_15_out, nand_13_out, nand_14_out);
  nand nand_16 (nand_16_out, nand_15_out, nand_15_out);
  nand nand_17 (nand_17_out, I[6], I[6]);
  nand nand_18 (nand_18_out, nand_16_out, nand_17_out);
  nand nand_19 (nand_19_out, nand_18_out, nand_18_out);
  nand nand_20 (nand_20_out, I[7], I[7]);
  nand nand_21 (nand_21_out, nand_19_out, nand_20_out);
  nand nand_22 (nand_22_out, nand_21_out, nand_21_out);
  nand nand_23 (nand_23_out, I[8], I[8]);
  nand nand_24 (nand_24_out, nand_22_out, nand_23_out);
  nand nand_25 (nand_25_out, nand_24_out, nand_24_out);
  nand nand_26 (nand_26_out, I[9], I[9]);
  nand nand_27 (O, nand_25_out, nand_26_out);
endmodule

module Buffer38 (
  input  [37:0] I,
  input  E,
  output [37:0] O
);

  assign O[30] = E ? I[30] : 1'bz;  // Controlled_Buffer controlled_buffer_1
  assign O[31] = E ? I[31] : 1'bz;  // Controlled_Buffer controlled_buffer_2
  assign O[32] = E ? I[32] : 1'bz;  // Controlled_Buffer controlled_buffer_3
  assign O[33] = E ? I[33] : 1'bz;  // Controlled_Buffer controlled_buffer_4
  assign O[34] = E ? I[34] : 1'bz;  // Controlled_Buffer controlled_buffer_5
  assign O[35] = E ? I[35] : 1'bz;  // Controlled_Buffer controlled_buffer_6
  assign O[36] = E ? I[36] : 1'bz;  // Controlled_Buffer controlled_buffer_7
  assign O[37] = E ? I[37] : 1'bz;  // Controlled_Buffer controlled_buffer_8
  Buffer10 buffer10_1 (.I(I[9:0]), .E(E), .O(O[9:0]));
  Buffer10 buffer10_2 (.I(I[19:10]), .E(E), .O(O[19:10]));
  Buffer10 buffer10_3 (.I(I[29:20]), .E(E), .O(O[29:20]));
endmodule

module And10 (
  input  [9:0] I,
  output O
);

  wire nand_1_out, nand_2_out, nand_3_out, nand_4_out, nand_5_out, nand_6_out, nand_7_out, nand_8_out,
       nand_9_out, nand_10_out, nand_11_out, nand_12_out, nand_13_out, nand_14_out, nand_15_out, nand_16_out,
       nand_17_out;

  nand nand_1 (nand_1_out, I[0], I[1]);
  nand nand_2 (nand_2_out, nand_1_out, nand_1_out);
  nand nand_3 (nand_3_out, nand_2_out, I[2]);
  nand nand_4 (nand_4_out, nand_3_out, nand_3_out);
  nand nand_5 (nand_5_out, nand_4_out, I[3]);
  nand nand_6 (nand_6_out, nand_5_out, nand_5_out);
  nand nand_7 (nand_7_out, nand_6_out, I[4]);
  nand nand_8 (nand_8_out, nand_7_out, nand_7_out);
  nand nand_9 (nand_9_out, nand_8_out, I[5]);
  nand nand_10 (nand_10_out, nand_9_out, nand_9_out);
  nand nand_11 (nand_11_out, nand_10_out, I[6]);
  nand nand_12 (nand_12_out, nand_11_out, nand_11_out);
  nand nand_13 (nand_13_out, nand_12_out, I[7]);
  nand nand_14 (nand_14_out, nand_13_out, nand_13_out);
  nand nand_15 (nand_15_out, nand_14_out, I[8]);
  nand nand_16 (nand_16_out, nand_15_out, nand_15_out);
  nand nand_17 (nand_17_out, nand_16_out, I[9]);
  nand nand_18 (O, nand_17_out, nand_17_out);
endmodule

module Demux1To2 (
  input  I,
  input  S,
  output A,
  output B
);

  wire nand_1_out, nand_2_out, nand_4_out;

  nand nand_1 (nand_1_out, S, S);
  nand nand_2 (nand_2_out, I, nand_1_out);
  nand nand_3 (A, nand_2_out, nand_2_out);
  nand nand_4 (nand_4_out, I, S);
  nand nand_5 (B, nand_4_out, nand_4_out);
endmodule

module Demux1To8S3 (
  input  I,
  input  [2:0] S,
  output [7:0] O
);

  wire and3_1_o, and3_2_o, and3_3_o, and3_4_o, and3_5_o, and3_6_o, and3_7_o, and3_8_o, nand_4_out,
       nand_5_out, nand_6_out, nand_7_out, nand_8_out, nand_9_out, nand_10_out, nand_11_out;
  wire [2:0] nand_3_out;

  nand nand_1 (nand_3_out[0], S[0], S[0]);
  nand nand_2 (nand_3_out[1], S[1], S[1]);
  nand nand_3 (nand_3_out[2], S[2], S[2]);
  And3 and3_1 (.I(nand_3_out), .O(and3_1_o));
  And3 and3_2 (.I({nand_3_out[2:1], S[0]}), .O(and3_2_o));
  And3 and3_3 (.I({nand_3_out[2], S[1], nand_3_out[0]}), .O(and3_3_o));
  And3 and3_4 (.I({nand_3_out[2], S[1:0]}), .O(and3_4_o));
  And3 and3_5 (.I({S[2], nand_3_out[1:0]}), .O(and3_5_o));
  And3 and3_6 (.I({S[2], nand_3_out[1], S[0]}), .O(and3_6_o));
  And3 and3_7 (.I({S[2:1], nand_3_out[0]}), .O(and3_7_o));
  And3 and3_8 (.I(S), .O(and3_8_o));
  nand nand_4 (nand_4_out, I, and3_1_o);
  nand nand_5 (nand_5_out, I, and3_2_o);
  nand nand_6 (nand_6_out, I, and3_3_o);
  nand nand_7 (nand_7_out, I, and3_4_o);
  nand nand_8 (nand_8_out, I, and3_5_o);
  nand nand_9 (nand_9_out, I, and3_6_o);
  nand nand_10 (nand_10_out, I, and3_7_o);
  nand nand_11 (nand_11_out, I, and3_8_o);
  nand nand_12 (O[0], nand_4_out, nand_4_out);
  nand nand_13 (O[1], nand_5_out, nand_5_out);
  nand nand_14 (O[2], nand_6_out, nand_6_out);
  nand nand_15 (O[3], nand_7_out, nand_7_out);
  nand nand_16 (O[4], nand_8_out, nand_8_out);
  nand nand_17 (O[5], nand_9_out, nand_9_out);
  nand nand_18 (O[6], nand_10_out, nand_10_out);
  nand nand_19 (O[7], nand_11_out, nand_11_out);
endmodule

module And3 (
  input  [2:0] I,
  output O
);

  wire nand_1_out, nand_2_out, nand_3_out;

  nand nand_1 (nand_1_out, I[0], I[1]);
  nand nand_2 (nand_2_out, nand_1_out, nand_1_out);
  nand nand_3 (nand_3_out, nand_2_out, I[2]);
  nand nand_4 (O, nand_3_out, nand_3_out);
endmodule

module Demux1To9S4 (
  input  I,
  input  [3:0] S,
  output [8:0] O
);

  wire and4_1_o, and4_2_o, and4_3_o, and4_4_o, and4_5_o, and4_6_o, and4_7_o, and4_8_o, and4_9_o, nand_5_out,
       nand_6_out, nand_7_out, nand_8_out, nand_9_out, nand_10_out, nand_11_out, nand_12_out, nand_13_out;
  wire [2:0] nand_1_out;
  wire [3:3] nand_4_out;

  nand nand_1 (nand_1_out[0], S[0], S[0]);
  nand nand_2 (nand_1_out[1], S[1], S[1]);
  nand nand_3 (nand_1_out[2], S[2], S[2]);
  nand nand_4 (nand_4_out[3], S[3], S[3]);
  And4 and4_1 (.I({nand_4_out[3], nand_1_out}), .O(and4_1_o));
  And4 and4_2 (.I({nand_4_out[3], nand_1_out[2:1], S[0]}), .O(and4_2_o));
  And4 and4_3 (.I({nand_4_out[3], nand_1_out[2], S[1], nand_1_out[0]}), .O(and4_3_o));
  And4 and4_4 (.I({nand_4_out[3], nand_1_out[2], S[1:0]}), .O(and4_4_o));
  And4 and4_5 (.I({nand_4_out[3], S[2], nand_1_out[1:0]}), .O(and4_5_o));
  And4 and4_6 (.I({nand_4_out[3], S[2], nand_1_out[1], S[0]}), .O(and4_6_o));
  And4 and4_7 (.I({nand_4_out[3], S[2:1], nand_1_out[0]}), .O(and4_7_o));
  And4 and4_8 (.I({nand_4_out[3], S[2:0]}), .O(and4_8_o));
  And4 and4_9 (.I({S[3], nand_1_out}), .O(and4_9_o));
  nand nand_5 (nand_5_out, I, and4_1_o);
  nand nand_6 (nand_6_out, I, and4_2_o);
  nand nand_7 (nand_7_out, I, and4_3_o);
  nand nand_8 (nand_8_out, I, and4_4_o);
  nand nand_9 (nand_9_out, I, and4_5_o);
  nand nand_10 (nand_10_out, I, and4_6_o);
  nand nand_11 (nand_11_out, I, and4_7_o);
  nand nand_12 (nand_12_out, I, and4_8_o);
  nand nand_13 (nand_13_out, I, and4_9_o);
  nand nand_14 (O[0], nand_5_out, nand_5_out);
  nand nand_15 (O[1], nand_6_out, nand_6_out);
  nand nand_16 (O[2], nand_7_out, nand_7_out);
  nand nand_17 (O[3], nand_8_out, nand_8_out);
  nand nand_18 (O[4], nand_9_out, nand_9_out);
  nand nand_19 (O[5], nand_10_out, nand_10_out);
  nand nand_20 (O[6], nand_11_out, nand_11_out);
  nand nand_21 (O[7], nand_12_out, nand_12_out);
  nand nand_22 (O[8], nand_13_out, nand_13_out);
endmodule

module And4 (
  input  [3:0] I,
  output O
);

  wire nand_1_out, nand_2_out, nand_3_out, nand_4_out, nand_5_out;

  nand nand_1 (nand_1_out, I[0], I[1]);
  nand nand_2 (nand_2_out, nand_1_out, nand_1_out);
  nand nand_3 (nand_3_out, nand_2_out, I[2]);
  nand nand_4 (nand_4_out, nand_3_out, nand_3_out);
  nand nand_5 (nand_5_out, nand_4_out, I[3]);
  nand nand_6 (O, nand_5_out, nand_5_out);
endmodule

module ControlDestination (
  input  OUTPUT_ENABLE,
  input  UPPER,
  input  LOWER,
  input  [2:0] S,
  output [37:0] O
);

  wire A_LOAD_HIGH_out, A_LOAD_LOW_out, B_LOAD_HIGH_out, B_LOAD_LOW_out, C_LOAD_HIGH_out, C_LOAD_LOW_out,
       D_LOAD_HIGH_out, D_LOAD_LOW_out, MARH_LOAD_HIGH_out, MARH_LOAD_LOW_out, MARL_LOAD_HIGH_out,
       MARL_LOAD_LOW_out, SP_LOAD_HIGH_out, SP_LOAD_LOW_out;
  wire [7:1] REG_DESTINATION_SELECT_o;
  wire [37:0] undriven;

  Demux1To8S3 REG_DESTINATION_SELECT (
    .I(OUTPUT_ENABLE), .S(S),
    .O({REG_DESTINATION_SELECT_o[7:6], undriven[21], REG_DESTINATION_SELECT_o[4:1], undriven[10]}));
  nand A_LOAD_HIGH (A_LOAD_HIGH_out, UPPER, undriven[10]);
  nand nand_1 (undriven[8], A_LOAD_HIGH_out, A_LOAD_HIGH_out);
  nand A_LOAD_LOW (A_LOAD_LOW_out, LOWER, undriven[10]);
  nand B_LOAD_LOW (B_LOAD_LOW_out, REG_DESTINATION_SELECT_o[1], LOWER);
  nand B_LOAD_HIGH (B_LOAD_HIGH_out, REG_DESTINATION_SELECT_o[1], UPPER);
  nand C_LOAD_LOW (C_LOAD_LOW_out, REG_DESTINATION_SELECT_o[2], LOWER);
  nand C_LOAD_HIGH (C_LOAD_HIGH_out, REG_DESTINATION_SELECT_o[2], UPPER);
  nand D_LOAD_LOW (D_LOAD_LOW_out, REG_DESTINATION_SELECT_o[3], LOWER);
  nand D_LOAD_HIGH (D_LOAD_HIGH_out, REG_DESTINATION_SELECT_o[3], UPPER);
  nand SP_LOAD_LOW (SP_LOAD_LOW_out, REG_DESTINATION_SELECT_o[4], LOWER);
  nand SP_LOAD_HIGH (SP_LOAD_HIGH_out, REG_DESTINATION_SELECT_o[4], UPPER);
  nand MARL_LOAD_LOW (MARL_LOAD_LOW_out, REG_DESTINATION_SELECT_o[6], LOWER);
  nand MARL_LOAD_HIGH (MARL_LOAD_HIGH_out, REG_DESTINATION_SELECT_o[6], UPPER);
  nand MARH_LOAD_LOW (MARH_LOAD_LOW_out, REG_DESTINATION_SELECT_o[7], LOWER);
  nand MARH_LOAD_HIGH (MARH_LOAD_HIGH_out, REG_DESTINATION_SELECT_o[7], UPPER);
  nand nand_2 (undriven[7], A_LOAD_LOW_out, A_LOAD_LOW_out);
  nand nand_3 (undriven[11], B_LOAD_LOW_out, B_LOAD_LOW_out);
  nand nand_4 (undriven[12], B_LOAD_HIGH_out, B_LOAD_HIGH_out);
  nand nand_5 (undriven[14], C_LOAD_LOW_out, C_LOAD_LOW_out);
  nand nand_6 (undriven[15], C_LOAD_HIGH_out, C_LOAD_HIGH_out);
  nand nand_7 (undriven[17], D_LOAD_LOW_out, D_LOAD_LOW_out);
  nand nand_8 (undriven[18], D_LOAD_HIGH_out, D_LOAD_HIGH_out);
  nand nand_9 (undriven[24], SP_LOAD_LOW_out, SP_LOAD_LOW_out);
  nand nand_10 (undriven[25], SP_LOAD_HIGH_out, SP_LOAD_HIGH_out);
  nand nand_11 (undriven[31], MARL_LOAD_LOW_out, MARL_LOAD_LOW_out);
  nand nand_12 (undriven[32], MARL_LOAD_HIGH_out, MARL_LOAD_HIGH_out);
  nand nand_13 (undriven[33], MARH_LOAD_LOW_out, MARH_LOAD_LOW_out);
  nand nand_14 (undriven[34], MARH_LOAD_HIGH_out, MARH_LOAD_HIGH_out);
  Buffer38 buffer38_1 (.I({undriven[37:10], undriven[10], undriven[8:0]}), .E(OUTPUT_ENABLE), .O(O));
endmodule

module Or4 (
  input  [3:0] I,
  output O
);

  wire nand_1_out, nand_2_out, nand_3_out, nand_4_out, nand_5_out, nand_6_out, nand_7_out, nand_8_out;

  nand nand_1 (nand_1_out, I[0], I[0]);
  nand nand_2 (nand_2_out, I[1], I[1]);
  nand nand_3 (nand_3_out, nand_1_out, nand_2_out);
  nand nand_4 (nand_4_out, nand_3_out, nand_3_out);
  nand nand_5 (nand_5_out, I[2], I[2]);
  nand nand_6 (nand_6_out, nand_4_out, nand_5_out);
  nand nand_7 (nand_7_out, nand_6_out, nand_6_out);
  nand nand_8 (nand_8_out, I[3], I[3]);
  nand nand_9 (O, nand_7_out, nand_8_out);
endmodule

module ControlSource (
  input  OUTPUT_ENABLE,
  input  [2:0] S,
  output [37:0] O
);

  wire [7:7] demux1to8s3_1_o;
  wire [37:0] undriven;

  Demux1To8S3 demux1to8s3_1 (
    .I(OUTPUT_ENABLE), .S(S),
    .O({demux1to8s3_1_o[7], undriven[22], undriven[23], undriven[26], undriven[19], undriven[16], undriven[13], undriven[6]}));
  Buffer38 buffer38_1 (.I(undriven), .E(OUTPUT_ENABLE), .O(O));
endmodule

module Or5 (
  input  [4:0] I,
  output O
);

  wire nand_1_out, nand_2_out, nand_3_out, nand_4_out, nand_5_out, nand_6_out, nand_7_out, nand_8_out,
       nand_9_out, nand_10_out, nand_11_out;

  nand nand_1 (nand_1_out, I[0], I[0]);
  nand nand_2 (nand_2_out, I[1], I[1]);
  nand nand_3 (nand_3_out, nand_1_out, nand_2_out);
  nand nand_4 (nand_4_out, nand_3_out, nand_3_out);
  nand nand_5 (nand_5_out, I[2], I[2]);
  nand nand_6 (nand_6_out, nand_4_out, nand_5_out);
  nand nand_7 (nand_7_out, nand_6_out, nand_6_out);
  nand nand_8 (nand_8_out, I[3], I[3]);
  nand nand_9 (nand_9_out, nand_7_out, nand_8_out);
  nand nand_10 (nand_10_out, nand_9_out, nand_9_out);
  nand nand_11 (nand_11_out, I[4], I[4]);
  nand nand_12 (O, nand_10_out, nand_11_out);
endmodule

module Or3 (
  input  [2:0] I,
  output O
);

  wire nand_1_out, nand_2_out, nand_3_out, nand_4_out, nand_5_out;

  nand nand_1 (nand_1_out, I[0], I[0]);
  nand nand_2 (nand_2_out, I[1], I[1]);
  nand nand_3 (nand_3_out, nand_1_out, nand_2_out);
  nand nand_4 (nand_4_out, nand_3_out, nand_3_out);
  nand nand_5 (nand_5_out, I[2], I[2]);
  nand nand_6 (O, nand_4_out, nand_5_out);
endmodule

module Mux2To1_4 (
  input  [3:0] A,
  input  [3:0] B,
  input  S,
  output [3:0] O
);

  Mux2To1 mux2to1_1 (.A(A[0]), .B(B[0]), .S(S), .O(O[0]));
  Mux2To1 mux2to1_2 (.A(A[1]), .B(B[1]), .S(S), .O(O[1]));
  Mux2To1 mux2to1_3 (.A(A[2]), .B(B[2]), .S(S), .O(O[2]));
  Mux2To1 mux2to1_4 (.A(A[3]), .B(B[3]), .S(S), .O(O[3]));
endmodule

module Not4 (
  input  [3:0] I,
  output [3:0] O
);

  nand nand_1 (O[0], I[0], I[0]);
  nand nand_2 (O[1], I[1], I[1]);
  nand nand_3 (O[2], I[2], I[2]);
  nand nand_4 (O[3], I[3], I[3]);
endmodule

module And2_4 (
  input  [3:0] A,
  input  [3:0] B,
  output [3:0] O
);

  wire nand_1_out, nand_2_out, nand_3_out, nand_4_out;

  nand nand_1 (nand_1_out, A[0], B[0]);
  nand nand_2 (nand_2_out, A[1], B[1]);
  nand nand_3 (nand_3_out, A[2], B[2]);
  nand nand_4 (nand_4_out, A[3], B[3]);
  nand nand_5 (O[0], nand_1_out, nand_1_out);
  nand nand_6 (O[1], nand_2_out, nand_2_out);
  nand nand_7 (O[2], nand_3_out, nand_3_out);
  nand nand_8 (O[3], nand_4_out, nand_4_out);
endmodule

module NormalRegister1 (
  input  CLK,
  input  LOAD,
  input  D,
  input  SB,
  output O,
  output OC
);

  wire nand_1_out, nand_2_out;

  nand nand_1 (nand_1_out, CLK, LOAD);
  nand nand_2 (nand_2_out, nand_1_out, nand_1_out);
  DFlipFlop dflipflop_1 (.CLK(nand_2_out), .D(D), .SB(SB), .O(O), .OC(OC));
endmodule

module Or2_4 (
  input  [3:0] A,
  input  [3:0] B,
  output [3:0] O
);

  wire nand_1_out, nand_3_out, nand_4_out, nand_6_out, nand_7_out, nand_9_out, nand_10_out, nand_12_out;

  nand nand_1 (nand_1_out, A[0], A[0]);
  nand nand_2 (O[0], nand_1_out, nand_3_out);
  nand nand_3 (nand_3_out, B[0], B[0]);
  nand nand_4 (nand_4_out, A[1], A[1]);
  nand nand_5 (O[1], nand_4_out, nand_6_out);
  nand nand_6 (nand_6_out, B[1], B[1]);
  nand nand_7 (nand_7_out, A[2], A[2]);
  nand nand_8 (O[2], nand_7_out, nand_9_out);
  nand nand_9 (nand_9_out, B[2], B[2]);
  nand nand_10 (nand_10_out, A[3], A[3]);
  nand nand_11 (O[3], nand_10_out, nand_12_out);
  nand nand_12 (nand_12_out, B[3], B[3]);
endmodule

module ScreenController (
  input  [9:0] DATA,
  input  CLK,
  output [31:0] C,
  output [31:0] C_1,
  output [31:0] C_2,
  output [31:0] C_3,
  output [31:0] C_4,
  output [31:0] C_5,
  output [31:0] C_6,
  output [31:0] C_7,
  output [31:0] C_8,
  output [31:0] C_9,
  output [31:0] C_10,
  output [31:0] C_11,
  output [31:0] C_12,
  output [31:0] C_13,
  output [31:0] C_14,
  output [31:0] C_15,
  output [31:0] C_16,
  output [31:0] C_17,
  output [31:0] C_18,
  output [31:0] C_19,
  output [31:0] C_20,
  output [31:0] C_21,
  output [31:0] C_22,
  output [31:0] C_23,
  output [31:0] C_24,
  output [31:0] C_25,
  output [31:0] C_26,
  output [31:0] C_27,
  output [31:0] C_28,
  output [31:0] C_29,
  output [31:0] C_30,
  output [31:0] C_31,
  output [31:0] C_32,
  output [31:0] C_33,
  output [31:0] C_34,
  output [31:0] C_35,
  output [31:0] C_36,
  output [31:0] C_37,
  output [31:0] C_38,
  output [31:0] C_39,
  output [31:0] C_40,
  output [31:0] C_41,
  output [31:0] C_42,
  output [31:0] C_43,
  output [31:0] C_44,
  output [31:0] C_45,
  output [31:0] C_46,
  output [31:0] C_47,
  output [31:0] C_48,
  output [31:0] C_49,
  output [31:0] C_50,
  output [31:0] C_51,
  output [31:0] C_52,
  output [31:0] C_53,
  output [31:0] C_54,
  output [31:0] C_55,
  output [31:0] C_56,
  output [31:0] C_57,
  output [31:0] C_58,
  output [31:0] C_59,
  output [31:0] C_60,
  output [31:0] C_61,
  output [31:0] C_62,
  output [31:0] C_63
);

  wire decoder_1_out1, decoder_1_out2, decoder_1_out3;
  wire [1:0] ROW_BANK_q;
  wire [5:0] COLUMN_q;
  wire [31:0] screencolumnunit_1_o, screencolumnunit_2_o, screencolumnunit_3_o, screencolumnunit_4_o,
       screencolumnunit_5_o, screencolumnunit_6_o, screencolumnunit_7_o, screencolumnunit_8_o,
       screencolumnunit_9_o, screencolumnunit_10_o, screencolumnunit_11_o, screencolumnunit_12_o,
       screencolumnunit_13_o, screencolumnunit_14_o, screencolumnunit_15_o, screencolumnunit_16_o,
       screencolumnunit_17_o, screencolumnunit_18_o, screencolumnunit_19_o, screencolumnunit_20_o,
       screencolumnunit_21_o, screencolumnunit_22_o, screencolumnunit_23_o, screencolumnunit_24_o,
       screencolumnunit_25_o, screencolumnunit_26_o, screencolumnunit_27_o, screencolumnunit_28_o,
       screencolumnunit_29_o, screencolumnunit_30_o, screencolumnunit_31_o, screencolumnunit_32_o,
       screencolumnunit_33_o, screencolumnunit_34_o, screencolumnunit_35_o, screencolumnunit_36_o,
       screencolumnunit_37_o, screencolumnunit_38_o, screencolumnunit_39_o, screencolumnunit_40_o,
       screencolumnunit_41_o, screencolumnunit_42_o, screencolumnunit_43_o, screencolumnunit_44_o,
       screencolumnunit_45_o, screencolumnunit_46_o, screencolumnunit_47_o, screencolumnunit_48_o,
       screencolumnunit_49_o, screencolumnunit_50_o, screencolumnunit_51_o, screencolumnunit_52_o,
       screencolumnunit_53_o, screencolumnunit_54_o, screencolumnunit_55_o, screencolumnunit_56_o,
       screencolumnunit_57_o, screencolumnunit_58_o, screencolumnunit_59_o, screencolumnunit_60_o,
       screencolumnunit_61_o, screencolumnunit_62_o, screencolumnunit_63_o, screencolumnunit_64_o;
  wire [63:0] decoder64_1_o;

  Decoder #(.select(2)) decoder_1 (
    .out1(decoder_1_out1), .out2(decoder_1_out2), .out3(decoder_1_out3), .sel(DATA[9:8]), .en(1'b1));  // open: out0
  Register #(.trigger("high"), .width(6)) COLUMN (
    .D(DATA[5:0]), .en(decoder_1_out1), .clk(CLK), .Q(COLUMN_q), .clr(1'b0));
  Register #(.trigger("high"), .width(2)) ROW_BANK (
    .D(DATA[7:6]), .en(decoder_1_out1), .clk(CLK), .Q(ROW_BANK_q), .clr(1'b0));
  Decoder64 decoder64_1 (.in_1(COLUMN_q), .O(decoder64_1_o));
  ScreenColumnUnit screencolumnunit_1 (
    .RB_VALUE(DATA[7:0]), .ROW_BANK(ROW_BANK_q), .S(decoder64_1_o[0]), .WD(decoder_1_out2), .CLK(CLK),
    .O(screencolumnunit_1_o));
  ScreenColumnUnit screencolumnunit_2 (
    .RB_VALUE(DATA[7:0]), .ROW_BANK(ROW_BANK_q), .S(decoder64_1_o[1]), .WD(decoder_1_out2), .CLK(CLK),
    .O(screencolumnunit_2_o));
  ScreenColumnUnit screencolumnunit_3 (
    .RB_VALUE(DATA[7:0]), .ROW_BANK(ROW_BANK_q), .S(decoder64_1_o[2]), .WD(decoder_1_out2), .CLK(CLK),
    .O(screencolumnunit_3_o));
  ScreenColumnUnit screencolumnunit_4 (
    .RB_VALUE(DATA[7:0]), .ROW_BANK(ROW_BANK_q), .S(decoder64_1_o[3]), .WD(decoder_1_out2), .CLK(CLK),
    .O(screencolumnunit_4_o));
  ScreenColumnUnit screencolumnunit_5 (
    .RB_VALUE(DATA[7:0]), .ROW_BANK(ROW_BANK_q), .S(decoder64_1_o[4]), .WD(decoder_1_out2), .CLK(CLK),
    .O(screencolumnunit_5_o));
  ScreenColumnUnit screencolumnunit_6 (
    .RB_VALUE(DATA[7:0]), .ROW_BANK(ROW_BANK_q), .S(decoder64_1_o[5]), .WD(decoder_1_out2), .CLK(CLK),
    .O(screencolumnunit_6_o));
  ScreenColumnUnit screencolumnunit_7 (
    .RB_VALUE(DATA[7:0]), .ROW_BANK(ROW_BANK_q), .S(decoder64_1_o[6]), .WD(decoder_1_out2), .CLK(CLK),
    .O(screencolumnunit_7_o));
  ScreenColumnUnit screencolumnunit_8 (
    .RB_VALUE(DATA[7:0]), .ROW_BANK(ROW_BANK_q), .S(decoder64_1_o[7]), .WD(decoder_1_out2), .CLK(CLK),
    .O(screencolumnunit_8_o));
  ScreenColumnUnit screencolumnunit_9 (
    .RB_VALUE(DATA[7:0]), .ROW_BANK(ROW_BANK_q), .S(decoder64_1_o[8]), .WD(decoder_1_out2), .CLK(CLK),
    .O(screencolumnunit_9_o));
  ScreenColumnUnit screencolumnunit_10 (
    .RB_VALUE(DATA[7:0]), .ROW_BANK(ROW_BANK_q), .S(decoder64_1_o[9]), .WD(decoder_1_out2), .CLK(CLK),
    .O(screencolumnunit_10_o));
  ScreenColumnUnit screencolumnunit_11 (
    .RB_VALUE(DATA[7:0]), .ROW_BANK(ROW_BANK_q), .S(decoder64_1_o[10]), .WD(decoder_1_out2), .CLK(CLK),
    .O(screencolumnunit_11_o));
  ScreenColumnUnit screencolumnunit_12 (
    .RB_VALUE(DATA[7:0]), .ROW_BANK(ROW_BANK_q), .S(decoder64_1_o[11]), .WD(decoder_1_out2), .CLK(CLK),
    .O(screencolumnunit_12_o));
  ScreenColumnUnit screencolumnunit_13 (
    .RB_VALUE(DATA[7:0]), .ROW_BANK(ROW_BANK_q), .S(decoder64_1_o[12]), .WD(decoder_1_out2), .CLK(CLK),
    .O(screencolumnunit_13_o));
  ScreenColumnUnit screencolumnunit_14 (
    .RB_VALUE(DATA[7:0]), .ROW_BANK(ROW_BANK_q), .S(decoder64_1_o[13]), .WD(decoder_1_out2), .CLK(CLK),
    .O(screencolumnunit_14_o));
  ScreenColumnUnit screencolumnunit_15 (
    .RB_VALUE(DATA[7:0]), .ROW_BANK(ROW_BANK_q), .S(decoder64_1_o[14]), .WD(decoder_1_out2), .CLK(CLK),
    .O(screencolumnunit_15_o));
  ScreenColumnUnit screencolumnunit_16 (
    .RB_VALUE(DATA[7:0]), .ROW_BANK(ROW_BANK_q), .S(decoder64_1_o[15]), .WD(decoder_1_out2), .CLK(CLK),
    .O(screencolumnunit_16_o));
  ScreenColumnUnit screencolumnunit_17 (
    .RB_VALUE(DATA[7:0]), .ROW_BANK(ROW_BANK_q), .S(decoder64_1_o[16]), .WD(decoder_1_out2), .CLK(CLK),
    .O(screencolumnunit_17_o));
  ScreenColumnUnit screencolumnunit_18 (
    .RB_VALUE(DATA[7:0]), .ROW_BANK(ROW_BANK_q), .S(decoder64_1_o[17]), .WD(decoder_1_out2), .CLK(CLK),
    .O(screencolumnunit_18_o));
  ScreenColumnUnit screencolumnunit_19 (
    .RB_VALUE(DATA[7:0]), .ROW_BANK(ROW_BANK_q), .S(decoder64_1_o[18]), .WD(decoder_1_out2), .CLK(CLK),
    .O(screencolumnunit_19_o));
  ScreenColumnUnit screencolumnunit_20 (
    .RB_VALUE(DATA[7:0]), .ROW_BANK(ROW_BANK_q), .S(decoder64_1_o[19]), .WD(decoder_1_out2), .CLK(CLK),
    .O(screencolumnunit_20_o));
  ScreenColumnUnit screencolumnunit_21 (
    .RB_VALUE(DATA[7:0]), .ROW_BANK(ROW_BANK_q), .S(decoder64_1_o[20]), .WD(decoder_1_out2), .CLK(CLK),
    .O(screencolumnunit_21_o));
  ScreenColumnUnit screencolumnunit_22 (
    .RB_VALUE(DATA[7:0]), .ROW_BANK(ROW_BANK_q), .S(decoder64_1_o[21]), .WD(decoder_1_out2), .CLK(CLK),
    .O(screencolumnunit_22_o));
  ScreenColumnUnit screencolumnunit_23 (
    .RB_VALUE(DATA[7:0]), .ROW_BANK(ROW_BANK_q), .S(decoder64_1_o[22]), .WD(decoder_1_out2), .CLK(CLK),
    .O(screencolumnunit_23_o));
  ScreenColumnUnit screencolumnunit_24 (
    .RB_VALUE(DATA[7:0]), .ROW_BANK(ROW_BANK_q), .S(decoder64_1_o[23]), .WD(decoder_1_out2), .CLK(CLK),
    .O(screencolumnunit_24_o));
  ScreenColumnUnit screencolumnunit_25 (
    .RB_VALUE(DATA[7:0]), .ROW_BANK(ROW_BANK_q), .S(decoder64_1_o[24]), .WD(decoder_1_out2), .CLK(CLK),
    .O(screencolumnunit_25_o));
  ScreenColumnUnit screencolumnunit_26 (
    .RB_VALUE(DATA[7:0]), .ROW_BANK(ROW_BANK_q), .S(decoder64_1_o[25]), .WD(decoder_1_out2), .CLK(CLK),
    .O(screencolumnunit_26_o));
  ScreenColumnUnit screencolumnunit_27 (
    .RB_VALUE(DATA[7:0]), .ROW_BANK(ROW_BANK_q), .S(decoder64_1_o[26]), .WD(decoder_1_out2), .CLK(CLK),
    .O(screencolumnunit_27_o));
  ScreenColumnUnit screencolumnunit_28 (
    .RB_VALUE(DATA[7:0]), .ROW_BANK(ROW_BANK_q), .S(decoder64_1_o[27]), .WD(decoder_1_out2), .CLK(CLK),
    .O(screencolumnunit_28_o));
  ScreenColumnUnit screencolumnunit_29 (
    .RB_VALUE(DATA[7:0]), .ROW_BANK(ROW_BANK_q), .S(decoder64_1_o[28]), .WD(decoder_1_out2), .CLK(CLK),
    .O(screencolumnunit_29_o));
  ScreenColumnUnit screencolumnunit_30 (
    .RB_VALUE(DATA[7:0]), .ROW_BANK(ROW_BANK_q), .S(decoder64_1_o[29]), .WD(decoder_1_out2), .CLK(CLK),
    .O(screencolumnunit_30_o));
  ScreenColumnUnit screencolumnunit_31 (
    .RB_VALUE(DATA[7:0]), .ROW_BANK(ROW_BANK_q), .S(decoder64_1_o[30]), .WD(decoder_1_out2), .CLK(CLK),
    .O(screencolumnunit_31_o));
  ScreenColumnUnit screencolumnunit_32 (
    .RB_VALUE(DATA[7:0]), .ROW_BANK(ROW_BANK_q), .S(decoder64_1_o[31]), .WD(decoder_1_out2), .CLK(CLK),
    .O(screencolumnunit_32_o));
  ScreenColumnUnit screencolumnunit_33 (
    .RB_VALUE(DATA[7:0]), .ROW_BANK(ROW_BANK_q), .S(decoder64_1_o[32]), .WD(decoder_1_out2), .CLK(CLK),
    .O(screencolumnunit_33_o));
  ScreenColumnUnit screencolumnunit_34 (
    .RB_VALUE(DATA[7:0]), .ROW_BANK(ROW_BANK_q), .S(decoder64_1_o[33]), .WD(decoder_1_out2), .CLK(CLK),
    .O(screencolumnunit_34_o));
  ScreenColumnUnit screencolumnunit_35 (
    .RB_VALUE(DATA[7:0]), .ROW_BANK(ROW_BANK_q), .S(decoder64_1_o[34]), .WD(decoder_1_out2), .CLK(CLK),
    .O(screencolumnunit_35_o));
  ScreenColumnUnit screencolumnunit_36 (
    .RB_VALUE(DATA[7:0]), .ROW_BANK(ROW_BANK_q), .S(decoder64_1_o[35]), .WD(decoder_1_out2), .CLK(CLK),
    .O(screencolumnunit_36_o));
  ScreenColumnUnit screencolumnunit_37 (
    .RB_VALUE(DATA[7:0]), .ROW_BANK(ROW_BANK_q), .S(decoder64_1_o[36]), .WD(decoder_1_out2), .CLK(CLK),
    .O(screencolumnunit_37_o));
  ScreenColumnUnit screencolumnunit_38 (
    .RB_VALUE(DATA[7:0]), .ROW_BANK(ROW_BANK_q), .S(decoder64_1_o[37]), .WD(decoder_1_out2), .CLK(CLK),
    .O(screencolumnunit_38_o));
  ScreenColumnUnit screencolumnunit_39 (
    .RB_VALUE(DATA[7:0]), .ROW_BANK(ROW_BANK_q), .S(decoder64_1_o[38]), .WD(decoder_1_out2), .CLK(CLK),
    .O(screencolumnunit_39_o));
  ScreenColumnUnit screencolumnunit_40 (
    .RB_VALUE(DATA[7:0]), .ROW_BANK(ROW_BANK_q), .S(decoder64_1_o[39]), .WD(decoder_1_out2), .CLK(CLK),
    .O(screencolumnunit_40_o));
  ScreenColumnUnit screencolumnunit_41 (
    .RB_VALUE(DATA[7:0]), .ROW_BANK(ROW_BANK_q), .S(decoder64_1_o[40]), .WD(decoder_1_out2), .CLK(CLK),
    .O(screencolumnunit_41_o));
  ScreenColumnUnit screencolumnunit_42 (
    .RB_VALUE(DATA[7:0]), .ROW_BANK(ROW_BANK_q), .S(decoder64_1_o[41]), .WD(decoder_1_out2), .CLK(CLK),
    .O(screencolumnunit_42_o));
  ScreenColumnUnit screencolumnunit_43 (
    .RB_VALUE(DATA[7:0]), .ROW_BANK(ROW_BANK_q), .S(decoder64_1_o[42]), .WD(decoder_1_out2), .CLK(CLK),
    .O(screencolumnunit_43_o));
  ScreenColumnUnit screencolumnunit_44 (
    .RB_VALUE(DATA[7:0]), .ROW_BANK(ROW_BANK_q), .S(decoder64_1_o[43]), .WD(decoder_1_out2), .CLK(CLK),
    .O(screencolumnunit_44_o));
  ScreenColumnUnit screencolumnunit_45 (
    .RB_VALUE(DATA[7:0]), .ROW_BANK(ROW_BANK_q), .S(decoder64_1_o[44]), .WD(decoder_1_out2), .CLK(CLK),
    .O(screencolumnunit_45_o));
  ScreenColumnUnit screencolumnunit_46 (
    .RB_VALUE(DATA[7:0]), .ROW_BANK(ROW_BANK_q), .S(decoder64_1_o[45]), .WD(decoder_1_out2), .CLK(CLK),
    .O(screencolumnunit_46_o));
  ScreenColumnUnit screencolumnunit_47 (
    .RB_VALUE(DATA[7:0]), .ROW_BANK(ROW_BANK_q), .S(decoder64_1_o[46]), .WD(decoder_1_out2), .CLK(CLK),
    .O(screencolumnunit_47_o));
  ScreenColumnUnit screencolumnunit_48 (
    .RB_VALUE(DATA[7:0]), .ROW_BANK(ROW_BANK_q), .S(decoder64_1_o[47]), .WD(decoder_1_out2), .CLK(CLK),
    .O(screencolumnunit_48_o));
  ScreenColumnUnit screencolumnunit_49 (
    .RB_VALUE(DATA[7:0]), .ROW_BANK(ROW_BANK_q), .S(decoder64_1_o[48]), .WD(decoder_1_out2), .CLK(CLK),
    .O(screencolumnunit_49_o));
  ScreenColumnUnit screencolumnunit_50 (
    .RB_VALUE(DATA[7:0]), .ROW_BANK(ROW_BANK_q), .S(decoder64_1_o[49]), .WD(decoder_1_out2), .CLK(CLK),
    .O(screencolumnunit_50_o));
  ScreenColumnUnit screencolumnunit_51 (
    .RB_VALUE(DATA[7:0]), .ROW_BANK(ROW_BANK_q), .S(decoder64_1_o[50]), .WD(decoder_1_out2), .CLK(CLK),
    .O(screencolumnunit_51_o));
  ScreenColumnUnit screencolumnunit_52 (
    .RB_VALUE(DATA[7:0]), .ROW_BANK(ROW_BANK_q), .S(decoder64_1_o[51]), .WD(decoder_1_out2), .CLK(CLK),
    .O(screencolumnunit_52_o));
  ScreenColumnUnit screencolumnunit_53 (
    .RB_VALUE(DATA[7:0]), .ROW_BANK(ROW_BANK_q), .S(decoder64_1_o[52]), .WD(decoder_1_out2), .CLK(CLK),
    .O(screencolumnunit_53_o));
  ScreenColumnUnit screencolumnunit_54 (
    .RB_VALUE(DATA[7:0]), .ROW_BANK(ROW_BANK_q), .S(decoder64_1_o[53]), .WD(decoder_1_out2), .CLK(CLK),
    .O(screencolumnunit_54_o));
  ScreenColumnUnit screencolumnunit_55 (
    .RB_VALUE(DATA[7:0]), .ROW_BANK(ROW_BANK_q), .S(decoder64_1_o[54]), .WD(decoder_1_out2), .CLK(CLK),
    .O(screencolumnunit_55_o));
  ScreenColumnUnit screencolumnunit_56 (
    .RB_VALUE(DATA[7:0]), .ROW_BANK(ROW_BANK_q), .S(decoder64_1_o[55]), .WD(decoder_1_out2), .CLK(CLK),
    .O(screencolumnunit_56_o));
  ScreenColumnUnit screencolumnunit_57 (
    .RB_VALUE(DATA[7:0]), .ROW_BANK(ROW_BANK_q), .S(decoder64_1_o[56]), .WD(decoder_1_out2), .CLK(CLK),
    .O(screencolumnunit_57_o));
  ScreenColumnUnit screencolumnunit_58 (
    .RB_VALUE(DATA[7:0]), .ROW_BANK(ROW_BANK_q), .S(decoder64_1_o[57]), .WD(decoder_1_out2), .CLK(CLK),
    .O(screencolumnunit_58_o));
  ScreenColumnUnit screencolumnunit_59 (
    .RB_VALUE(DATA[7:0]), .ROW_BANK(ROW_BANK_q), .S(decoder64_1_o[58]), .WD(decoder_1_out2), .CLK(CLK),
    .O(screencolumnunit_59_o));
  ScreenColumnUnit screencolumnunit_60 (
    .RB_VALUE(DATA[7:0]), .ROW_BANK(ROW_BANK_q), .S(decoder64_1_o[59]), .WD(decoder_1_out2), .CLK(CLK),
    .O(screencolumnunit_60_o));
  ScreenColumnUnit screencolumnunit_61 (
    .RB_VALUE(DATA[7:0]), .ROW_BANK(ROW_BANK_q), .S(decoder64_1_o[60]), .WD(decoder_1_out2), .CLK(CLK),
    .O(screencolumnunit_61_o));
  ScreenColumnUnit screencolumnunit_62 (
    .RB_VALUE(DATA[7:0]), .ROW_BANK(ROW_BANK_q), .S(decoder64_1_o[61]), .WD(decoder_1_out2), .CLK(CLK),
    .O(screencolumnunit_62_o));
  ScreenColumnUnit screencolumnunit_63 (
    .RB_VALUE(DATA[7:0]), .ROW_BANK(ROW_BANK_q), .S(decoder64_1_o[62]), .WD(decoder_1_out2), .CLK(CLK),
    .O(screencolumnunit_63_o));
  ScreenColumnUnit screencolumnunit_64 (
    .RB_VALUE(DATA[7:0]), .ROW_BANK(ROW_BANK_q), .S(decoder64_1_o[63]), .WD(decoder_1_out2), .CLK(CLK),
    .O(screencolumnunit_64_o));
  Register #(.trigger("high"), .width(32)) register_1 (
    .D(screencolumnunit_1_o), .en(decoder_1_out3), .clk(CLK), .Q(C));  // open: clr
  Register #(.trigger("high"), .width(32)) register_2 (
    .D(screencolumnunit_2_o), .en(decoder_1_out3), .clk(CLK), .Q(C_1));  // open: clr
  Register #(.trigger("high"), .width(32)) register_3 (
    .D(screencolumnunit_3_o), .en(decoder_1_out3), .clk(CLK), .Q(C_2));  // open: clr
  Register #(.trigger("high"), .width(32)) register_4 (
    .D(screencolumnunit_4_o), .en(decoder_1_out3), .clk(CLK), .Q(C_3));  // open: clr
  Register #(.trigger("high"), .width(32)) register_5 (
    .D(screencolumnunit_5_o), .en(decoder_1_out3), .clk(CLK), .Q(C_4));  // open: clr
  Register #(.trigger("high"), .width(32)) register_6 (
    .D(screencolumnunit_6_o), .en(decoder_1_out3), .clk(CLK), .Q(C_5));  // open: clr
  Register #(.trigger("high"), .width(32)) register_7 (
    .D(screencolumnunit_7_o), .en(decoder_1_out3), .clk(CLK), .Q(C_6));  // open: clr
  Register #(.trigger("high"), .width(32)) register_8 (
    .D(screencolumnunit_8_o), .en(decoder_1_out3), .clk(CLK), .Q(C_7));  // open: clr
  Register #(.trigger("high"), .width(32)) register_9 (
    .D(screencolumnunit_9_o), .en(decoder_1_out3), .clk(CLK), .Q(C_8));  // open: clr
  Register #(.trigger("high"), .width(32)) register_10 (
    .D(screencolumnunit_10_o), .en(decoder_1_out3), .clk(CLK), .Q(C_9));  // open: clr
  Register #(.trigger("high"), .width(32)) register_11 (
    .D(screencolumnunit_11_o), .en(decoder_1_out3), .clk(CLK), .Q(C_10));  // open: clr
  Register #(.trigger("high"), .width(32)) register_12 (
    .D(screencolumnunit_12_o), .en(decoder_1_out3), .clk(CLK), .Q(C_11));  // open: clr
  Register #(.trigger("high"), .width(32)) register_13 (
    .D(screencolumnunit_13_o), .en(decoder_1_out3), .clk(CLK), .Q(C_12));  // open: clr
  Register #(.trigger("high"), .width(32)) register_14 (
    .D(screencolumnunit_14_o), .en(decoder_1_out3), .clk(CLK), .Q(C_13));  // open: clr
  Register #(.trigger("high"), .width(32)) register_15 (
    .D(screencolumnunit_15_o), .en(decoder_1_out3), .clk(CLK), .Q(C_14));  // open: clr
  Register #(.trigger("high"), .width(32)) register_16 (
    .D(screencolumnunit_16_o), .en(decoder_1_out3), .clk(CLK), .Q(C_15));  // open: clr
  Register #(.trigger("high"), .width(32)) register_17 (
    .D(screencolumnunit_17_o), .en(decoder_1_out3), .clk(CLK), .Q(C_16));  // open: clr
  Register #(.trigger("high"), .width(32)) register_18 (
    .D(screencolumnunit_18_o), .en(decoder_1_out3), .clk(CLK), .Q(C_17));  // open: clr
  Register #(.trigger("high"), .width(32)) register_19 (
    .D(screencolumnunit_19_o), .en(decoder_1_out3), .clk(CLK), .Q(C_18));  // open: clr
  Register #(.trigger("high"), .width(32)) register_20 (
    .D(screencolumnunit_20_o), .en(decoder_1_out3), .clk(CLK), .Q(C_19));  // open: clr
  Register #(.trigger("high"), .width(32)) register_21 (
    .D(screencolumnunit_21_o), .en(decoder_1_out3), .clk(CLK), .Q(C_20));  // open: clr
  Register #(.trigger("high"), .width(32)) register_22 (
    .D(screencolumnunit_22_o), .en(decoder_1_out3), .clk(CLK), .Q(C_21));  // open: clr
  Register #(.trigger("high"), .width(32)) register_23 (
    .D(screencolumnunit_23_o), .en(decoder_1_out3), .clk(CLK), .Q(C_22));  // open: clr
  Register #(.trigger("high"), .width(32)) register_24 (
    .D(screencolumnunit_24_o), .en(decoder_1_out3), .clk(CLK), .Q(C_23));  // open: clr
  Register #(.trigger("high"), .width(32)) register_25 (
    .D(screencolumnunit_25_o), .en(decoder_1_out3), .clk(CLK), .Q(C_24));  // open: clr
  Register #(.trigger("high"), .width(32)) register_26 (
    .D(screencolumnunit_26_o), .en(decoder_1_out3), .clk(CLK), .Q(C_25));  // open: clr
  Register #(.trigger("high"), .width(32)) register_27 (
    .D(screencolumnunit_27_o), .en(decoder_1_out3), .clk(CLK), .Q(C_26));  // open: clr
  Register #(.trigger("high"), .width(32)) register_28 (
    .D(screencolumnunit_28_o), .en(decoder_1_out3), .clk(CLK), .Q(C_27));  // open: clr
  Register #(.trigger("high"), .width(32)) register_29 (
    .D(screencolumnunit_29_o), .en(decoder_1_out3), .clk(CLK), .Q(C_28));  // open: clr
  Register #(.trigger("high"), .width(32)) register_30 (
    .D(screencolumnunit_30_o), .en(decoder_1_out3), .clk(CLK), .Q(C_29));  // open: clr
  Register #(.trigger("high"), .width(32)) register_31 (
    .D(screencolumnunit_31_o), .en(decoder_1_out3), .clk(CLK), .Q(C_30));  // open: clr
  Register #(.trigger("high"), .width(32)) register_32 (
    .D(screencolumnunit_32_o), .en(decoder_1_out3), .clk(CLK), .Q(C_31));  // open: clr
  Register #(.trigger("high"), .width(32)) register_33 (
    .D(screencolumnunit_33_o), .en(decoder_1_out3), .clk(CLK), .Q(C_32));  // open: clr
  Register #(.trigger("high"), .width(32)) register_34 (
    .D(screencolumnunit_34_o), .en(decoder_1_out3), .clk(CLK), .Q(C_33));  // open: clr
  Register #(.trigger("high"), .width(32)) register_35 (
    .D(screencolumnunit_35_o), .en(decoder_1_out3), .clk(CLK), .Q(C_34));  // open: clr
  Register #(.trigger("high"), .width(32)) register_36 (
    .D(screencolumnunit_36_o), .en(decoder_1_out3), .clk(CLK), .Q(C_35));  // open: clr
  Register #(.trigger("high"), .width(32)) register_37 (
    .D(screencolumnunit_37_o), .en(decoder_1_out3), .clk(CLK), .Q(C_36));  // open: clr
  Register #(.trigger("high"), .width(32)) register_38 (
    .D(screencolumnunit_38_o), .en(decoder_1_out3), .clk(CLK), .Q(C_37));  // open: clr
  Register #(.trigger("high"), .width(32)) register_39 (
    .D(screencolumnunit_39_o), .en(decoder_1_out3), .clk(CLK), .Q(C_38));  // open: clr
  Register #(.trigger("high"), .width(32)) register_40 (
    .D(screencolumnunit_40_o), .en(decoder_1_out3), .clk(CLK), .Q(C_39));  // open: clr
  Register #(.trigger("high"), .width(32)) register_41 (
    .D(screencolumnunit_41_o), .en(decoder_1_out3), .clk(CLK), .Q(C_40));  // open: clr
  Register #(.trigger("high"), .width(32)) register_42 (
    .D(screencolumnunit_42_o), .en(decoder_1_out3), .clk(CLK), .Q(C_41));  // open: clr
  Register #(.trigger("high"), .width(32)) register_43 (
    .D(screencolumnunit_43_o), .en(decoder_1_out3), .clk(CLK), .Q(C_42));  // open: clr
  Register #(.trigger("high"), .width(32)) register_44 (
    .D(screencolumnunit_44_o), .en(decoder_1_out3), .clk(CLK), .Q(C_43));  // open: clr
  Register #(.trigger("high"), .width(32)) register_45 (
    .D(screencolumnunit_45_o), .en(decoder_1_out3), .clk(CLK), .Q(C_44));  // open: clr
  Register #(.trigger("high"), .width(32)) register_46 (
    .D(screencolumnunit_46_o), .en(decoder_1_out3), .clk(CLK), .Q(C_45));  // open: clr
  Register #(.trigger("high"), .width(32)) register_47 (
    .D(screencolumnunit_47_o), .en(decoder_1_out3), .clk(CLK), .Q(C_46));  // open: clr
  Register #(.trigger("high"), .width(32)) register_48 (
    .D(screencolumnunit_48_o), .en(decoder_1_out3), .clk(CLK), .Q(C_47));  // open: clr
  Register #(.trigger("high"), .width(32)) register_49 (
    .D(screencolumnunit_49_o), .en(decoder_1_out3), .clk(CLK), .Q(C_48));  // open: clr
  Register #(.trigger("high"), .width(32)) register_50 (
    .D(screencolumnunit_50_o), .en(decoder_1_out3), .clk(CLK), .Q(C_49));  // open: clr
  Register #(.trigger("high"), .width(32)) register_51 (
    .D(screencolumnunit_51_o), .en(decoder_1_out3), .clk(CLK), .Q(C_50));  // open: clr
  Register #(.trigger("high"), .width(32)) register_52 (
    .D(screencolumnunit_52_o), .en(decoder_1_out3), .clk(CLK), .Q(C_51));  // open: clr
  Register #(.trigger("high"), .width(32)) register_53 (
    .D(screencolumnunit_53_o), .en(decoder_1_out3), .clk(CLK), .Q(C_52));  // open: clr
  Register #(.trigger("high"), .width(32)) register_54 (
    .D(screencolumnunit_54_o), .en(decoder_1_out3), .clk(CLK), .Q(C_53));  // open: clr
  Register #(.trigger("high"), .width(32)) register_55 (
    .D(screencolumnunit_55_o), .en(decoder_1_out3), .clk(CLK), .Q(C_54));  // open: clr
  Register #(.trigger("high"), .width(32)) register_56 (
    .D(screencolumnunit_56_o), .en(decoder_1_out3), .clk(CLK), .Q(C_55));  // open: clr
  Register #(.trigger("high"), .width(32)) register_57 (
    .D(screencolumnunit_57_o), .en(decoder_1_out3), .clk(CLK), .Q(C_56));  // open: clr
  Register #(.trigger("high"), .width(32)) register_58 (
    .D(screencolumnunit_58_o), .en(decoder_1_out3), .clk(CLK), .Q(C_57));  // open: clr
  Register #(.trigger("high"), .width(32)) register_59 (
    .D(screencolumnunit_59_o), .en(decoder_1_out3), .clk(CLK), .Q(C_58));  // open: clr
  Register #(.trigger("high"), .width(32)) register_60 (
    .D(screencolumnunit_60_o), .en(decoder_1_out3), .clk(CLK), .Q(C_59));  // open: clr
  Register #(.trigger("high"), .width(32)) register_61 (
    .D(screencolumnunit_61_o), .en(decoder_1_out3), .clk(CLK), .Q(C_60));  // open: clr
  Register #(.trigger("high"), .width(32)) register_62 (
    .D(screencolumnunit_62_o), .en(decoder_1_out3), .clk(CLK), .Q(C_61));  // open: clr
  Register #(.trigger("high"), .width(32)) register_63 (
    .D(screencolumnunit_63_o), .en(decoder_1_out3), .clk(CLK), .Q(C_62));  // open: clr
  Register #(.trigger("high"), .width(32)) register_64 (
    .D(screencolumnunit_64_o), .en(decoder_1_out3), .clk(CLK), .Q(C_63));  // open: clr
endmodule

module ScreenColumnUnit (
  input  [7:0] RB_VALUE,
  input  [1:0] ROW_BANK,
  input  S,
  input  WD,
  input  CLK,
  output [31:0] O
);

  wire nand_1_out, nand_2_out;
  wire [3:0] decoder_1_out0;
  wire [7:0] multiplexer_1_out, multiplexer_2_out, multiplexer_3_out, multiplexer_4_out;

  Decoder #(.select(2)) decoder_1 (
    .out0(decoder_1_out0[0]), .out1(decoder_1_out0[1]), .out2(decoder_1_out0[2]), .out3(decoder_1_out0[3]),
    .sel(ROW_BANK), .en(1'b1));
  nand nand_1 (nand_1_out, S, WD);
  Multiplexer #(.width(8)) multiplexer_1 (
    .in0(O[7:0]), .in1(RB_VALUE), .out(multiplexer_1_out), .sel(decoder_1_out0[0]));
  Multiplexer #(.width(8)) multiplexer_2 (
    .in0(O[15:8]), .in1(RB_VALUE), .out(multiplexer_2_out), .sel(decoder_1_out0[1]));
  Multiplexer #(.width(8)) multiplexer_3 (
    .in0(O[23:16]), .in1(RB_VALUE), .out(multiplexer_3_out), .sel(decoder_1_out0[2]));
  Multiplexer #(.width(8)) multiplexer_4 (
    .in0(O[31:24]), .in1(RB_VALUE), .out(multiplexer_4_out), .sel(decoder_1_out0[3]));
  nand nand_2 (nand_2_out, nand_1_out, nand_1_out);
  Register #(.trigger("high"), .width(32)) register_1 (
    .D({multiplexer_4_out, multiplexer_3_out, multiplexer_2_out, multiplexer_1_out}), .en(nand_2_out),
    .clk(CLK), .Q(O), .clr(1'b0));
endmodule

module Decoder64 (
  input  [5:0] in_1,
  output [63:0] O
);

  wire nand_1_out;

  nand nand_1 (nand_1_out, in_1[5], in_1[5]);
  Decoder #(.select(5)) decoder_1 (
    .out0(O[0]), .out1(O[1]), .out2(O[2]), .out3(O[3]), .out4(O[4]), .out5(O[5]), .out6(O[6]), .out7(O[7]),
    .out8(O[8]), .out9(O[9]), .out10(O[10]), .out11(O[11]), .out12(O[12]), .out13(O[13]), .out14(O[14]),
    .out15(O[15]), .out16(O[16]), .out17(O[17]), .out18(O[18]), .out19(O[19]), .out20(O[20]), .out21(O[21]),
    .out22(O[22]), .out23(O[23]), .out24(O[24]), .out25(O[25]), .out26(O[26]), .out27(O[27]), .out28(O[28]),
    .out29(O[29]), .out30(O[30]), .out31(O[31]), .sel(in_1[4:0]), .en(nand_1_out));
  Decoder #(.select(5)) decoder_2 (
    .out0(O[32]), .out1(O[33]), .out2(O[34]), .out3(O[35]), .out4(O[36]), .out5(O[37]), .out6(O[38]),
    .out7(O[39]), .out8(O[40]), .out9(O[41]), .out10(O[42]), .out11(O[43]), .out12(O[44]), .out13(O[45]),
    .out14(O[46]), .out15(O[47]), .out16(O[48]), .out17(O[49]), .out18(O[50]), .out19(O[51]), .out20(O[52]),
    .out21(O[53]), .out22(O[54]), .out23(O[55]), .out24(O[56]), .out25(O[57]), .out26(O[58]), .out27(O[59]),
    .out28(O[60]), .out29(O[61]), .out30(O[62]), .out31(O[63]), .sel(in_1[4:0]), .en(in_1[5]));
endmodule
module SyncCounterNew (
  input  SB,
  input  CLK,
  input  ENABLE,
  input  L,
  input  [19:0] I,
  output [19:0] O
);

  wire mux2to1_1_o, mux2to1_2_o, mux2to1_3_o, mux2to1_4_o, mux2to1_5_o, mux2to1_6_o, mux2to1_7_o,
       mux2to1_8_o, mux2to1_9_o, mux2to1_10_o, mux2to1_11_o, mux2to1_12_o, mux2to1_13_o, mux2to1_14_o,
       mux2to1_15_o, mux2to1_16_o, mux2to1_17_o, mux2to1_18_o, mux2to1_19_o, mux2to1_20_o, mux2to1_21_o,
       mux2to1_22_o, mux2to1_23_o, mux2to1_24_o, mux2to1_25_o, mux2to1_26_o, mux2to1_27_o, mux2to1_28_o,
       mux2to1_29_o, mux2to1_30_o, mux2to1_31_o, mux2to1_32_o, mux2to1_33_o, mux2to1_34_o, mux2to1_35_o,
       mux2to1_36_o, mux2to1_37_o, mux2to1_38_o, mux2to1_39_o, mux2to1_40_o, nand_1_out, nand_2_out,
       nand_3_out, nand_4_out, nand_5_out, nand_6_out, nand_7_out, nand_8_out, nand_9_out, nand_10_out,
       nand_11_out, nand_12_out, nand_13_out, nand_14_out, nand_15_out, nand_16_out, nand_17_out,
       nand_18_out, nand_19_out, nand_20_out, nand_21_out, nand_22_out, nand_23_out, nand_24_out,
       nand_25_out, nand_26_out, nand_27_out, nand_28_out, nand_29_out, nand_30_out, nand_31_out,
       nand_32_out, nand_33_out, nand_34_out, nand_35_out, nand_36_out, nand_37_out, nand_38_out,
       nand_39_out, nand_40_out, nand_41_out, nand_42_out, nand_43_out, nand_44_out, nand_45_out,
       nand_46_out, nand_47_out, nand_48_out, nand_49_out, nand_50_out, nand_51_out, nand_52_out,
       nand_53_out, nand_54_out, nand_55_out, nand_56_out, nand_57_out, nand_58_out;

  nand nand_1 (nand_1_out, CLK, ENABLE);
  nand nand_2 (nand_2_out, nand_1_out, nand_1_out);
  nand nand_3 (nand_3_out, I[0], I[0]);
  Mux2To1 mux2to1_1 (.A(1'b1), .B(I[0]), .S(L), .O(mux2to1_1_o));
  Mux2To1 mux2to1_2 (.A(1'b1), .B(nand_3_out), .S(L), .O(mux2to1_2_o));
  JKFlipFlop jkflipflop_1 (.SB(SB), .J(mux2to1_1_o), .CLK(nand_2_out), .K(mux2to1_2_o), .O(O[0]));  // open: OC
  nand nand_4 (nand_4_out, I[1], I[1]);
  Mux2To1 mux2to1_3 (.A(O[0]), .B(I[1]), .S(L), .O(mux2to1_3_o));
  Mux2To1 mux2to1_4 (.A(O[0]), .B(nand_4_out), .S(L), .O(mux2to1_4_o));
  JKFlipFlop jkflipflop_2 (.SB(SB), .J(mux2to1_3_o), .CLK(nand_2_out), .K(mux2to1_4_o), .O(O[1]));  // open: OC
  nand nand_5 (nand_5_out, O[0], O[1]);
  nand nand_6 (nand_6_out, nand_5_out, nand_5_out);
  nand nand_7 (nand_7_out, I[2], I[2]);
  Mux2To1 mux2to1_5 (.A(nand_6_out), .B(I[2]), .S(L), .O(mux2to1_5_o));
  Mux2To1 mux2to1_6 (.A(nand_6_out), .B(nand_7_out), .S(L), .O(mux2to1_6_o));
  JKFlipFlop jkflipflop_3 (.SB(SB), .J(mux2to1_5_o), .CLK(nand_2_out), .K(mux2to1_6_o), .O(O[2]));  // open: OC
  nand nand_8 (nand_8_out, nand_6_out, O[2]);
  nand nand_9 (nand_9_out, nand_8_out, nand_8_out);
  nand nand_10 (nand_10_out, I[3], I[3]);
  Mux2To1 mux2to1_7 (.A(nand_9_out), .B(I[3]), .S(L), .O(mux2to1_7_o));
  Mux2To1 mux2to1_8 (.A(nand_9_out), .B(nand_10_out), .S(L), .O(mux2to1_8_o));
  JKFlipFlop jkflipflop_4 (.SB(SB), .J(mux2to1_7_o), .CLK(nand_2_out), .K(mux2to1_8_o), .O(O[3]));  // open: OC
  nand nand_11 (nand_11_out, nand_9_out, O[3]);
  nand nand_12 (nand_12_out, nand_11_out, nand_11_out);
  nand nand_13 (nand_13_out, I[4], I[4]);
  Mux2To1 mux2to1_9 (.A(nand_12_out), .B(I[4]), .S(L), .O(mux2to1_9_o));
  Mux2To1 mux2to1_10 (.A(nand_12_out), .B(nand_13_out), .S(L), .O(mux2to1_10_o));
  JKFlipFlop jkflipflop_5 (.SB(SB), .J(mux2to1_9_o), .CLK(nand_2_out), .K(mux2to1_10_o), .O(O[4]));  // open: OC
  nand nand_14 (nand_14_out, nand_12_out, O[4]);
  nand nand_15 (nand_15_out, nand_14_out, nand_14_out);
  nand nand_16 (nand_16_out, I[5], I[5]);
  Mux2To1 mux2to1_11 (.A(nand_15_out), .B(I[5]), .S(L), .O(mux2to1_11_o));
  Mux2To1 mux2to1_12 (.A(nand_15_out), .B(nand_16_out), .S(L), .O(mux2to1_12_o));
  JKFlipFlop jkflipflop_6 (.SB(SB), .J(mux2to1_11_o), .CLK(nand_2_out), .K(mux2to1_12_o), .O(O[5]));  // open: OC
  nand nand_17 (nand_17_out, nand_15_out, O[5]);
  nand nand_18 (nand_18_out, nand_17_out, nand_17_out);
  nand nand_19 (nand_19_out, I[6], I[6]);
  Mux2To1 mux2to1_13 (.A(nand_18_out), .B(I[6]), .S(L), .O(mux2to1_13_o));
  Mux2To1 mux2to1_14 (.A(nand_18_out), .B(nand_19_out), .S(L), .O(mux2to1_14_o));
  JKFlipFlop jkflipflop_7 (.SB(SB), .J(mux2to1_13_o), .CLK(nand_2_out), .K(mux2to1_14_o), .O(O[6]));  // open: OC
  nand nand_20 (nand_20_out, nand_18_out, O[6]);
  nand nand_21 (nand_21_out, nand_20_out, nand_20_out);
  nand nand_22 (nand_22_out, I[7], I[7]);
  Mux2To1 mux2to1_15 (.A(nand_21_out), .B(I[7]), .S(L), .O(mux2to1_15_o));
  Mux2To1 mux2to1_16 (.A(nand_21_out), .B(nand_22_out), .S(L), .O(mux2to1_16_o));
  JKFlipFlop jkflipflop_8 (.SB(SB), .J(mux2to1_15_o), .CLK(nand_2_out), .K(mux2to1_16_o), .O(O[7]));  // open: OC
  nand nand_23 (nand_23_out, nand_21_out, O[7]);
  nand nand_24 (nand_24_out, nand_23_out, nand_23_out);
  nand nand_25 (nand_25_out, I[8], I[8]);
  Mux2To1 mux2to1_17 (.A(nand_24_out), .B(I[8]), .S(L), .O(mux2to1_17_o));
  Mux2To1 mux2to1_18 (.A(nand_24_out), .B(nand_25_out), .S(L), .O(mux2to1_18_o));
  JKFlipFlop jkflipflop_9 (.SB(SB), .J(mux2to1_17_o), .CLK(nand_2_out), .K(mux2to1_18_o), .O(O[8]));  // open: OC
  nand nand_26 (nand_26_out, nand_24_out, O[8]);
  nand nand_27 (nand_27_out, nand_26_out, nand_26_out);
  nand nand_28 (nand_28_out, I[9], I[9]);
  Mux2To1 mux2to1_19 (.A(nand_27_out), .B(I[9]), .S(L), .O(mux2to1_19_o));
  Mux2To1 mux2to1_20 (.A(nand_27_out), .B(nand_28_out), .S(L), .O(mux2to1_20_o));
  JKFlipFlop jkflipflop_10 (.SB(SB), .J(mux2to1_19_o), .CLK(nand_2_out), .K(mux2to1_20_o), .O(O[9]));  // open: OC
  nand nand_29 (nand_29_out, nand_27_out, O[9]);
  nand nand_30 (nand_30_out, nand_29_out, nand_29_out);
  nand nand_31 (nand_31_out, I[10], I[10]);
  Mux2To1 mux2to1_21 (.A(nand_30_out), .B(I[10]), .S(L), .O(mux2to1_21_o));
  Mux2To1 mux2to1_22 (.A(nand_30_out), .B(nand_31_out), .S(L), .O(mux2to1_22_o));
  JKFlipFlop jkflipflop_11 (.SB(SB), .J(mux2to1_21_o), .CLK(nand_2_out), .K(mux2to1_22_o), .O(O[10]));  // open: OC
  nand nand_32 (nand_32_out, nand_30_out, O[10]);
  nand nand_33 (nand_33_out, nand_32_out, nand_32_out);
  nand nand_34 (nand_34_out, I[11], I[11]);
  Mux2To1 mux2to1_23 (.A(nand_33_out), .B(I[11]), .S(L), .O(mux2to1_23_o));
  Mux2To1 mux2to1_24 (.A(nand_33_out), .B(nand_34_out), .S(L), .O(mux2to1_24_o));
  JKFlipFlop jkflipflop_12 (.SB(SB), .J(mux2to1_23_o), .CLK(nand_2_out), .K(mux2to1_24_o), .O(O[11]));  // open: OC
  nand nand_35 (nand_35_out, nand_33_out, O[11]);
  nand nand_36 (nand_36_out, nand_35_out, nand_35_out);
  nand nand_37 (nand_37_out, I[12], I[12]);
  Mux2To1 mux2to1_25 (.A(nand_36_out), .B(I[12]), .S(L), .O(mux2to1_25_o));
  Mux2To1 mux2to1_26 (.A(nand_36_out), .B(nand_37_out), .S(L), .O(mux2to1_26_o));
  JKFlipFlop jkflipflop_13 (.SB(SB), .J(mux2to1_25_o), .CLK(nand_2_out), .K(mux2to1_26_o), .O(O[12]));  // open: OC
  nand nand_38 (nand_38_out, nand_36_out, O[12]);
  nand nand_39 (nand_39_out, nand_38_out, nand_38_out);
  nand nand_40 (nand_40_out, I[13], I[13]);
  Mux2To1 mux2to1_27 (.A(nand_39_out), .B(I[13]), .S(L), .O(mux2to1_27_o));
  Mux2To1 mux2to1_28 (.A(nand_39_out), .B(nand_40_out), .S(L), .O(mux2to1_28_o));
  JKFlipFlop jkflipflop_14 (.SB(SB), .J(mux2to1_27_o), .CLK(nand_2_out), .K(mux2to1_28_o), .O(O[13]));  // open: OC
  nand nand_41 (nand_41_out, nand_39_out, O[13]);
  nand nand_42 (nand_42_out, nand_41_out, nand_41_out);
  nand nand_43 (nand_43_out, I[14], I[14]);
  Mux2To1 mux2to1_29 (.A(nand_42_out), .B(I[14]), .S(L), .O(mux2to1_29_o));
  Mux2To1 mux2to1_30 (.A(nand_42_out), .B(nand_43_out), .S(L), .O(mux2to1_30_o));
  JKFlipFlop jkflipflop_15 (.SB(SB), .J(mux2to1_29_o), .CLK(nand_2_out), .K(mux2to1_30_o), .O(O[14]));  // open: OC
  nand nand_44 (nand_44_out, nand_42_out, O[14]);
  nand nand_45 (nand_45_out, nand_44_out, nand_44_out);
  nand nand_46 (nand_46_out, I[15], I[15]);
  Mux2To1 mux2to1_31 (.A(nand_45_out), .B(I[15]), .S(L), .O(mux2to1_31_o));
  Mux2To1 mux2to1_32 (.A(nand_45_out), .B(nand_46_out), .S(L), .O(mux2to1_32_o));
  JKFlipFlop jkflipflop_16 (.SB(SB), .J(mux2to1_31_o), .CLK(nand_2_out), .K(mux2to1_32_o), .O(O[15]));  // open: OC
  nand nand_47 (nand_47_out, nand_45_out, O[15]);
  nand nand_48 (nand_48_out, nand_47_out, nand_47_out);
  nand nand_49 (nand_49_out, I[16], I[16]);
  Mux2To1 mux2to1_33 (.A(nand_48_out), .B(I[16]), .S(L), .O(mux2to1_33_o));
  Mux2To1 mux2to1_34 (.A(nand_48_out), .B(nand_49_out), .S(L), .O(mux2to1_34_o));
  JKFlipFlop jkflipflop_17 (.SB(SB), .J(mux2to1_33_o), .CLK(nand_2_out), .K(mux2to1_34_o), .O(O[16]));  // open: OC
  nand nand_50 (nand_50_out, nand_48_out, O[16]);
  nand nand_51 (nand_51_out, nand_50_out, nand_50_out);
  nand nand_52 (nand_52_out, I[17], I[17]);
  Mux2To1 mux2to1_35 (.A(nand_51_out), .B(I[17]), .S(L), .O(mux2to1_35_o));
  Mux2To1 mux2to1_36 (.A(nand_51_out), .B(nand_52_out), .S(L), .O(mux2to1_36_o));
  JKFlipFlop jkflipflop_18 (.SB(SB), .J(mux2to1_35_o), .CLK(nand_2_out), .K(mux2to1_36_o), .O(O[17]));  // open: OC
  nand nand_53 (nand_53_out, nand_51_out, O[17]);
  nand nand_54 (nand_54_out, nand_53_out, nand_53_out);
  nand nand_55 (nand_55_out, I[18], I[18]);
  Mux2To1 mux2to1_37 (.A(nand_54_out), .B(I[18]), .S(L), .O(mux2to1_37_o));
  Mux2To1 mux2to1_38 (.A(nand_54_out), .B(nand_55_out), .S(L), .O(mux2to1_38_o));
  JKFlipFlop jkflipflop_19 (.SB(SB), .J(mux2to1_37_o), .CLK(nand_2_out), .K(mux2to1_38_o), .O(O[18]));  // open: OC
  nand nand_56 (nand_56_out, nand_54_out, O[18]);
  nand nand_57 (nand_57_out, nand_56_out, nand_56_out);
  nand nand_58 (nand_58_out, I[19], I[19]);
  Mux2To1 mux2to1_39 (.A(nand_57_out), .B(I[19]), .S(L), .O(mux2to1_39_o));
  Mux2To1 mux2to1_40 (.A(nand_57_out), .B(nand_58_out), .S(L), .O(mux2to1_40_o));
  JKFlipFlop jkflipflop_20 (.SB(SB), .J(mux2to1_39_o), .CLK(nand_2_out), .K(mux2to1_40_o), .O(O[19]));  // open: OC
endmodule

module JKFlipFlopOld (
  input  SB,
  input  J,
  input  CLK,
  input  K,
  output O,
  output OC
);

  wire nand_1_out, nand_2_out, nand_3_out, nand_4_out, nand_5_out, nand_6_out, nand_7_out, nand_8_out,
       nand_9_out, nand_10_out, nand_11_out;

  nand nand_1 (nand_1_out, OC, J);
  nand nand_2 (nand_2_out, K, O);
  nand nand_3 (nand_3_out, nand_1_out, nand_1_out);
  nand nand_4 (nand_4_out, CLK, CLK);
  nand nand_5 (nand_5_out, nand_2_out, nand_2_out);
  nand nand_6 (nand_6_out, nand_3_out, nand_4_out);
  nand nand_7 (nand_7_out, nand_4_out, nand_5_out);
  nand nand_8 (nand_8_out, nand_6_out, nand_9_out);
  nand nand_9 (nand_9_out, nand_8_out, SB, nand_7_out);
  nand nand_10 (nand_10_out, nand_8_out, CLK);
  nand nand_11 (nand_11_out, CLK, nand_9_out);
  nand nand_12 (O, nand_10_out, OC);
  nand nand_13 (OC, O, SB, nand_11_out);
endmodule

module SyncCounterNewer (
  input  SB,
  input  CLK,
  input  ENABLE,
  input  L,
  input  in_5
);

  wire jkflipflop_1_o, mux4to1_1_o, mux4to1_2_o, nand_1_out;

  nand nand_1 (nand_1_out, in_5, in_5);
  Mux4To1 mux4to1_1 (.A(1'b0), .B(1'b0), .C(1'b1), .D(in_5), .S1(ENABLE), .S2(L), .O(mux4to1_1_o));
  Mux4To1 mux4to1_2 (.A(1'b0), .B(1'b0), .C(1'b1), .D(nand_1_out), .S1(ENABLE), .S2(L), .O(mux4to1_2_o));
  JKFlipFlop jkflipflop_1 (.SB(SB), .J(mux4to1_1_o), .CLK(CLK), .K(mux4to1_2_o), .O(jkflipflop_1_o));  // open: OC
endmodule

module UniversalShiftRegisterOld (
  input  CLK,
  input  LL,
  input  LH,
  input  SB,
  input  S1,
  input  S2,
  input  [9:0] I,
  output [9:0] O
);

  wire mux4to1_1_o, mux4to1_2_o, mux4to1_3_o, mux4to1_4_o, mux4to1_5_o, mux4to1_6_o, mux4to1_7_o,
       mux4to1_8_o, mux4to1_9_o, mux4to1_10_o, nand_1_out, nand_2_out, nand_3_out, nand_4_out;

  nand nand_1 (nand_1_out, CLK, LL);
  nand nand_2 (nand_2_out, nand_1_out, nand_1_out);
  nand nand_3 (nand_3_out, CLK, LH);
  nand nand_4 (nand_4_out, nand_3_out, nand_3_out);
  Mux4To1 mux4to1_1 (.A(O[1]), .B(1'b0), .C(I[0]), .D(1'b0), .S1(S1), .S2(S2), .O(mux4to1_1_o));
  DFlipFlop dflipflop_1 (.CLK(nand_2_out), .D(mux4to1_1_o), .SB(SB), .O(O[0]));  // open: OC
  Mux4To1 mux4to1_2 (.A(O[2]), .B(O[0]), .C(I[1]), .D(1'b0), .S1(S1), .S2(S2), .O(mux4to1_2_o));
  DFlipFlop dflipflop_2 (.CLK(nand_2_out), .D(mux4to1_2_o), .SB(SB), .O(O[1]));  // open: OC
  Mux4To1 mux4to1_3 (.A(O[3]), .B(O[1]), .C(I[2]), .D(1'b0), .S1(S1), .S2(S2), .O(mux4to1_3_o));
  DFlipFlop dflipflop_3 (.CLK(nand_2_out), .D(mux4to1_3_o), .SB(SB), .O(O[2]));  // open: OC
  Mux4To1 mux4to1_4 (.A(O[4]), .B(O[2]), .C(I[3]), .D(1'b0), .S1(S1), .S2(S2), .O(mux4to1_4_o));
  DFlipFlop dflipflop_4 (.CLK(nand_2_out), .D(mux4to1_4_o), .SB(SB), .O(O[3]));  // open: OC
  Mux4To1 mux4to1_5 (.A(O[5]), .B(O[3]), .C(I[4]), .D(1'b0), .S1(S1), .S2(S2), .O(mux4to1_5_o));
  DFlipFlop dflipflop_5 (.CLK(nand_2_out), .D(mux4to1_5_o), .SB(SB), .O(O[4]));  // open: OC
  Mux4To1 mux4to1_6 (.A(O[6]), .B(O[4]), .C(I[5]), .D(1'b0), .S1(S1), .S2(S2), .O(mux4to1_6_o));
  DFlipFlop dflipflop_6 (.CLK(nand_4_out), .D(mux4to1_6_o), .SB(SB), .O(O[5]));  // open: OC
  Mux4To1 mux4to1_7 (.A(O[7]), .B(O[5]), .C(I[6]), .D(1'b0), .S1(S1), .S2(S2), .O(mux4to1_7_o));
  DFlipFlop dflipflop_7 (.CLK(nand_4_out), .D(mux4to1_7_o), .SB(SB), .O(O[6]));  // open: OC
  Mux4To1 mux4to1_8 (.A(O[8]), .B(O[6]), .C(I[7]), .D(1'b0), .S1(S1), .S2(S2), .O(mux4to1_8_o));
  DFlipFlop dflipflop_8 (.CLK(nand_4_out), .D(mux4to1_8_o), .SB(SB), .O(O[7]));  // open: OC
  Mux4To1 mux4to1_9 (.A(O[9]), .B(O[7]), .C(I[8]), .D(1'b0), .S1(S1), .S2(S2), .O(mux4to1_9_o));
  DFlipFlop dflipflop_9 (.CLK(nand_4_out), .D(mux4to1_9_o), .SB(SB), .O(O[8]));  // open: OC
  Mux4To1 mux4to1_10 (.A(1'b0), .B(O[8]), .C(I[9]), .D(1'b0), .S1(S1), .S2(S2), .O(mux4to1_10_o));
  DFlipFlop dflipflop_10 (.CLK(nand_4_out), .D(mux4to1_10_o), .SB(SB), .O(O[9]));  // open: OC
endmodule
